// Logisim project MINIRISCV6.circ as structural Verilog: 7 circuits, main circuit RegisterFile
module main (
  input  Reset
);

  wire alu_1_i, alu_1_s, alu_1_wb, Clk_out, decodeunit_1_add, decodeunit_1_aluusedop,
       decodeunit_1_errortypeop, decodeunit_1_istypeop, decodeunit_1_isword, decodeunit_1_jumpop,
       decodeunit_1_onlyrfusedop, decodeunit_1_va1, decodeunit_1_va2, decodeunit_1_var;
  wire [1:0] alu_1_infolow2;
  wire [3:0] decodeunit_1_infoadd1, decodeunit_1_infoadd2, decodeunit_1_infoaddr;
  wire [7:0] alu_1_ramsbinfo, alu_1_saddr, pc_1_addr, pc_1_nextaddr;
  wire [31:0] alu_1_result, dataram_1_raminfo, decodeunit_1_imdadd2, decodeunit_1_imdls, decodeunit_1_imdlui,
       registerfile_1_value1, registerfile_1_value2, rom_1_data;

  Clock Clk (.out(Clk_out));
  ROM #(.dataWidth(32)) rom_1 (.addr(pc_1_addr), .data(rom_1_data));
  PC pc_1 (
    .AddrC(alu_1_result), .Jump(decodeunit_1_jumpop), .clk(Clk_out), .Reset(Reset), .Addr(pc_1_addr),
    .NextAddr(pc_1_nextaddr));
  DecodeUnit decodeunit_1 (
    .Data(rom_1_data), .ErrorTypeOP(decodeunit_1_errortypeop), .ALUUsedOP(decodeunit_1_aluusedop),
    .OnlyRFusedOP(decodeunit_1_onlyrfusedop), .JumpOP(decodeunit_1_jumpop), .IStypeOP(decodeunit_1_istypeop),
    .InfoAdd1(decodeunit_1_infoadd1), .VA1(decodeunit_1_va1), .InfoAdd2(decodeunit_1_infoadd2),
    .VA2(decodeunit_1_va2), .InfoAddR(decodeunit_1_infoaddr), .VAR(decodeunit_1_var),
    .ImdAdd2(decodeunit_1_imdadd2), .ImdLuI(decodeunit_1_imdlui), .ImdLS(decodeunit_1_imdls),
    .Add(decodeunit_1_add), .ISWord(decodeunit_1_isword));
  RegisterFile registerfile_1 (
    .ErrorOP(decodeunit_1_errortypeop), .ALUType(decodeunit_1_aluusedop),
    .GPRType(decodeunit_1_onlyrfusedop), .JumpType(decodeunit_1_jumpop), .IStypeOP(decodeunit_1_istypeop),
    .Add1(decodeunit_1_infoadd1), .VA1(decodeunit_1_va1), .Add2(decodeunit_1_infoadd2),
    .VA2(decodeunit_1_va2), .AddR(decodeunit_1_infoaddr), .VR(decodeunit_1_var), .WBget(alu_1_wb),
    .InfoResult(alu_1_result), .InfoAdd2(decodeunit_1_imdadd2), .InfoLUI(decodeunit_1_imdlui),
    .InfoJump(pc_1_nextaddr), .InfoRAM(dataram_1_raminfo), .ISword(decodeunit_1_isword), .clk(Clk_out),
    .R(Reset), .Value1(registerfile_1_value1), .Value2(registerfile_1_value2));
  ALU alu_1 (
    .Cal1(registerfile_1_value1), .Cal2(registerfile_1_value2), .ISinfo(decodeunit_1_imdls),
    .Add(decodeunit_1_add), .ALUDemand(decodeunit_1_aluusedop), .JumpOP(decodeunit_1_jumpop),
    .ISOP(decodeunit_1_istypeop), .SaveIns(decodeunit_1_va2), .Result(alu_1_result), .Saddr(alu_1_saddr),
    .S(alu_1_s), .I(alu_1_i), .WB(alu_1_wb), .InfoLow2(alu_1_infolow2), .RAMSbInfo(alu_1_ramsbinfo));
  DataRAM dataram_1 (
    .In32(registerfile_1_value2), .In8(alu_1_ramsbinfo), .WBus(alu_1_s), .RBus(alu_1_i), .Saddr(alu_1_saddr),
    .ISOP(decodeunit_1_istypeop), .ISword(decodeunit_1_isword), .Sel(alu_1_infolow2), .clk(Clk_out),
    .RAMInfo(dataram_1_raminfo));

  // Notes on the sheet:
  //   contents of rom_1 (hex, n*v repeats v):
  //   4000093 1800113 402081b3 40110233 401002b3 40108333 103b7 100413 408384b3 848533 302023 400005b3
  //   2603 4800693 68767 0 0 0 5500793 5000693 68067 19*0 30000000 23*0 ff214203 420233 420233 440233
  //   22203 fe412623 ff114203 420233 420233 440233 22203 fe412423 ff014203 420233 420233 440233 22203
  //   fe412223 fed14183 fea14203 4181b3 fe714203 4181b3 fe312223 fee14183 feb14203 4181b3 fe3102a3
  //   fef14183 fe310323 fe412183 8237 20213 440433 ff314203 420233 420233 440233 22203 ffc12403 4181b3
  //   74503 350533 6a603 270713 468693 fe312a23 fec12423 31237 50020213 feb14183 4181b3 1c183 fe3103a3
  //   fea14183 4181b3 1c183 fe310323 fe914183 4181b3 1c183 fe3102a3 fe814183 4181b3 1c183 fe310223
  //   ff412183 fe412203 450533 150513 fea12823 fe812e23 1437 40840413 ff014183 3401b3 1c183 ff114203
  //   440233 24203 4181b3 ff214203 440233 24203 4181b3 ff314203 440233 24203 4181b3 1237 40020213 320233
  //   24503 ffc12403 e12223 d12023 1800093 80e7 412703 497b7 6c078793 12683 fee12823 fef12623 fe812e23
  //   fe912c23 1437 30040413 ff014183 340233 100193 320023 fec14183 3401b3 18023 24183 ff114483 940233
  //   100493 920023 fed14483 9404b3 48023 24483 9181b3 ff214483 940233 100493 920023 fee14483 9404b3 48023
  //   24483 9181b3 ff314483 940233 100493 920023 fef14483 9404b3 48023 24483 9181b3 1237 40020213 320233
  //   24203 ff812483 ffc12403 420233 420233 410233 37800193 fe312823 e000193 fe312623 fec22203 20067 49737
  //   67070713 72683 fe012823 14c203 fe4108a3 ff012203 4c503 450533 470713 e12023 fe312a23 fed12423 31237
  //   50020213 feb14183 4181b3 1c183 fe3103a3 fea14183 4181b3 1c183 fe310323 fe914183 4181b3 1c183
  //   fe3102a3 fe814183 4181b3 1c183 fe310223 ff412183 fe412203 450533
endmodule

module PC (
  input  [31:0] AddrC,
  input  Jump,
  input  clk,
  input  Reset,
  output [7:0] Addr,
  output [7:0] NextAddr
);

  wire not_1_out;
  wire [31:0] adder_1_out, controlled_buffer_1_out, register_1_q;

  assign controlled_buffer_1_out = Jump ? AddrC : 32'bz;  // Controlled_Buffer controlled_buffer_1
  not not_1 (not_1_out, Jump);
  assign controlled_buffer_1_out = not_1_out ? {adder_1_out[31:10], NextAddr, adder_1_out[1:0]} : 32'bz;  // Controlled_Buffer controlled_buffer_2
  Register #(.width(32)) register_1 (
    .D(controlled_buffer_1_out), .en(1'b1), .clk(clk), .Q({register_1_q[31:10], Addr, register_1_q[1:0]}),
    .clr(Reset));
  Adder #(.width(32)) adder_1 (
    .a({register_1_q[31:10], Addr, register_1_q[1:0]}), .b(32'h4),
    .out({adder_1_out[31:10], NextAddr, adder_1_out[1:0]}));  // open: cin, cout
endmodule

module DecodeUnit (
  input  [31:0] Data,
  output ErrorTypeOP,
  output ALUUsedOP,
  output OnlyRFusedOP,
  output JumpOP,
  output IStypeOP,
  output [3:0] InfoAdd1,
  output VA1,
  output [3:0] InfoAdd2,
  output VA2,
  output [3:0] InfoAddR,
  output VAR,
  output [31:0] ImdAdd2,
  output [31:0] ImdLuI,
  output [31:0] ImdLS,
  output Add,
  output ISWord
);

  wire and_1_out, and_2_out, and_3_out, and_5_out, and_6_out, and_7_out, and_8_out, decoder_1_out0,
       decoder_1_out2, decoder_1_out4, decoder_1_out6, decoder_1_out13, decoder_2_out0, decoder_2_out2,
       decoder_2_out4, not_1_out, not_2_out;

  not not_1 (not_1_out, Data[3]);
  nand nand_1 (ErrorTypeOP, Data[0], not_1_out, Data[1]);
  Decoder #(.select(4)) decoder_1 (
    .out0(decoder_1_out0), .out2(decoder_1_out2), .out4(decoder_1_out4), .out6(decoder_1_out6),
    .out7(OnlyRFusedOP), .out13(decoder_1_out13), .sel({Data[6:4], Data[2]}));  // open: out1, out3, out5, out8, out9, out10, out11, out12, out14, out15, en
  Decoder #(.select(3)) decoder_2 (
    .out0(decoder_2_out0), .out2(decoder_2_out2), .out4(decoder_2_out4), .sel(Data[14:12]));  // open: out1, out3, out5, out6, out7, en
  assign ImdAdd2 = {{20{Data[31]}}, Data[31:20]};  // Bit_Extender bit_extender_1
  assign ImdLS = {{20{Data[31]}}, {Data[31:25], Data[11:7]}};  // Bit_Extender bit_extender_2
  not not_2 (not_2_out, Data[30]);
  and and_1 (and_1_out, decoder_1_out2, decoder_2_out0);
  and and_2 (and_2_out, decoder_1_out6, decoder_2_out0);
  and and_3 (and_3_out, decoder_1_out4, decoder_2_out2);
  and and_4 (JumpOP, decoder_1_out13, decoder_2_out0);
  and and_5 (and_5_out, decoder_1_out4, decoder_2_out0);
  and and_6 (and_6_out, decoder_1_out0, decoder_2_out2);
  and and_7 (and_7_out, decoder_1_out0, decoder_2_out4);
  or or_1 (ISWord, and_6_out, and_3_out);
  and and_8 (and_8_out, and_2_out, not_2_out);
  or or_2 (ALUUsedOP, and_7_out, and_1_out, and_3_out, JumpOP, and_6_out, and_2_out, and_5_out);
  or or_3 (IStypeOP, and_3_out, and_7_out, and_6_out, and_5_out);
  or or_4 (VA1, and_1_out, and_2_out, JumpOP, and_3_out, and_6_out, and_5_out, and_7_out);
  or or_5 (VA2, and_2_out, and_3_out, and_5_out);
  or or_6 (VAR, and_1_out, and_2_out, OnlyRFusedOP, JumpOP, and_6_out, and_7_out);
  or or_7 (Add, and_8_out, JumpOP, and_1_out);

  assign ImdLuI = {Data[31:12], {12{1'b0}}};
  assign InfoAdd1 = Data[18:15];
  assign InfoAdd2 = Data[23:20];
  assign InfoAddR = Data[10:7];
endmodule

module RegisterFile (
  input  ErrorOP,
  input  ALUType,
  input  GPRType,
  input  JumpType,
  input  IStypeOP,
  input  [3:0] Add1,
  input  VA1,
  input  [3:0] Add2,
  input  VA2,
  input  [3:0] AddR,
  input  VR,
  input  WBget,
  input  [31:0] InfoResult,
  input  [31:0] InfoAdd2,
  input  [31:0] InfoLUI,
  input  [7:0] InfoJump,
  input  [31:0] InfoRAM,
  input  ISword,
  input  clk,
  input  R,
  output [31:0] Value1,
  output [31:0] Value2
);

  wire decoder_1_out16, decoder_1_out17, decoder_1_out18, decoder_1_out19, decoder_1_out20, decoder_1_out21,
       decoder_1_out22, decoder_1_out23, decoder_1_out24, decoder_1_out25, decoder_1_out26, decoder_1_out27,
       decoder_1_out28, decoder_1_out29, decoder_1_out30, decoder_1_out31, decoder_2_out0, decoder_2_out1,
       decoder_2_out2, decoder_2_out3, decoder_2_out4, decoder_2_out5, decoder_2_out6, decoder_2_out7,
       decoder_2_out8, decoder_2_out9, decoder_2_out10, decoder_2_out11, decoder_2_out12, decoder_2_out13,
       decoder_2_out14, decoder_2_out15, decoder_3_out0, decoder_3_out1, decoder_3_out2, decoder_3_out3,
       decoder_3_out4, decoder_3_out5, decoder_3_out6, decoder_3_out7, decoder_3_out8, decoder_3_out9,
       decoder_3_out10, decoder_3_out11, decoder_3_out12, decoder_3_out13, decoder_3_out14, decoder_3_out15,
       not_1_out;
  wire [31:0] controlled_buffer_1_out, controller_1_inputvalue, controller_1_output2, register_1_q,
       register_2_q, register_3_q, register_4_q, register_5_q, register_6_q, register_7_q, register_8_q,
       register_9_q, register_10_q, register_11_q, register_12_q, register_13_q, register_14_q,
       register_15_q, register_16_q;

  Controller controller_1 (
    .ALUType(ALUType), .GPRType(GPRType), .JumpType(JumpType), .LStype(IStypeOP), .Addr(AddR), .VA2(VA2),
    .VR(VR), .VBget(WBget), .LSWord(ISword), .InfoALU(InfoResult), .InfoAdd2(InfoAdd2), .InfoLui(InfoLUI),
    .InfoRAM(InfoRAM), .InfoJump(InfoJump), .Output2(controller_1_output2),
    .InputValue(controller_1_inputvalue));
  Decoder #(.select(5)) decoder_1 (
    .out16(decoder_1_out16), .out17(decoder_1_out17), .out18(decoder_1_out18), .out19(decoder_1_out19),
    .out20(decoder_1_out20), .out21(decoder_1_out21), .out22(decoder_1_out22), .out23(decoder_1_out23),
    .out24(decoder_1_out24), .out25(decoder_1_out25), .out26(decoder_1_out26), .out27(decoder_1_out27),
    .out28(decoder_1_out28), .out29(decoder_1_out29), .out30(decoder_1_out30), .out31(decoder_1_out31),
    .sel({VR, AddR}));  // open: out0, out1, out2, out3, out4, out5, out6, out7, out8, out9, out10, out11, out12, out13, out14, out15, en
  Decoder #(.select(4)) decoder_2 (
    .out0(decoder_2_out0), .out1(decoder_2_out1), .out2(decoder_2_out2), .out3(decoder_2_out3),
    .out4(decoder_2_out4), .out5(decoder_2_out5), .out6(decoder_2_out6), .out7(decoder_2_out7),
    .out8(decoder_2_out8), .out9(decoder_2_out9), .out10(decoder_2_out10), .out11(decoder_2_out11),
    .out12(decoder_2_out12), .out13(decoder_2_out13), .out14(decoder_2_out14), .out15(decoder_2_out15),
    .sel(Add1), .en(VA1));
  Decoder #(.select(4)) decoder_3 (
    .out0(decoder_3_out0), .out1(decoder_3_out1), .out2(decoder_3_out2), .out3(decoder_3_out3),
    .out4(decoder_3_out4), .out5(decoder_3_out5), .out6(decoder_3_out6), .out7(decoder_3_out7),
    .out8(decoder_3_out8), .out9(decoder_3_out9), .out10(decoder_3_out10), .out11(decoder_3_out11),
    .out12(decoder_3_out12), .out13(decoder_3_out13), .out14(decoder_3_out14), .out15(decoder_3_out15),
    .sel(Add2), .en(VA2));
  Register #(.width(32)) register_1 (.D({32{1'b0}}), .en(decoder_1_out16), .clk(clk), .Q(register_1_q), .clr(R));
  Register #(.width(32)) register_2 (
    .D(controller_1_inputvalue), .en(decoder_1_out17), .clk(clk), .Q(register_2_q), .clr(R));
  Register #(.width(32)) register_3 (
    .D(controller_1_inputvalue), .en(decoder_1_out18), .clk(clk), .Q(register_3_q), .clr(R));
  Register #(.width(32)) register_4 (
    .D(controller_1_inputvalue), .en(decoder_1_out19), .clk(clk), .Q(register_4_q), .clr(R));
  assign controlled_buffer_1_out = decoder_2_out0 ? register_1_q : 32'bz;  // Controlled_Buffer controlled_buffer_1
  assign controlled_buffer_1_out = decoder_2_out1 ? register_2_q : 32'bz;  // Controlled_Buffer controlled_buffer_2
  assign controller_1_output2 = decoder_3_out0 ? register_1_q : 32'bz;  // Controlled_Buffer controlled_buffer_3
  assign controller_1_output2 = decoder_3_out1 ? register_2_q : 32'bz;  // Controlled_Buffer controlled_buffer_4
  assign controlled_buffer_1_out = decoder_2_out2 ? register_3_q : 32'bz;  // Controlled_Buffer controlled_buffer_5
  assign controlled_buffer_1_out = decoder_2_out3 ? register_4_q : 32'bz;  // Controlled_Buffer controlled_buffer_6
  Register #(.width(32)) register_5 (
    .D(controller_1_inputvalue), .en(decoder_1_out20), .clk(clk), .Q(register_5_q), .clr(R));
  Register #(.width(32)) register_6 (
    .D(controller_1_inputvalue), .en(decoder_1_out21), .clk(clk), .Q(register_6_q), .clr(R));
  Register #(.width(32)) register_7 (
    .D(controller_1_inputvalue), .en(decoder_1_out22), .clk(clk), .Q(register_7_q), .clr(R));
  assign controller_1_output2 = decoder_3_out2 ? register_3_q : 32'bz;  // Controlled_Buffer controlled_buffer_7
  Register #(.width(32)) register_8 (
    .D(controller_1_inputvalue), .en(decoder_1_out23), .clk(clk), .Q(register_8_q), .clr(R));
  assign controller_1_output2 = decoder_3_out3 ? register_4_q : 32'bz;  // Controlled_Buffer controlled_buffer_8
  assign controlled_buffer_1_out = decoder_2_out4 ? register_5_q : 32'bz;  // Controlled_Buffer controlled_buffer_9
  assign controlled_buffer_1_out = decoder_2_out5 ? register_6_q : 32'bz;  // Controlled_Buffer controlled_buffer_10
  assign controller_1_output2 = decoder_3_out4 ? register_5_q : 32'bz;  // Controlled_Buffer controlled_buffer_11
  assign controller_1_output2 = decoder_3_out5 ? register_6_q : 32'bz;  // Controlled_Buffer controlled_buffer_12
  assign controlled_buffer_1_out = decoder_2_out6 ? register_7_q : 32'bz;  // Controlled_Buffer controlled_buffer_13
  assign controlled_buffer_1_out = decoder_2_out7 ? register_8_q : 32'bz;  // Controlled_Buffer controlled_buffer_14
  Register #(.width(32)) register_9 (
    .D(controller_1_inputvalue), .en(decoder_1_out24), .clk(clk), .Q(register_9_q), .clr(R));
  Register #(.width(32)) register_10 (
    .D(controller_1_inputvalue), .en(decoder_1_out25), .clk(clk), .Q(register_10_q), .clr(R));
  Register #(.width(32)) register_11 (
    .D(controller_1_inputvalue), .en(decoder_1_out26), .clk(clk), .Q(register_11_q), .clr(R));
  assign controller_1_output2 = decoder_3_out6 ? register_7_q : 32'bz;  // Controlled_Buffer controlled_buffer_15
  Register #(.width(32)) register_12 (
    .D(controller_1_inputvalue), .en(decoder_1_out27), .clk(clk), .Q(register_12_q), .clr(R));
  assign controller_1_output2 = decoder_3_out7 ? register_8_q : 32'bz;  // Controlled_Buffer controlled_buffer_16
  assign controlled_buffer_1_out = decoder_2_out8 ? register_9_q : 32'bz;  // Controlled_Buffer controlled_buffer_17
  assign controlled_buffer_1_out = decoder_2_out9 ? register_10_q : 32'bz;  // Controlled_Buffer controlled_buffer_18
  assign controller_1_output2 = decoder_3_out8 ? register_9_q : 32'bz;  // Controlled_Buffer controlled_buffer_19
  assign controller_1_output2 = decoder_3_out9 ? register_10_q : 32'bz;  // Controlled_Buffer controlled_buffer_20
  assign controlled_buffer_1_out = decoder_2_out10 ? register_11_q : 32'bz;  // Controlled_Buffer controlled_buffer_21
  assign controlled_buffer_1_out = decoder_2_out11 ? register_12_q : 32'bz;  // Controlled_Buffer controlled_buffer_22
  Register #(.width(32)) register_13 (
    .D(controller_1_inputvalue), .en(decoder_1_out28), .clk(clk), .Q(register_13_q), .clr(R));
  Register #(.width(32)) register_14 (
    .D(controller_1_inputvalue), .en(decoder_1_out29), .clk(clk), .Q(register_14_q), .clr(R));
  Register #(.width(32)) register_15 (
    .D(controller_1_inputvalue), .en(decoder_1_out30), .clk(clk), .Q(register_15_q), .clr(R));
  assign controller_1_output2 = decoder_3_out10 ? register_11_q : 32'bz;  // Controlled_Buffer controlled_buffer_23
  Register #(.width(32)) register_16 (
    .D(controller_1_inputvalue), .en(decoder_1_out31), .clk(clk), .Q(register_16_q), .clr(R));
  assign controller_1_output2 = decoder_3_out11 ? register_12_q : 32'bz;  // Controlled_Buffer controlled_buffer_24
  assign controlled_buffer_1_out = decoder_2_out12 ? register_13_q : 32'bz;  // Controlled_Buffer controlled_buffer_25
  assign controlled_buffer_1_out = decoder_2_out13 ? register_14_q : 32'bz;  // Controlled_Buffer controlled_buffer_26
  assign controller_1_output2 = decoder_3_out12 ? register_13_q : 32'bz;  // Controlled_Buffer controlled_buffer_27
  assign controller_1_output2 = decoder_3_out13 ? register_14_q : 32'bz;  // Controlled_Buffer controlled_buffer_28
  assign controlled_buffer_1_out = decoder_2_out14 ? register_15_q : 32'bz;  // Controlled_Buffer controlled_buffer_29
  assign controlled_buffer_1_out = decoder_2_out15 ? register_16_q : 32'bz;  // Controlled_Buffer controlled_buffer_30
  not not_1 (not_1_out, ErrorOP);
  assign controller_1_output2 = decoder_3_out14 ? register_15_q : 32'bz;  // Controlled_Buffer controlled_buffer_31
  assign controller_1_output2 = decoder_3_out15 ? register_16_q : 32'bz;  // Controlled_Buffer controlled_buffer_32
  assign Value1 = not_1_out ? controlled_buffer_1_out : 32'bz;  // Controlled_Buffer controlled_buffer_33
  assign Value1 = ErrorOP ? {32{1'b0}} : 32'bz;  // Controlled_Buffer controlled_buffer_34
  assign Value2 = not_1_out ? controller_1_output2 : 32'bz;  // Controlled_Buffer controlled_buffer_35
  assign Value2 = ErrorOP ? {32{1'b0}} : 32'bz;  // Controlled_Buffer controlled_buffer_36
endmodule

module Controller (
  input  ALUType,
  input  GPRType,
  input  JumpType,
  input  LStype,
  input  [3:0] Addr,
  input  VA2,
  input  VR,
  input  VBget,
  input  LSWord,
  input  [31:0] InfoALU,
  input  [31:0] InfoAdd2,
  input  [31:0] InfoLui,
  input  [31:0] InfoRAM,
  input  [7:0] InfoJump,
  output [31:0] Output2,
  output [31:0] InputValue
);

  wire and_1_out, decoder_1_out0, decoder_1_out1, decoder_1_out2, decoder_1_out3, decoder_1_out4,
       decoder_1_out5, decoder_1_out6, decoder_1_out7, decoder_1_out8, decoder_1_out9, decoder_1_out10,
       decoder_1_out11, decoder_1_out12, decoder_1_out13, decoder_1_out14, decoder_1_out15, decoder_2_out0,
       decoder_2_out1, decoder_3_out0, decoder_3_out1, decoder_3_out2, decoder_3_out3, not_1_out, or_1_out;
  wire [31:0] controlled_buffer_1_out, controlled_buffer_4_out, controlled_buffer_14_out,
       controlled_buffer_15_out, controlled_buffer_17_out, controlled_buffer_20_out;

  Decoder #(.select(4)) decoder_1 (
    .out0(decoder_1_out0), .out1(decoder_1_out1), .out2(decoder_1_out2), .out3(decoder_1_out3),
    .out4(decoder_1_out4), .out5(decoder_1_out5), .out6(decoder_1_out6), .out7(decoder_1_out7),
    .out8(decoder_1_out8), .out9(decoder_1_out9), .out10(decoder_1_out10), .out11(decoder_1_out11),
    .out12(decoder_1_out12), .out13(decoder_1_out13), .out14(decoder_1_out14), .out15(decoder_1_out15),
    .sel({LStype, JumpType, GPRType, ALUType}));  // open: en
  not not_1 (not_1_out, VA2);
  and and_1 (and_1_out, VR, VBget);
  assign controlled_buffer_1_out = not_1_out ? InfoAdd2 : 32'bz;  // Controlled_Buffer controlled_buffer_1
  Decoder decoder_2 (.out0(decoder_2_out0), .out1(decoder_2_out1), .sel(and_1_out));  // open: en
  assign Output2 = decoder_1_out1 ? controlled_buffer_1_out : 32'bz;  // Controlled_Buffer controlled_buffer_2
  assign InputValue = decoder_1_out1 ? controlled_buffer_4_out : 32'bz;  // Controlled_Buffer controlled_buffer_3
  assign controlled_buffer_4_out = decoder_2_out0 ? {32{1'b0}} : 32'bz;  // Controlled_Buffer controlled_buffer_4
  assign controlled_buffer_4_out = decoder_2_out1 ? InfoALU : 32'bz;  // Controlled_Buffer controlled_buffer_5
  assign Output2 = decoder_1_out2 ? {32{1'b0}} : 32'bz;  // Controlled_Buffer controlled_buffer_6
  assign InputValue = decoder_1_out2 ? InfoLui : 32'bz;  // Controlled_Buffer controlled_buffer_7
  assign Output2 = decoder_1_out5 ? controlled_buffer_1_out : 32'bz;  // Controlled_Buffer controlled_buffer_8
  assign InputValue = decoder_1_out5 ? {{22{1'b0}}, InfoJump, 2'b00} : 32'bz;  // Controlled_Buffer controlled_buffer_9
  assign Output2 = decoder_1_out9 ? controlled_buffer_14_out : 32'bz;  // Controlled_Buffer controlled_buffer_10
  assign InputValue = decoder_1_out9 ? controlled_buffer_20_out : 32'bz;  // Controlled_Buffer controlled_buffer_11
  Decoder #(.select(2)) decoder_3 (
    .out0(decoder_3_out0), .out1(decoder_3_out1), .out2(decoder_3_out2), .out3(decoder_3_out3),
    .sel({VA2, LSWord}));  // open: en
  or or_1 (or_1_out, decoder_1_out0, decoder_1_out3, decoder_1_out4, decoder_1_out6, decoder_1_out7, decoder_1_out8, decoder_1_out10, decoder_1_out11, decoder_1_out12, decoder_1_out13, decoder_1_out14, decoder_1_out15);
  assign Output2 = or_1_out ? {32{1'b0}} : 32'bz;  // Controlled_Buffer controlled_buffer_12
  assign InputValue = or_1_out ? {32{1'b0}} : 32'bz;  // Controlled_Buffer controlled_buffer_13
  assign controlled_buffer_14_out = decoder_3_out3 ? controlled_buffer_15_out : 32'bz;  // Controlled_Buffer controlled_buffer_14
  assign controlled_buffer_15_out = 1'b0 ? {32{1'b0}} : 32'bz;  // Controlled_Buffer controlled_buffer_15
  assign controlled_buffer_14_out = decoder_3_out2 ? controlled_buffer_17_out : 32'bz;  // Controlled_Buffer controlled_buffer_16
  assign controlled_buffer_17_out = 1'b0 ? controlled_buffer_1_out : 32'bz;  // Controlled_Buffer controlled_buffer_17
  assign controlled_buffer_14_out = decoder_3_out1 ? controlled_buffer_1_out : 32'bz;  // Controlled_Buffer controlled_buffer_18
  assign controlled_buffer_14_out = decoder_3_out0 ? controlled_buffer_1_out : 32'bz;  // Controlled_Buffer controlled_buffer_19
  assign controlled_buffer_20_out = decoder_3_out3 ? {32{1'b0}} : 32'bz;  // Controlled_Buffer controlled_buffer_20
  assign controlled_buffer_20_out = decoder_3_out2 ? controlled_buffer_1_out : 32'bz;  // Controlled_Buffer controlled_buffer_21
  assign controlled_buffer_20_out = decoder_3_out1 ? InfoRAM : 32'bz;  // Controlled_Buffer controlled_buffer_22
  assign controlled_buffer_20_out = decoder_3_out0 ? InfoRAM : 32'bz;  // Controlled_Buffer controlled_buffer_23
endmodule

module ALU (
  input  [31:0] Cal1,
  input  [31:0] Cal2,
  input  [31:0] ISinfo,
  input  Add,
  input  ALUDemand,
  input  JumpOP,
  input  ISOP,
  input  SaveIns,
  output [31:0] Result,
  output [7:0] Saddr,
  output S,
  output I,
  output WB,
  output [1:0] InfoLow2,
  output [7:0] RAMSbInfo
);

  wire and_1_out, decoder_1_out0, decoder_1_out1, decoder_1_out2, decoder_1_out3, decoder_1_out4,
       decoder_1_out5, decoder_1_out6, decoder_1_out7, not_2_out, not_3_out, not_4_out, or_1_out, or_2_out;
  wire [31:0] adder_1_out, adder_2_out, adder_3_out, controlled_buffer_1_out, not_1_out;

  assign controlled_buffer_1_out = SaveIns ? ISinfo : 32'bz;  // Controlled_Buffer controlled_buffer_1
  assign not_1_out = ~Cal2;  // NOT_Gate not_1, 32 bits wide
  Adder #(.width(32)) adder_1 (.a(Cal1), .b(controlled_buffer_1_out), .out(adder_1_out));  // open: cin, cout
  assign controlled_buffer_1_out = not_2_out ? Cal2 : 32'bz;  // Controlled_Buffer controlled_buffer_2
  not not_2 (not_2_out, SaveIns);
  Decoder #(.select(3)) decoder_1 (
    .out0(decoder_1_out0), .out1(decoder_1_out1), .out2(decoder_1_out2), .out3(decoder_1_out3),
    .out4(decoder_1_out4), .out5(decoder_1_out5), .out6(decoder_1_out6), .out7(decoder_1_out7),
    .sel({ISOP, JumpOP, ALUDemand}));  // open: en
  Adder #(.width(32)) adder_2 (.a(Cal1), .b(Cal2), .out(adder_2_out));  // open: cin, cout
  Adder #(.width(32)) adder_3 (.a(Cal1), .b(not_1_out), .out(adder_3_out), .cin(1'b1));  // open: cout
  assign WB = decoder_1_out1 ? 1'b1 : 1'bz;  // Controlled_Buffer controlled_buffer_3
  assign I = decoder_1_out1 ? 1'b0 : 1'bz;  // Controlled_Buffer controlled_buffer_4
  assign S = decoder_1_out1 ? 1'b0 : 1'bz;  // Controlled_Buffer controlled_buffer_5
  assign WB = decoder_1_out3 ? 1'b1 : 1'bz;  // Controlled_Buffer controlled_buffer_6
  assign I = decoder_1_out3 ? 1'b0 : 1'bz;  // Controlled_Buffer controlled_buffer_7
  assign S = decoder_1_out3 ? 1'b0 : 1'bz;  // Controlled_Buffer controlled_buffer_8
  assign WB = decoder_1_out5 ? 1'b0 : 1'bz;  // Controlled_Buffer controlled_buffer_9
  assign I = decoder_1_out5 ? not_3_out : 1'bz;  // Controlled_Buffer controlled_buffer_10
  assign S = decoder_1_out5 ? SaveIns : 1'bz;  // Controlled_Buffer controlled_buffer_11
  not not_3 (not_3_out, SaveIns);
  assign Result = and_1_out ? adder_2_out : 32'bz;  // Controlled_Buffer controlled_buffer_12
  assign Result = not_4_out ? adder_3_out : 32'bz;  // Controlled_Buffer controlled_buffer_13
  assign Saddr = decoder_1_out1 ? {8{1'b0}} : 8'bz;  // Controlled_Buffer controlled_buffer_14
  assign Saddr = decoder_1_out3 ? {8{1'b0}} : 8'bz;  // Controlled_Buffer controlled_buffer_15
  assign Saddr = decoder_1_out5 ? adder_1_out[9:2] : 8'bz;  // Controlled_Buffer controlled_buffer_16
  assign RAMSbInfo = decoder_1_out1 ? {8{1'b0}} : 8'bz;  // Controlled_Buffer controlled_buffer_17
  assign InfoLow2 = decoder_1_out1 ? 2'b00 : 2'bz;  // Controlled_Buffer controlled_buffer_18
  assign RAMSbInfo = decoder_1_out3 ? {8{1'b0}} : 8'bz;  // Controlled_Buffer controlled_buffer_19
  assign InfoLow2 = decoder_1_out3 ? 2'b00 : 2'bz;  // Controlled_Buffer controlled_buffer_20
  assign RAMSbInfo = decoder_1_out5 ? Cal2[7:0] : 8'bz;  // Controlled_Buffer controlled_buffer_21
  assign InfoLow2 = decoder_1_out5 ? adder_1_out[1:0] : 2'bz;  // Controlled_Buffer controlled_buffer_22
  assign WB = or_1_out ? 1'b0 : 1'bz;  // Controlled_Buffer controlled_buffer_23
  or or_1 (or_1_out, decoder_1_out0, decoder_1_out2, decoder_1_out4, decoder_1_out6, decoder_1_out7);
  not not_4 (not_4_out, and_1_out);
  and and_1 (and_1_out, Add, or_2_out);
  assign I = or_1_out ? 1'b0 : 1'bz;  // Controlled_Buffer controlled_buffer_24
  assign S = or_1_out ? 1'b0 : 1'bz;  // Controlled_Buffer controlled_buffer_25
  or or_2 (or_2_out, decoder_1_out1, decoder_1_out3, I);
  assign Saddr = or_1_out ? {8{1'b0}} : 8'bz;  // Controlled_Buffer controlled_buffer_26
  assign RAMSbInfo = or_1_out ? {8{1'b0}} : 8'bz;  // Controlled_Buffer controlled_buffer_27
  assign InfoLow2 = or_1_out ? 2'b00 : 2'bz;  // Controlled_Buffer controlled_buffer_28
endmodule

module DataRAM (
  input  [31:0] In32,
  input  [7:0] In8,
  input  WBus,
  input  RBus,
  input  [7:0] Saddr,
  input  ISOP,
  input  ISword,
  input  [1:0] Sel,
  input  clk,
  output [31:0] RAMInfo
);

  wire and_1_out, and_2_out, and_3_out, and_4_out, and_5_out, controlled_buffer_1_out,
       controlled_buffer_10_out, controlled_buffer_16_out, controlled_buffer_17_out, decoder_1_out0,
       decoder_1_out1, decoder_1_out2, decoder_1_out3, decoder_2_out0, decoder_2_out1, decoder_2_out2,
       decoder_2_out3, decoder_3_out0, decoder_3_out1, decoder_3_out2, decoder_3_out3, decoder_3_out4,
       decoder_3_out5, decoder_3_out6, decoder_3_out7, or_1_out, or_2_out, or_3_out, or_4_out;
  wire [7:0] controlled_buffer_4_out, controlled_buffer_5_out, controlled_buffer_13_out,
       controlled_buffer_22_out, multiplexer_1_out, ram_1_dout, ram_2_dout, ram_3_dout, ram_4_dout;
  wire [31:0] bit_extender_1_out;

  Decoder #(.select(2)) decoder_1 (
    .out0(decoder_1_out0), .out1(decoder_1_out1), .out2(decoder_1_out2), .out3(decoder_1_out3),
    .sel({ISword, ISOP}));  // open: en
  Decoder #(.select(2)) decoder_2 (
    .out0(decoder_2_out0), .out1(decoder_2_out1), .out2(decoder_2_out2), .out3(decoder_2_out3), .sel(Sel));  // open: en
  and and_1 (and_1_out, RBus, or_1_out);
  assign controlled_buffer_1_out = or_2_out ? 1'b0 : 1'bz;  // Controlled_Buffer controlled_buffer_1
  assign controlled_buffer_1_out = decoder_1_out3 ? WBus : 1'bz;  // Controlled_Buffer controlled_buffer_2
  assign controlled_buffer_1_out = decoder_1_out1 ? and_2_out : 1'bz;  // Controlled_Buffer controlled_buffer_3
  or or_1 (or_1_out, decoder_1_out1, decoder_1_out3);
  or or_2 (or_2_out, decoder_1_out0, decoder_1_out2);
  and and_2 (and_2_out, decoder_2_out0, WBus);
  assign controlled_buffer_4_out = decoder_1_out3 ? In32[7:0] : 8'bz;  // Controlled_Buffer controlled_buffer_4
  assign controlled_buffer_5_out = decoder_1_out3 ? In32[15:8] : 8'bz;  // Controlled_Buffer controlled_buffer_5
  assign controlled_buffer_4_out = decoder_1_out1 ? In8 : 8'bz;  // Controlled_Buffer controlled_buffer_6
  assign controlled_buffer_5_out = decoder_1_out1 ? In8 : 8'bz;  // Controlled_Buffer controlled_buffer_7
  assign controlled_buffer_4_out = or_2_out ? {8{1'b0}} : 8'bz;  // Controlled_Buffer controlled_buffer_8
  assign controlled_buffer_5_out = or_2_out ? {8{1'b0}} : 8'bz;  // Controlled_Buffer controlled_buffer_9
  assign controlled_buffer_10_out = or_2_out ? 1'b0 : 1'bz;  // Controlled_Buffer controlled_buffer_10
  assign controlled_buffer_10_out = decoder_1_out3 ? WBus : 1'bz;  // Controlled_Buffer controlled_buffer_11
  assign controlled_buffer_10_out = decoder_1_out1 ? and_3_out : 1'bz;  // Controlled_Buffer controlled_buffer_12
  or or_3 (or_3_out, and_1_out, or_2_out);
  and and_3 (and_3_out, decoder_2_out1, WBus);
  and and_4 (and_4_out, decoder_2_out2, WBus);
  assign controlled_buffer_13_out = decoder_1_out3 ? In32[23:16] : 8'bz;  // Controlled_Buffer controlled_buffer_13
  assign controlled_buffer_13_out = decoder_1_out1 ? In8 : 8'bz;  // Controlled_Buffer controlled_buffer_14
  assign controlled_buffer_13_out = or_2_out ? {8{1'b0}} : 8'bz;  // Controlled_Buffer controlled_buffer_15
  assign controlled_buffer_16_out = or_2_out ? 1'b0 : 1'bz;  // Controlled_Buffer controlled_buffer_16
  assign controlled_buffer_17_out = or_2_out ? 1'b0 : 1'bz;  // Controlled_Buffer controlled_buffer_17
  assign controlled_buffer_16_out = decoder_1_out3 ? WBus : 1'bz;  // Controlled_Buffer controlled_buffer_18
  assign controlled_buffer_17_out = decoder_1_out3 ? WBus : 1'bz;  // Controlled_Buffer controlled_buffer_19
  assign controlled_buffer_16_out = decoder_1_out1 ? and_4_out : 1'bz;  // Controlled_Buffer controlled_buffer_20
  assign controlled_buffer_17_out = decoder_1_out1 ? and_5_out : 1'bz;  // Controlled_Buffer controlled_buffer_21
  and and_5 (and_5_out, decoder_2_out3, WBus);
  assign controlled_buffer_22_out = decoder_1_out3 ? In32[31:24] : 8'bz;  // Controlled_Buffer controlled_buffer_22
  assign controlled_buffer_22_out = decoder_1_out1 ? In8 : 8'bz;  // Controlled_Buffer controlled_buffer_23
  assign controlled_buffer_22_out = or_2_out ? {8{1'b0}} : 8'bz;  // Controlled_Buffer controlled_buffer_24
  RAM #(.asyncread("true")) ram_1 (
    .addr(Saddr), .we(controlled_buffer_1_out), .oe(or_3_out), .clk(clk), .din(controlled_buffer_4_out),
    .dout(ram_1_dout));
  RAM #(.asyncread("true")) ram_2 (
    .addr(Saddr), .we(controlled_buffer_10_out), .oe(or_3_out), .clk(clk), .din(controlled_buffer_5_out),
    .dout(ram_2_dout));
  RAM #(.asyncread("true")) ram_3 (
    .addr(Saddr), .we(controlled_buffer_16_out), .oe(or_3_out), .clk(clk), .din(controlled_buffer_13_out),
    .dout(ram_3_dout));
  RAM #(.asyncread("true")) ram_4 (
    .addr(Saddr), .we(controlled_buffer_17_out), .oe(or_3_out), .clk(clk), .din(controlled_buffer_22_out),
    .dout(ram_4_dout));
  Multiplexer #(.select(2), .width(8)) multiplexer_1 (
    .in0(ram_1_dout), .in1(ram_2_dout), .in2(ram_3_dout), .in3(ram_4_dout), .out(multiplexer_1_out), .sel(Sel));
  assign bit_extender_1_out = {{24{1'b0}}, multiplexer_1_out};  // Bit_Extender bit_extender_1
  Decoder #(.select(3)) decoder_3 (
    .out0(decoder_3_out0), .out1(decoder_3_out1), .out2(decoder_3_out2), .out3(decoder_3_out3),
    .out4(decoder_3_out4), .out5(decoder_3_out5), .out6(decoder_3_out6), .out7(decoder_3_out7),
    .sel({ISOP, RBus, ISword}));  // open: en
  assign RAMInfo = decoder_3_out7 ? {ram_4_dout, ram_3_dout, ram_2_dout, ram_1_dout} : 32'bz;  // Controlled_Buffer controlled_buffer_25
  assign RAMInfo = decoder_3_out6 ? bit_extender_1_out : 32'bz;  // Controlled_Buffer controlled_buffer_26
  assign RAMInfo = or_4_out ? {32{1'b0}} : 32'bz;  // Controlled_Buffer controlled_buffer_27
  or or_4 (or_4_out, decoder_3_out0, decoder_3_out1, decoder_3_out2, decoder_3_out3, decoder_3_out4, decoder_3_out5);
endmodule
