// Logisim project MINIRISCVv3.circ as structural Verilog: 5 circuits, main circuit RegisterFile
module main (
  input  Reset
);

  wire alu_1_rb, Clk_out, decodeunit_1_add, decodeunit_1_aluusedop, decodeunit_1_errortypeop,
       decodeunit_1_jumpop, decodeunit_1_onlyrfusedop, decodeunit_1_va1, decodeunit_1_va2, decodeunit_1_var;
  wire [3:0] decodeunit_1_infoadd1, decodeunit_1_infoadd2, decodeunit_1_infoaddr;
  wire [7:0] pc_1_addr, pc_1_nextaddr;
  wire [31:0] alu_1_result, decodeunit_1_imdadd2, decodeunit_1_imdlui, registerfile_1_value1,
       registerfile_1_value2, rom_1_data;

  Clock Clk (.out(Clk_out));
  ROM #(.dataWidth(32)) rom_1 (.addr(pc_1_addr), .data(rom_1_data));
  PC pc_1 (
    .AddrC(alu_1_result), .Jump(decodeunit_1_jumpop), .clk(Clk_out), .Reset(Reset), .Addr(pc_1_addr),
    .NextAddr(pc_1_nextaddr));
  DecodeUnit decodeunit_1 (
    .Data(rom_1_data), .ErrorTypeOP(decodeunit_1_errortypeop), .ALUUsedOP(decodeunit_1_aluusedop),
    .OnlyRFusedOP(decodeunit_1_onlyrfusedop), .JumpOP(decodeunit_1_jumpop), .InfoAdd1(decodeunit_1_infoadd1),
    .VA1(decodeunit_1_va1), .InfoAdd2(decodeunit_1_infoadd2), .VA2(decodeunit_1_va2),
    .InfoAddR(decodeunit_1_infoaddr), .VAR(decodeunit_1_var), .ImdAdd2(decodeunit_1_imdadd2),
    .ImdLuI(decodeunit_1_imdlui), .Add(decodeunit_1_add));
  RegisterFile registerfile_1 (
    .ErrorOP(decodeunit_1_errortypeop), .ALUType(decodeunit_1_aluusedop),
    .GPRType(decodeunit_1_onlyrfusedop), .JumpType(decodeunit_1_jumpop), .Add1(decodeunit_1_infoadd1),
    .VA1(decodeunit_1_va1), .Add2(decodeunit_1_infoadd2), .VA2(decodeunit_1_va2),
    .AddR(decodeunit_1_infoaddr), .VR(decodeunit_1_var), .WBget(alu_1_rb), .InfoResult(alu_1_result),
    .InfoAdd2(decodeunit_1_imdadd2), .InfoLUI(decodeunit_1_imdlui), .InfoJump(pc_1_nextaddr), .clk(Clk_out),
    .R(Reset), .Value1(registerfile_1_value1), .Value2(registerfile_1_value2));
  ALU alu_1 (
    .Cal1(registerfile_1_value1), .Cal2(registerfile_1_value2), .Add(decodeunit_1_add),
    .ALUDemand(decodeunit_1_aluusedop), .JumpOP(decodeunit_1_jumpop), .Result(alu_1_result), .RB(alu_1_rb));

  // Notes on the sheet:
  //   contents of rom_1 (hex, n*v repeats v):
  //   123450b7 500113 fff00193 310233 1c00293 28367 6300393 5800413
endmodule

module PC (
  input  [31:0] AddrC,
  input  Jump,
  input  clk,
  input  Reset,
  output [7:0] Addr,
  output [7:0] NextAddr
);

  wire not_1_out;
  wire [31:0] adder_1_out, controlled_buffer_1_out, register_1_q;

  assign controlled_buffer_1_out = Jump ? AddrC : 32'bz;  // Controlled_Buffer controlled_buffer_1
  not not_1 (not_1_out, Jump);
  assign controlled_buffer_1_out = not_1_out ? {adder_1_out[31:10], NextAddr, adder_1_out[1:0]} : 32'bz;  // Controlled_Buffer controlled_buffer_2
  Register #(.width(32)) register_1 (
    .D(controlled_buffer_1_out), .en(1'b1), .clk(clk), .Q({register_1_q[31:10], Addr, register_1_q[1:0]}),
    .clr(Reset));
  Adder #(.width(32)) adder_1 (
    .a({register_1_q[31:10], Addr, register_1_q[1:0]}), .b(32'h4),
    .out({adder_1_out[31:10], NextAddr, adder_1_out[1:0]}));  // open: cin, cout
endmodule

module DecodeUnit (
  input  [31:0] Data,
  output ErrorTypeOP,
  output ALUUsedOP,
  output OnlyRFusedOP,
  output JumpOP,
  output [3:0] InfoAdd1,
  output VA1,
  output [3:0] InfoAdd2,
  output VA2,
  output [3:0] InfoAddR,
  output VAR,
  output [31:0] ImdAdd2,
  output [31:0] ImdLuI,
  output Add
);

  wire and_1_out, and_2_out, decoder_1_out2, decoder_1_out6, decoder_1_out7, decoder_1_out13, decoder_2_p3,
       not_1_out;

  not not_1 (not_1_out, Data[3]);
  nand nand_1 (ErrorTypeOP, Data[0], not_1_out, Data[1]);
  Decoder #(.select(4)) decoder_1 (
    .out2(decoder_1_out2), .out6(decoder_1_out6), .out7(decoder_1_out7), .out13(decoder_1_out13),
    .sel({Data[6:4], Data[2]}));  // open: out0, out1, out3, out4, out5, out8, out9, out10, out11, out12, out14, out15, en
  // Decoder #(.select(3)) decoder_2: pin names not known; wires that end beside it: Data[14:12], Data[11:7], decoder_2_p3, Data[19:15]
  assign ImdAdd2 = {{20{Data[31]}}, Data[31:20]};  // Bit_Extender bit_extender_1
  and and_1 (and_1_out, decoder_1_out2, decoder_2_p3);
  and and_2 (and_2_out, decoder_1_out6, decoder_2_p3);
  // AND_Gate and_3 is placed but not wired
  and and_4 (JumpOP, decoder_1_out13, decoder_2_p3);
  or or_1 (ALUUsedOP, and_1_out, JumpOP, and_2_out);
  buf or_2 (OnlyRFusedOP, decoder_1_out7);  // OR_Gate
  or or_3 (VA1, and_1_out, and_2_out, JumpOP);
  buf or_4 (VA2, and_2_out);  // OR_Gate
  or or_5 (VAR, and_1_out, and_2_out, decoder_1_out7, JumpOP);
  or or_6 (Add, and_2_out, JumpOP, and_1_out);

  assign ImdLuI = {Data[31:12], {12{1'b0}}};
  assign InfoAdd1 = Data[18:15];
  assign InfoAdd2 = Data[23:20];
  assign InfoAddR = Data[10:7];
endmodule

module RegisterFile (
  input  ErrorOP,
  input  ALUType,
  input  GPRType,
  input  JumpType,
  input  [3:0] Add1,
  input  VA1,
  input  [3:0] Add2,
  input  VA2,
  input  [3:0] AddR,
  input  VR,
  input  WBget,
  input  [31:0] InfoResult,
  input  [31:0] InfoAdd2,
  input  [31:0] InfoLUI,
  input  [7:0] InfoJump,
  input  clk,
  input  R,
  output [31:0] Value1,
  output [31:0] Value2
);

  wire and_1_out, and_2_out, and_3_out, and_4_out, and_5_out, decoder_1_out0, decoder_1_out1, decoder_1_out2,
       decoder_1_out3, decoder_1_out4, decoder_1_out5, decoder_1_out6, decoder_1_out7, decoder_1_out8,
       decoder_1_out9, decoder_1_out10, decoder_1_out11, decoder_1_out12, decoder_1_out13, decoder_1_out14,
       decoder_1_out15, decoder_2_out0, decoder_2_out1, decoder_2_out2, decoder_2_out3, decoder_2_out4,
       decoder_2_out5, decoder_2_out6, decoder_2_out7, decoder_2_out8, decoder_2_out9, decoder_2_out10,
       decoder_2_out11, decoder_2_out12, decoder_2_out13, decoder_2_out14, decoder_2_out15, decoder_3_out16,
       decoder_3_out17, decoder_3_out18, decoder_3_out19, decoder_3_out20, decoder_3_out21, decoder_3_out22,
       decoder_3_out23, decoder_3_out24, decoder_3_out25, decoder_3_out26, decoder_3_out27, decoder_3_out28,
       decoder_3_out29, decoder_3_out30, decoder_3_out31, not_1_out, not_2_out;
  wire [3:0] controlled_buffer_5_out, controlled_buffer_6_out;
  wire [4:4] or_1_out;
  wire [31:0] controlled_buffer_1_out, controlled_buffer_4_out, controlled_buffer_7_out, register_1_q,
       register_2_q, register_3_q, register_4_q, register_5_q, register_6_q, register_7_q, register_8_q,
       register_9_q, register_13_q, undriven, undriven_2, undriven_3, undriven_4, undriven_5, undriven_6;

  and and_1 (and_1_out, JumpType, VR);
  and and_2 (and_2_out, GPRType, VR);
  or or_1 (or_1_out[4], and_2_out, and_1_out, and_3_out);
  and and_3 (and_3_out, VR, WBget);
  assign controlled_buffer_1_out = WBget ? InfoResult : 32'bz;  // Controlled_Buffer controlled_buffer_1
  assign controlled_buffer_1_out = GPRType ? InfoLUI : 32'bz;  // Controlled_Buffer controlled_buffer_2
  assign controlled_buffer_1_out = JumpType ? {{22{1'b0}}, InfoJump, 2'b00} : 32'bz;  // Controlled_Buffer controlled_buffer_3
  not not_1 (not_1_out, VA2);
  assign controlled_buffer_4_out = not_1_out ? InfoAdd2 : 32'bz;  // Controlled_Buffer controlled_buffer_4
  Decoder #(.select(4)) decoder_1 (
    .out0(decoder_1_out0), .out1(decoder_1_out1), .out2(decoder_1_out2), .out3(decoder_1_out3),
    .out4(decoder_1_out4), .out5(decoder_1_out5), .out6(decoder_1_out6), .out7(decoder_1_out7),
    .out8(decoder_1_out8), .out9(decoder_1_out9), .out10(decoder_1_out10), .out11(decoder_1_out11),
    .out12(decoder_1_out12), .out13(decoder_1_out13), .out14(decoder_1_out14), .out15(decoder_1_out15),
    .sel(controlled_buffer_5_out));  // open: en
  assign controlled_buffer_5_out = and_4_out ? Add1 : 4'bz;  // Controlled_Buffer controlled_buffer_5
  and and_4 (and_4_out, ALUType, VA1);
  assign controlled_buffer_6_out = and_5_out ? Add2 : 4'bz;  // Controlled_Buffer controlled_buffer_6
  Decoder #(.select(4)) decoder_2 (
    .out0(decoder_2_out0), .out1(decoder_2_out1), .out2(decoder_2_out2), .out3(decoder_2_out3),
    .out4(decoder_2_out4), .out5(decoder_2_out5), .out6(decoder_2_out6), .out7(decoder_2_out7),
    .out8(decoder_2_out8), .out9(decoder_2_out9), .out10(decoder_2_out10), .out11(decoder_2_out11),
    .out12(decoder_2_out12), .out13(decoder_2_out13), .out14(decoder_2_out14), .out15(decoder_2_out15),
    .sel(controlled_buffer_6_out));  // open: en
  and and_5 (and_5_out, ALUType, VA2);
  Decoder #(.select(5)) decoder_3 (
    .out16(decoder_3_out16), .out17(decoder_3_out17), .out18(decoder_3_out18), .out19(decoder_3_out19),
    .out20(decoder_3_out20), .out21(decoder_3_out21), .out22(decoder_3_out22), .out23(decoder_3_out23),
    .out24(decoder_3_out24), .out25(decoder_3_out25), .out26(decoder_3_out26), .out27(decoder_3_out27),
    .out28(decoder_3_out28), .out29(decoder_3_out29), .out30(decoder_3_out30), .out31(decoder_3_out31),
    .sel({or_1_out[4], AddR}));  // open: out0, out1, out2, out3, out4, out5, out6, out7, out8, out9, out10, out11, out12, out13, out14, out15, en
  Register #(.width(32)) register_1 (
    .D(controlled_buffer_1_out), .en(decoder_3_out16), .clk(clk), .Q(register_1_q), .clr(R));
  Register #(.width(32)) register_2 (
    .D(controlled_buffer_1_out), .en(decoder_3_out17), .clk(clk), .Q(register_2_q), .clr(R));
  Register #(.width(32)) register_3 (
    .D(controlled_buffer_1_out), .en(decoder_3_out18), .clk(clk), .Q(register_3_q), .clr(R));
  Register #(.width(32)) register_4 (
    .D(controlled_buffer_1_out), .en(decoder_3_out19), .clk(clk), .Q(register_4_q), .clr(R));
  assign controlled_buffer_7_out = decoder_1_out0 ? register_1_q : 32'bz;  // Controlled_Buffer controlled_buffer_7
  assign controlled_buffer_7_out = decoder_1_out1 ? register_2_q : 32'bz;  // Controlled_Buffer controlled_buffer_8
  assign controlled_buffer_7_out = decoder_1_out2 ? register_3_q : 32'bz;  // Controlled_Buffer controlled_buffer_9
  assign controlled_buffer_7_out = decoder_1_out3 ? register_4_q : 32'bz;  // Controlled_Buffer controlled_buffer_10
  assign controlled_buffer_4_out = decoder_2_out0 ? register_1_q : 32'bz;  // Controlled_Buffer controlled_buffer_11
  assign controlled_buffer_4_out = decoder_2_out1 ? register_2_q : 32'bz;  // Controlled_Buffer controlled_buffer_12
  assign controlled_buffer_4_out = decoder_2_out2 ? register_3_q : 32'bz;  // Controlled_Buffer controlled_buffer_13
  assign controlled_buffer_4_out = decoder_2_out3 ? register_4_q : 32'bz;  // Controlled_Buffer controlled_buffer_14
  Register #(.width(32)) register_5 (
    .D(controlled_buffer_1_out), .en(decoder_3_out20), .clk(clk), .Q(register_5_q), .clr(R));
  Register #(.width(32)) register_6 (
    .D(controlled_buffer_1_out), .en(decoder_3_out21), .clk(clk), .Q(register_6_q), .clr(R));
  Register #(.width(32)) register_7 (
    .D(controlled_buffer_1_out), .en(decoder_3_out22), .clk(clk), .Q(register_7_q), .clr(R));
  Register #(.width(32)) register_8 (
    .D(controlled_buffer_1_out), .en(decoder_3_out23), .clk(clk), .Q(register_8_q), .clr(R));
  assign controlled_buffer_7_out = decoder_1_out4 ? register_5_q : 32'bz;  // Controlled_Buffer controlled_buffer_15
  assign controlled_buffer_7_out = decoder_1_out5 ? register_6_q : 32'bz;  // Controlled_Buffer controlled_buffer_16
  assign controlled_buffer_7_out = decoder_1_out6 ? register_7_q : 32'bz;  // Controlled_Buffer controlled_buffer_17
  assign controlled_buffer_7_out = decoder_1_out7 ? register_8_q : 32'bz;  // Controlled_Buffer controlled_buffer_18
  assign controlled_buffer_4_out = decoder_2_out4 ? register_5_q : 32'bz;  // Controlled_Buffer controlled_buffer_19
  assign controlled_buffer_4_out = decoder_2_out5 ? register_6_q : 32'bz;  // Controlled_Buffer controlled_buffer_20
  assign controlled_buffer_4_out = decoder_2_out6 ? register_7_q : 32'bz;  // Controlled_Buffer controlled_buffer_21
  assign controlled_buffer_4_out = decoder_2_out7 ? register_8_q : 32'bz;  // Controlled_Buffer controlled_buffer_22
  Register #(.width(32)) register_9 (
    .D(controlled_buffer_1_out), .en(decoder_3_out24), .clk(clk), .Q(register_9_q), .clr(R));
  Register #(.width(32)) register_10 (
    .D(controlled_buffer_1_out), .en(decoder_3_out25), .clk(clk), .clr(R));  // open: Q
  Register #(.width(32)) register_11 (
    .D(controlled_buffer_1_out), .en(decoder_3_out26), .clk(clk), .clr(R));  // open: Q
  Register #(.width(32)) register_12 (
    .D(controlled_buffer_1_out), .en(decoder_3_out27), .clk(clk), .clr(R));  // open: Q
  assign controlled_buffer_7_out = decoder_1_out8 ? register_9_q : 32'bz;  // Controlled_Buffer controlled_buffer_23
  assign controlled_buffer_7_out = decoder_1_out9 ? undriven : 32'bz;  // Controlled_Buffer controlled_buffer_24
  assign controlled_buffer_7_out = decoder_1_out10 ? undriven_2 : 32'bz;  // Controlled_Buffer controlled_buffer_25
  assign controlled_buffer_7_out = decoder_1_out11 ? undriven_3 : 32'bz;  // Controlled_Buffer controlled_buffer_26
  assign controlled_buffer_4_out = decoder_2_out8 ? register_9_q : 32'bz;  // Controlled_Buffer controlled_buffer_27
  assign controlled_buffer_4_out = decoder_2_out9 ? undriven : 32'bz;  // Controlled_Buffer controlled_buffer_28
  assign controlled_buffer_4_out = decoder_2_out10 ? undriven_2 : 32'bz;  // Controlled_Buffer controlled_buffer_29
  assign controlled_buffer_4_out = decoder_2_out11 ? undriven_3 : 32'bz;  // Controlled_Buffer controlled_buffer_30
  Register #(.width(32)) register_13 (
    .D(controlled_buffer_1_out), .en(decoder_3_out28), .clk(clk), .Q(register_13_q), .clr(R));
  Register #(.width(32)) register_14 (
    .D(controlled_buffer_1_out), .en(decoder_3_out29), .clk(clk), .clr(R));  // open: Q
  Register #(.width(32)) register_15 (
    .D(controlled_buffer_1_out), .en(decoder_3_out30), .clk(clk), .clr(R));  // open: Q
  Register #(.width(32)) register_16 (
    .D(controlled_buffer_1_out), .en(decoder_3_out31), .clk(clk), .clr(R));  // open: Q
  assign controlled_buffer_7_out = decoder_1_out12 ? register_13_q : 32'bz;  // Controlled_Buffer controlled_buffer_31
  assign controlled_buffer_7_out = decoder_1_out13 ? undriven_4 : 32'bz;  // Controlled_Buffer controlled_buffer_32
  assign controlled_buffer_7_out = decoder_1_out14 ? undriven_5 : 32'bz;  // Controlled_Buffer controlled_buffer_33
  assign controlled_buffer_7_out = decoder_1_out15 ? undriven_6 : 32'bz;  // Controlled_Buffer controlled_buffer_34
  assign controlled_buffer_4_out = decoder_2_out12 ? register_13_q : 32'bz;  // Controlled_Buffer controlled_buffer_35
  assign controlled_buffer_4_out = decoder_2_out13 ? undriven_4 : 32'bz;  // Controlled_Buffer controlled_buffer_36
  assign controlled_buffer_4_out = decoder_2_out14 ? undriven_5 : 32'bz;  // Controlled_Buffer controlled_buffer_37
  assign controlled_buffer_4_out = decoder_2_out15 ? undriven_6 : 32'bz;  // Controlled_Buffer controlled_buffer_38
  not not_2 (not_2_out, ErrorOP);
  assign Value1 = not_2_out ? controlled_buffer_7_out : 32'bz;  // Controlled_Buffer controlled_buffer_39
  assign Value1 = ErrorOP ? {32{1'b0}} : 32'bz;  // Controlled_Buffer controlled_buffer_40
  assign Value2 = not_2_out ? controlled_buffer_4_out : 32'bz;  // Controlled_Buffer controlled_buffer_41
  assign Value2 = ErrorOP ? {32{1'b0}} : 32'bz;  // Controlled_Buffer controlled_buffer_42
endmodule

module ALU (
  input  [31:0] Cal1,
  input  [31:0] Cal2,
  input  Add,
  input  ALUDemand,
  input  JumpOP,
  output [31:0] Result,
  output RB
);

  wire and_1_out, not_1_out;
  wire [31:0] adder_1_out, multiplexer_1_out;

  Adder #(.width(32)) adder_1 (.a(Cal1), .b(Cal2), .out(adder_1_out));  // open: cin, cout
  Multiplexer #(.width(32)) multiplexer_1 (.in0({32{1'b0}}), .in1(adder_1_out), .out(multiplexer_1_out), .sel(Add));
  not not_1 (not_1_out, JumpOP);
  Multiplexer #(.width(32)) multiplexer_2 (.in0({32{1'b0}}), .in1(multiplexer_1_out), .out(Result), .sel(ALUDemand));
  and and_1 (and_1_out, ALUDemand, not_1_out);
  buf buffer_1 (RB, and_1_out);
endmodule
