// Logisim project sCPUsamplecmp.circ as structural Verilog: 25 circuits, main circuit main
module main (
  input  [7:0] PCP,
  input  R,
  input  PR,
  output [15:0] out_4,
  output [15:0] out_5,
  output [7:0] O
);

  wire alu_1_aluop, alu_1_calv, alu_1_oav, alu_1_os, alu_1_possubct, clk_out, compiler_1_oc,
       desvunitcoder_1_a, desvunitcoder_1_p, desvunitcoder_1_s, desvunitcoder_1_va1, desvunitcoder_1_va2,
       desvunitcoder_1_va3, desvunitcoder_1_vd1, desvunitcoder_1_vd2, desvunitcoder_1_wt, encoder_1_ov,
       gpr_1_oa, gpr_1_op, gpr_1_os, gpr_1_va, not_1_out, pc_1_c, pc_1_d4clk, svunit_1_vo;
  wire [3:0] alu_1_oaddress, compiler_1_oa, desvunitcoder_1_a1, desvunitcoder_1_a2, desvunitcoder_1_a3,
       gpr_1_oaddress, pc_1_s;
  wire [7:0] alu_1_d, desvunitcoder_1_d1, desvunitcoder_1_d2, gpr_1_o2;
  wire [15:0] compiler_1_od, encoder_1_op;

  Clock clk (.out(clk_out));
  not not_1 (not_1_out, PR);
  PC pc_1 (.D(PCP), .clk(clk_out), .R(R), .E(not_1_out), .S(pc_1_s), .C(pc_1_c), .D4clk(pc_1_d4clk));
  Compiler compiler_1 (.IA(pc_1_s), .C(pc_1_c), .OD(compiler_1_od), .OA(compiler_1_oa), .OC(compiler_1_oc));
  ALU alu_1 (
    .I1(O), .I2(gpr_1_o2), .A3(gpr_1_oaddress), .VA3(gpr_1_va), .S(gpr_1_os), .A(gpr_1_oa), .P(gpr_1_op),
    .D(alu_1_d), .PosSubCT(alu_1_possubct), .CalV(alu_1_calv), .OAddress(alu_1_oaddress), .OAV(alu_1_oav),
    .OS(alu_1_os), .ALUOP(alu_1_aluop));
  SvUnit svunit_1 (
    .I(compiler_1_od), .W(compiler_1_oc), .R(R), .clk(clk_out), .clkd4(pc_1_d4clk), .C(pc_1_c),
    .A(compiler_1_oa), .O(out_4), .VO(svunit_1_vo));
  Encoder encoder_1 (
    .D(alu_1_d), .C(alu_1_possubct), .VD(alu_1_calv), .A(alu_1_oaddress), .VA(alu_1_oav), .S(alu_1_os),
    .ALUOP(alu_1_aluop), .OP(encoder_1_op), .OV(encoder_1_ov));  // open: OC, PSpro
  DeSvUnitCoder desvunitcoder_1 (
    .I(out_5), .D1(desvunitcoder_1_d1), .VD1(desvunitcoder_1_vd1), .D2(desvunitcoder_1_d2),
    .VD2(desvunitcoder_1_vd2), .A1(desvunitcoder_1_a1), .VA1(desvunitcoder_1_va1), .A2(desvunitcoder_1_a2),
    .VA2(desvunitcoder_1_va2), .A3(desvunitcoder_1_a3), .VA3(desvunitcoder_1_va3), .S(desvunitcoder_1_s),
    .A(desvunitcoder_1_a), .P(desvunitcoder_1_p), .WT(desvunitcoder_1_wt));
  TimeController timecontroller_1 (
    .NxOdrIns(out_4), .ExctIns(encoder_1_op), .VN(svunit_1_vo), .VE(encoder_1_ov), .R(R), .C(pc_1_c),
    .clk(clk_out), .clk4(pc_1_d4clk), .ToDecoder(out_5));
  GPR gpr_1 (
    .D1(desvunitcoder_1_d1), .VD1(desvunitcoder_1_vd1), .D2(desvunitcoder_1_d2), .VD2(desvunitcoder_1_vd2),
    .A1(desvunitcoder_1_a1), .VA1(desvunitcoder_1_va1), .A2(desvunitcoder_1_a2), .VA2(desvunitcoder_1_va2),
    .A3(desvunitcoder_1_a3), .VA3(desvunitcoder_1_va3), .S(desvunitcoder_1_s), .A(desvunitcoder_1_a),
    .P(desvunitcoder_1_p), .WT(desvunitcoder_1_wt), .clk(clk_out), .O1(O), .O2(gpr_1_o2),
    .OAddress(gpr_1_oaddress), .VA(gpr_1_va), .OS(gpr_1_os), .OA(gpr_1_oa), .OP(gpr_1_op));
endmodule

module PC (
  input  [7:0] D,
  input  clk,
  input  R,
  input  E,
  output [3:0] S,
  output C,
  output D4clk
);

  wire not_1_out;
  wire [7:0] add8b_1_o, controlled_buffer_1_out, reg4_1_s;

  not not_1 (not_1_out, E);
  assign controlled_buffer_1_out = E ? D : 8'bz;  // Controlled_Buffer controlled_buffer_1
  assign controlled_buffer_1_out = not_1_out ? add8b_1_o : 8'bz;  // Controlled_Buffer controlled_buffer_2
  Reg4 reg4_1 (
    .D(controlled_buffer_1_out), .clk(clk), .R(R), .E(1'b1), .S({reg4_1_s[7:6], S[3:1], D4clk, reg4_1_s[1:0]}));  // open: I
  not not_2 (C, reg4_1_s[6]);
  Add8b add8b_1 (.I(1'b0), .A({reg4_1_s[7:6], S[3:1], D4clk, reg4_1_s[1:0]}), .B(8'h1), .O(add8b_1_o));  // open: OO

  assign S[0] = D4clk;
endmodule

module Compiler (
  input  [3:0] IA,
  input  C,
  output [15:0] OD,
  output [3:0] OA,
  output OC
);

  wire decoder4to16_1_o0000, decoder4to16_1_o0001, decoder4to16_1_o0010, decoder4to16_1_o0011,
       decoder4to16_1_o0100, decoder4to16_1_o0101, decoder4to16_1_o0110, decoder4to16_1_o0111,
       decoder4to16_1_o1000, decoder4to16_1_o1001, decoder4to16_1_o1010, decoder4to16_1_o1011,
       decoder4to16_1_o1100, decoder4to16_1_o1101, decoder4to16_1_o1110, decoder4to16_1_o1111;

  Decoder4to16 decoder4to16_1 (
    .I(IA), .O0000(decoder4to16_1_o0000), .O0001(decoder4to16_1_o0001), .O0010(decoder4to16_1_o0010),
    .O0011(decoder4to16_1_o0011), .O0100(decoder4to16_1_o0100), .O0101(decoder4to16_1_o0101),
    .O0110(decoder4to16_1_o0110), .O0111(decoder4to16_1_o0111), .O1000(decoder4to16_1_o1000),
    .O1001(decoder4to16_1_o1001), .O1010(decoder4to16_1_o1010), .O1011(decoder4to16_1_o1011),
    .O1100(decoder4to16_1_o1100), .O1101(decoder4to16_1_o1101), .O1110(decoder4to16_1_o1110),
    .O1111(decoder4to16_1_o1111));
  assign OD = decoder4to16_1_o0000 ? 16'hf000 : 16'bz;  // Controlled_Buffer controlled_buffer_1
  assign OD = decoder4to16_1_o0001 ? 16'h1 : 16'bz;  // Controlled_Buffer controlled_buffer_2
  assign OD = decoder4to16_1_o0010 ? 16'h102 : 16'bz;  // Controlled_Buffer controlled_buffer_3
  assign OD = decoder4to16_1_o0011 ? 16'h3330 : 16'bz;  // Controlled_Buffer controlled_buffer_4
  assign OD = decoder4to16_1_o0100 ? 16'h3001 : 16'bz;  // Controlled_Buffer controlled_buffer_5
  assign OD = decoder4to16_1_o0101 ? 16'h3330 : 16'bz;  // Controlled_Buffer controlled_buffer_6
  assign OD = decoder4to16_1_o0110 ? 16'h3001 : 16'bz;  // Controlled_Buffer controlled_buffer_7
  assign OD = decoder4to16_1_o0111 ? 16'h3330 : 16'bz;  // Controlled_Buffer controlled_buffer_8
  assign OD = decoder4to16_1_o1000 ? 16'h3001 : 16'bz;  // Controlled_Buffer controlled_buffer_9
  assign OD = decoder4to16_1_o1001 ? 16'h3330 : 16'bz;  // Controlled_Buffer controlled_buffer_10
  assign OD = decoder4to16_1_o1010 ? 16'h3001 : 16'bz;  // Controlled_Buffer controlled_buffer_11
  assign OD = decoder4to16_1_o1011 ? 16'h3330 : 16'bz;  // Controlled_Buffer controlled_buffer_12
  assign OD = decoder4to16_1_o1100 ? 16'h1300 : 16'bz;  // Controlled_Buffer controlled_buffer_13
  assign OD = decoder4to16_1_o1101 ? 16'hf000 : 16'bz;  // Controlled_Buffer controlled_buffer_14
  assign OD = decoder4to16_1_o1110 ? 16'h9000 : 16'bz;  // Controlled_Buffer controlled_buffer_15
  assign OD = decoder4to16_1_o1111 ? 16'h9000 : 16'bz;  // Controlled_Buffer controlled_buffer_16

  assign OA = IA;
  assign OC = C;
endmodule

module SvUnit (
  input  [15:0] I,
  input  W,
  input  R,
  input  clk,
  input  clkd4,
  input  C,
  input  [3:0] A,
  output [15:0] O,
  output VO
);

  wire and_1_out, clkanalysier_1_vd, L2_o00, L2_o01, L2_o10, L2_o11, not_1_out, not_2_out, not_3_out,
       signalchecker_1_e, signalchecker_1_g, signalchecker_2_e, signalchecker_2_g, signalchecker_3_e,
       signalchecker_3_g, signalchecker_4_e, signalchecker_4_g, signalchecker_5_e, signalchecker_5_g,
       signalchecker_6_e, signalchecker_6_g, signalchecker_7_e, signalchecker_7_g, signalchecker_8_e,
       signalchecker_8_g, signalchecker_9_e, signalchecker_9_g, signalchecker_10_e, signalchecker_10_g,
       signalchecker_11_e, signalchecker_11_g, signalchecker_12_e, signalchecker_12_g, signalchecker_13_e,
       signalchecker_13_g, signalchecker_14_e, signalchecker_14_g, signalchecker_15_e, signalchecker_15_g,
       signalchecker_16_e, signalchecker_16_g, U2_o00, U2_o01, U2_o10, U2_o11;
  wire [15:0] R0000_s, R0001_s, R0010_s, R0011_s, R0100_s, R0101_s, R0110_s, R0111_s, R1000_s, R1001_s,
       R1010_s, R1011_s, R1101_s, R1110_s, R1111_s, reg16b_1_s;

  not not_1 (not_1_out, W);
  not not_2 (not_2_out, R);
  and and_1 (and_1_out, not_1_out, not_2_out);
  assign VO = C ? and_1_out : 1'bz;  // Controlled_Buffer controlled_buffer_1
  not not_3 (not_3_out, C);
  assign VO = not_3_out ? clkanalysier_1_vd : 1'bz;  // Controlled_Buffer controlled_buffer_2
  Decoder2to4 U2 (.I(A[3:2]), .O11(U2_o11), .O10(U2_o10), .O01(U2_o01), .O00(U2_o00));
  ClkAnalysier clkanalysier_1 (.clkd4(clkd4), .clk(clk), .VD(clkanalysier_1_vd));
  SignalChecker signalchecker_1 (.S1(L2_o00), .S2(U2_o00), .W(W), .E(signalchecker_1_e), .G(signalchecker_1_g));
  SignalChecker signalchecker_2 (.S1(L2_o00), .S2(U2_o01), .W(W), .E(signalchecker_2_e), .G(signalchecker_2_g));
  SignalChecker signalchecker_3 (.S1(L2_o00), .S2(U2_o10), .W(W), .E(signalchecker_3_e), .G(signalchecker_3_g));
  SignalChecker signalchecker_4 (.S1(L2_o00), .S2(U2_o11), .W(W), .E(signalchecker_4_e), .G(signalchecker_4_g));
  Reg16b R0000 (.D(I), .clk(clk), .R(R), .E(signalchecker_1_e), .S(R0000_s));
  assign O = signalchecker_1_g ? R0000_s : 16'bz;  // Controlled_Buffer controlled_buffer_3
  Reg16b R0100 (.D(I), .clk(clk), .R(R), .E(signalchecker_2_e), .S(R0100_s));
  assign O = signalchecker_2_g ? R0100_s : 16'bz;  // Controlled_Buffer controlled_buffer_4
  Reg16b R1000 (.D(I), .clk(clk), .R(R), .E(signalchecker_3_e), .S(R1000_s));
  assign O = signalchecker_3_g ? R1000_s : 16'bz;  // Controlled_Buffer controlled_buffer_5
  Reg16b reg16b_1 (.D(I), .clk(clk), .R(R), .E(signalchecker_4_e), .S(reg16b_1_s));
  assign O = signalchecker_4_g ? reg16b_1_s : 16'bz;  // Controlled_Buffer controlled_buffer_6
  Decoder2to4 L2 (.I(A[1:0]), .O11(L2_o11), .O10(L2_o10), .O01(L2_o01), .O00(L2_o00));
  Reg16b R0001 (.D(I), .clk(clk), .R(R), .E(signalchecker_5_e), .S(R0001_s));
  assign O = signalchecker_5_g ? R0001_s : 16'bz;  // Controlled_Buffer controlled_buffer_7
  SignalChecker signalchecker_5 (.S1(L2_o01), .S2(U2_o00), .W(W), .E(signalchecker_5_e), .G(signalchecker_5_g));
  Reg16b R0101 (.D(I), .clk(clk), .R(R), .E(signalchecker_6_e), .S(R0101_s));
  assign O = signalchecker_6_g ? R0101_s : 16'bz;  // Controlled_Buffer controlled_buffer_8
  SignalChecker signalchecker_6 (.S1(L2_o01), .S2(U2_o01), .W(W), .E(signalchecker_6_e), .G(signalchecker_6_g));
  Reg16b R1001 (.D(I), .clk(clk), .R(R), .E(signalchecker_7_e), .S(R1001_s));
  assign O = signalchecker_7_g ? R1001_s : 16'bz;  // Controlled_Buffer controlled_buffer_9
  SignalChecker signalchecker_7 (.S1(L2_o01), .S2(U2_o10), .W(W), .E(signalchecker_7_e), .G(signalchecker_7_g));
  Reg16b R1101 (.D(I), .clk(clk), .R(R), .E(signalchecker_8_e), .S(R1101_s));
  assign O = signalchecker_8_g ? R1101_s : 16'bz;  // Controlled_Buffer controlled_buffer_10
  SignalChecker signalchecker_8 (.S1(L2_o01), .S2(U2_o11), .W(W), .E(signalchecker_8_e), .G(signalchecker_8_g));
  Reg16b R0010 (.D(I), .clk(clk), .R(R), .E(signalchecker_9_e), .S(R0010_s));
  assign O = signalchecker_9_g ? R0010_s : 16'bz;  // Controlled_Buffer controlled_buffer_11
  SignalChecker signalchecker_9 (.S1(L2_o10), .S2(U2_o00), .W(W), .E(signalchecker_9_e), .G(signalchecker_9_g));
  Reg16b R0110 (.D(I), .clk(clk), .R(R), .E(signalchecker_10_e), .S(R0110_s));
  assign O = signalchecker_10_g ? R0110_s : 16'bz;  // Controlled_Buffer controlled_buffer_12
  SignalChecker signalchecker_10 (.S1(L2_o10), .S2(U2_o01), .W(W), .E(signalchecker_10_e), .G(signalchecker_10_g));
  Reg16b R1010 (.D(I), .clk(clk), .R(R), .E(signalchecker_11_e), .S(R1010_s));
  assign O = signalchecker_11_g ? R1010_s : 16'bz;  // Controlled_Buffer controlled_buffer_13
  SignalChecker signalchecker_11 (.S1(L2_o10), .S2(U2_o10), .W(W), .E(signalchecker_11_e), .G(signalchecker_11_g));
  Reg16b R1110 (.D(I), .clk(clk), .R(R), .E(signalchecker_12_e), .S(R1110_s));
  assign O = signalchecker_12_g ? R1110_s : 16'bz;  // Controlled_Buffer controlled_buffer_14
  SignalChecker signalchecker_12 (.S1(L2_o10), .S2(U2_o11), .W(W), .E(signalchecker_12_e), .G(signalchecker_12_g));
  Reg16b R0011 (.D(I), .clk(clk), .R(R), .E(signalchecker_13_e), .S(R0011_s));
  assign O = signalchecker_13_g ? R0011_s : 16'bz;  // Controlled_Buffer controlled_buffer_15
  SignalChecker signalchecker_13 (.S1(L2_o11), .S2(U2_o00), .W(W), .E(signalchecker_13_e), .G(signalchecker_13_g));
  Reg16b R0111 (.D(I), .clk(clk), .R(R), .E(signalchecker_14_e), .S(R0111_s));
  assign O = signalchecker_14_g ? R0111_s : 16'bz;  // Controlled_Buffer controlled_buffer_16
  SignalChecker signalchecker_14 (.S1(L2_o11), .S2(U2_o01), .W(W), .E(signalchecker_14_e), .G(signalchecker_14_g));
  Reg16b R1011 (.D(I), .clk(clk), .R(R), .E(signalchecker_15_e), .S(R1011_s));
  assign O = signalchecker_15_g ? R1011_s : 16'bz;  // Controlled_Buffer controlled_buffer_17
  SignalChecker signalchecker_15 (.S1(L2_o11), .S2(U2_o10), .W(W), .E(signalchecker_15_e), .G(signalchecker_15_g));
  Reg16b R1111 (.D(I), .clk(clk), .R(R), .E(signalchecker_16_e), .S(R1111_s));
  assign O = signalchecker_16_g ? R1111_s : 16'bz;  // Controlled_Buffer controlled_buffer_18
  SignalChecker signalchecker_16 (.S1(L2_o11), .S2(U2_o11), .W(W), .E(signalchecker_16_e), .G(signalchecker_16_g));
endmodule

module DeSvUnitCoder (
  input  [15:0] I,
  output [7:0] D1,
  output VD1,
  output [7:0] D2,
  output VD2,
  output [3:0] A1,
  output VA1,
  output [3:0] A2,
  output VA2,
  output [3:0] A3,
  output VA3,
  output S,
  output A,
  output P,
  output WT
);

  wire decoder4to16_1_o0000, decoder4to16_1_o0001, decoder4to16_1_o0010, decoder4to16_1_o0011,
       decoder4to16_1_o0100, decoder4to16_1_o0101, decoder4to16_1_o1110, decoder4to16_1_o1111;

  Decoder4to16 decoder4to16_1 (
    .I(I[15:12]), .O0000(decoder4to16_1_o0000), .O0001(decoder4to16_1_o0001), .O0010(decoder4to16_1_o0010),
    .O0011(decoder4to16_1_o0011), .O0100(decoder4to16_1_o0100), .O0101(decoder4to16_1_o0101),
    .O1110(decoder4to16_1_o1110), .O1111(decoder4to16_1_o1111));  // open: O0110, O0111, O1000, O1001, O1010, O1011, O1100, O1101
  assign D1 = decoder4to16_1_o0000 ? I[7:0] : 8'bz;  // Controlled_Buffer controlled_buffer_1
  assign VD1 = decoder4to16_1_o0000 ? 1'b1 : 1'bz;  // Controlled_Buffer controlled_buffer_2
  assign VD2 = decoder4to16_1_o0000 ? 1'b0 : 1'bz;  // Controlled_Buffer controlled_buffer_3
  assign A1 = decoder4to16_1_o0000 ? I[11:8] : 4'bz;  // Controlled_Buffer controlled_buffer_4
  assign VA1 = decoder4to16_1_o0000 ? 1'b1 : 1'bz;  // Controlled_Buffer controlled_buffer_5
  assign VA2 = decoder4to16_1_o0000 ? 1'b0 : 1'bz;  // Controlled_Buffer controlled_buffer_6
  assign VA3 = decoder4to16_1_o0000 ? 1'b0 : 1'bz;  // Controlled_Buffer controlled_buffer_7
  assign S = decoder4to16_1_o0000 ? 1'b1 : 1'bz;  // Controlled_Buffer controlled_buffer_8
  assign A = decoder4to16_1_o0000 ? 1'b0 : 1'bz;  // Controlled_Buffer controlled_buffer_9
  assign P = decoder4to16_1_o0000 ? 1'b0 : 1'bz;  // Controlled_Buffer controlled_buffer_10
  assign WT = decoder4to16_1_o0000 ? 1'b0 : 1'bz;  // Controlled_Buffer controlled_buffer_11
  assign WT = decoder4to16_1_o0001 ? 1'b0 : 1'bz;  // Controlled_Buffer controlled_buffer_12
  assign D1 = decoder4to16_1_o0001 ? I[7:0] : 8'bz;  // Controlled_Buffer controlled_buffer_13
  assign VD1 = decoder4to16_1_o0001 ? 1'b0 : 1'bz;  // Controlled_Buffer controlled_buffer_14
  assign VD2 = decoder4to16_1_o0001 ? 1'b0 : 1'bz;  // Controlled_Buffer controlled_buffer_15
  assign A1 = decoder4to16_1_o0001 ? I[11:8] : 4'bz;  // Controlled_Buffer controlled_buffer_16
  assign VA1 = decoder4to16_1_o0001 ? 1'b1 : 1'bz;  // Controlled_Buffer controlled_buffer_17
  assign VA2 = decoder4to16_1_o0001 ? 1'b0 : 1'bz;  // Controlled_Buffer controlled_buffer_18
  assign VA3 = decoder4to16_1_o0001 ? 1'b0 : 1'bz;  // Controlled_Buffer controlled_buffer_19
  assign S = decoder4to16_1_o0001 ? 1'b1 : 1'bz;  // Controlled_Buffer controlled_buffer_20
  assign A = decoder4to16_1_o0001 ? 1'b0 : 1'bz;  // Controlled_Buffer controlled_buffer_21
  assign P = decoder4to16_1_o0001 ? 1'b0 : 1'bz;  // Controlled_Buffer controlled_buffer_22
  assign VD1 = decoder4to16_1_o0010 ? 1'b0 : 1'bz;  // Controlled_Buffer controlled_buffer_23
  assign D2 = decoder4to16_1_o0010 ? I[7:0] : 8'bz;  // Controlled_Buffer controlled_buffer_24
  assign VD2 = decoder4to16_1_o0010 ? 1'b1 : 1'bz;  // Controlled_Buffer controlled_buffer_25
  assign A1 = decoder4to16_1_o0010 ? I[11:8] : 4'bz;  // Controlled_Buffer controlled_buffer_26
  assign VA1 = decoder4to16_1_o0010 ? 1'b1 : 1'bz;  // Controlled_Buffer controlled_buffer_27
  assign VA2 = decoder4to16_1_o0010 ? 1'b0 : 1'bz;  // Controlled_Buffer controlled_buffer_28
  assign A3 = decoder4to16_1_o0010 ? I[11:8] : 4'bz;  // Controlled_Buffer controlled_buffer_29
  assign VA3 = decoder4to16_1_o0010 ? 1'b1 : 1'bz;  // Controlled_Buffer controlled_buffer_30
  assign S = decoder4to16_1_o0010 ? 1'b0 : 1'bz;  // Controlled_Buffer controlled_buffer_31
  assign A = decoder4to16_1_o0010 ? 1'b1 : 1'bz;  // Controlled_Buffer controlled_buffer_32
  assign P = decoder4to16_1_o0010 ? 1'b1 : 1'bz;  // Controlled_Buffer controlled_buffer_33
  assign WT = decoder4to16_1_o0010 ? 1'b0 : 1'bz;  // Controlled_Buffer controlled_buffer_34
  assign VD1 = decoder4to16_1_o0011 ? 1'b0 : 1'bz;  // Controlled_Buffer controlled_buffer_35
  assign VD2 = decoder4to16_1_o0011 ? 1'b0 : 1'bz;  // Controlled_Buffer controlled_buffer_36
  assign A1 = decoder4to16_1_o0011 ? I[7:4] : 4'bz;  // Controlled_Buffer controlled_buffer_37
  assign VA1 = decoder4to16_1_o0011 ? 1'b1 : 1'bz;  // Controlled_Buffer controlled_buffer_38
  assign A2 = decoder4to16_1_o0011 ? I[3:0] : 4'bz;  // Controlled_Buffer controlled_buffer_39
  assign VA2 = decoder4to16_1_o0011 ? 1'b1 : 1'bz;  // Controlled_Buffer controlled_buffer_40
  assign A3 = decoder4to16_1_o0011 ? I[11:8] : 4'bz;  // Controlled_Buffer controlled_buffer_41
  assign VA3 = decoder4to16_1_o0011 ? 1'b1 : 1'bz;  // Controlled_Buffer controlled_buffer_42
  assign S = decoder4to16_1_o0011 ? 1'b0 : 1'bz;  // Controlled_Buffer controlled_buffer_43
  assign A = decoder4to16_1_o0011 ? 1'b1 : 1'bz;  // Controlled_Buffer controlled_buffer_44
  assign P = decoder4to16_1_o0011 ? 1'b1 : 1'bz;  // Controlled_Buffer controlled_buffer_45
  assign WT = decoder4to16_1_o0011 ? 1'b0 : 1'bz;  // Controlled_Buffer controlled_buffer_46
  assign VD1 = decoder4to16_1_o0100 ? 1'b0 : 1'bz;  // Controlled_Buffer controlled_buffer_47
  assign D2 = decoder4to16_1_o0100 ? I[7:0] : 8'bz;  // Controlled_Buffer controlled_buffer_48
  assign VD2 = decoder4to16_1_o0100 ? 1'b1 : 1'bz;  // Controlled_Buffer controlled_buffer_49
  assign A1 = decoder4to16_1_o0100 ? I[11:8] : 4'bz;  // Controlled_Buffer controlled_buffer_50
  assign VA1 = decoder4to16_1_o0100 ? 1'b1 : 1'bz;  // Controlled_Buffer controlled_buffer_51
  assign VA2 = decoder4to16_1_o0100 ? 1'b0 : 1'bz;  // Controlled_Buffer controlled_buffer_52
  assign A3 = decoder4to16_1_o0100 ? I[11:8] : 4'bz;  // Controlled_Buffer controlled_buffer_53
  assign VA3 = decoder4to16_1_o0100 ? 1'b1 : 1'bz;  // Controlled_Buffer controlled_buffer_54
  assign S = decoder4to16_1_o0100 ? 1'b0 : 1'bz;  // Controlled_Buffer controlled_buffer_55
  assign A = decoder4to16_1_o0100 ? 1'b1 : 1'bz;  // Controlled_Buffer controlled_buffer_56
  assign P = decoder4to16_1_o0100 ? 1'b0 : 1'bz;  // Controlled_Buffer controlled_buffer_57
  assign WT = decoder4to16_1_o0100 ? 1'b0 : 1'bz;  // Controlled_Buffer controlled_buffer_58
  assign VD1 = decoder4to16_1_o0101 ? 1'b0 : 1'bz;  // Controlled_Buffer controlled_buffer_59
  assign VD2 = decoder4to16_1_o0101 ? 1'b0 : 1'bz;  // Controlled_Buffer controlled_buffer_60
  assign A1 = decoder4to16_1_o0101 ? I[7:4] : 4'bz;  // Controlled_Buffer controlled_buffer_61
  assign VA1 = decoder4to16_1_o0101 ? 1'b1 : 1'bz;  // Controlled_Buffer controlled_buffer_62
  assign A2 = decoder4to16_1_o0101 ? I[3:0] : 4'bz;  // Controlled_Buffer controlled_buffer_63
  assign VA2 = decoder4to16_1_o0101 ? 1'b1 : 1'bz;  // Controlled_Buffer controlled_buffer_64
  assign A3 = decoder4to16_1_o0101 ? I[11:8] : 4'bz;  // Controlled_Buffer controlled_buffer_65
  assign VA3 = decoder4to16_1_o0101 ? 1'b1 : 1'bz;  // Controlled_Buffer controlled_buffer_66
  assign S = decoder4to16_1_o0101 ? 1'b0 : 1'bz;  // Controlled_Buffer controlled_buffer_67
  assign A = decoder4to16_1_o0101 ? 1'b1 : 1'bz;  // Controlled_Buffer controlled_buffer_68
  assign P = decoder4to16_1_o0101 ? 1'b0 : 1'bz;  // Controlled_Buffer controlled_buffer_69
  assign WT = decoder4to16_1_o0101 ? 1'b0 : 1'bz;  // Controlled_Buffer controlled_buffer_70
  assign VD1 = decoder4to16_1_o1111 ? 1'b0 : 1'bz;  // Controlled_Buffer controlled_buffer_71
  assign VD2 = decoder4to16_1_o1111 ? 1'b0 : 1'bz;  // Controlled_Buffer controlled_buffer_72
  assign VA1 = decoder4to16_1_o1111 ? 1'b0 : 1'bz;  // Controlled_Buffer controlled_buffer_73
  assign VA2 = decoder4to16_1_o1111 ? 1'b0 : 1'bz;  // Controlled_Buffer controlled_buffer_74
  assign VA3 = decoder4to16_1_o1111 ? 1'b0 : 1'bz;  // Controlled_Buffer controlled_buffer_75
  assign S = decoder4to16_1_o1111 ? 1'b1 : 1'bz;  // Controlled_Buffer controlled_buffer_76
  assign A = decoder4to16_1_o1111 ? 1'b0 : 1'bz;  // Controlled_Buffer controlled_buffer_77
  assign P = decoder4to16_1_o1111 ? 1'b0 : 1'bz;  // Controlled_Buffer controlled_buffer_78
  assign WT = decoder4to16_1_o1111 ? 1'b0 : 1'bz;  // Controlled_Buffer controlled_buffer_79
  assign VD1 = decoder4to16_1_o1110 ? 1'b0 : 1'bz;  // Controlled_Buffer controlled_buffer_80
  assign VD2 = decoder4to16_1_o1110 ? 1'b0 : 1'bz;  // Controlled_Buffer controlled_buffer_81
  assign VA1 = decoder4to16_1_o1110 ? 1'b0 : 1'bz;  // Controlled_Buffer controlled_buffer_82
  assign VA2 = decoder4to16_1_o1110 ? 1'b0 : 1'bz;  // Controlled_Buffer controlled_buffer_83
  assign VA3 = decoder4to16_1_o1110 ? 1'b0 : 1'bz;  // Controlled_Buffer controlled_buffer_84
  assign S = decoder4to16_1_o1110 ? 1'b0 : 1'bz;  // Controlled_Buffer controlled_buffer_85
  assign A = decoder4to16_1_o1110 ? 1'b0 : 1'bz;  // Controlled_Buffer controlled_buffer_86
  assign P = decoder4to16_1_o1110 ? 1'b0 : 1'bz;  // Controlled_Buffer controlled_buffer_87
  assign WT = decoder4to16_1_o1110 ? 1'b1 : 1'bz;  // Controlled_Buffer controlled_buffer_88
endmodule

module GPR (
  input  [7:0] D1,
  input  VD1,
  input  [7:0] D2,
  input  VD2,
  input  [3:0] A1,
  input  VA1,
  input  [3:0] A2,
  input  VA2,
  input  [3:0] A3,
  input  VA3,
  input  S,
  input  A,
  input  P,
  input  WT,
  input  clk,
  output [7:0] O1,
  output [7:0] O2,
  output [3:0] OAddress,
  output VA,
  output OS,
  output OA,
  output OP
);

  wire A0000_i, A0001_i, A0010_i, A0011_i, regdeal_1_j, regdeal_1_r, regdeal_1_r1, regdeal_1_r2,
       regdeal_1_r3, regdeal_1_r4, regdeal_1_restart, regdeal_1_v00, regdeal_1_v01, regdeal_1_v10,
       regdeal_1_v11, regdeal_1_w, regdeal_1_w1, regdeal_1_w2, regdeal_1_w3, regdeal_1_w4, regdeal_2_j,
       regdeal_2_r, regdeal_2_r1, regdeal_2_r2, regdeal_2_r3, regdeal_2_r4, regdeal_2_restart, regdeal_2_v00,
       regdeal_2_v01, regdeal_2_v10, regdeal_2_v11, regdeal_2_w, regdeal_2_w1, regdeal_2_w2, regdeal_2_w3,
       regdeal_2_w4, resanddefdeal_1_or1, resanddefdeal_1_or2, resanddefdeal_1_or3, resanddefdeal_1_or4,
       resanddefdeal_1_ort1, resanddefdeal_1_ort2, resanddefdeal_1_ow1, resanddefdeal_1_ow2,
       resanddefdeal_1_ow3, resanddefdeal_1_ow4, resanddefdeal_1_owt1, resanddefdeal_1_owt2, T1_i, T2_i;
  wire [7:0] A0000_s, A0001_s, A0010_s, A0011_s, regdeal_1_d1, regdeal_1_d2, regdeal_1_d3, regdeal_1_d4,
       regdeal_1_dj, regdeal_2_d1, regdeal_2_d2, regdeal_2_d3, regdeal_2_d4, regdeal_2_dj,
       resanddefdeal_1_od1, resanddefdeal_1_od2, resanddefdeal_1_od3, resanddefdeal_1_od4,
       resanddefdeal_1_odt1, resanddefdeal_1_odt2, T1_s, T2_s;

  RegDeal regdeal_1 (
    .Dt(D1), .VD(VD1), .Ads(A1), .VA(VA1), .D1(regdeal_1_d1), .R1(regdeal_1_r1), .W1(regdeal_1_w1),
    .V00(regdeal_1_v00), .D2(regdeal_1_d2), .R2(regdeal_1_r2), .W2(regdeal_1_w2), .V01(regdeal_1_v01),
    .D3(regdeal_1_d3), .R3(regdeal_1_r3), .W3(regdeal_1_w3), .V10(regdeal_1_v10), .D4(regdeal_1_d4),
    .R4(regdeal_1_r4), .W4(regdeal_1_w4), .V11(regdeal_1_v11), .DJ(regdeal_1_dj), .R(regdeal_1_r),
    .W(regdeal_1_w), .J(regdeal_1_j), .Restart(regdeal_1_restart));
  RegDeal regdeal_2 (
    .Dt(D2), .VD(VD2), .Ads(A2), .VA(VA2), .D1(regdeal_2_d1), .R1(regdeal_2_r1), .W1(regdeal_2_w1),
    .V00(regdeal_2_v00), .D2(regdeal_2_d2), .R2(regdeal_2_r2), .W2(regdeal_2_w2), .V01(regdeal_2_v01),
    .D3(regdeal_2_d3), .R3(regdeal_2_r3), .W3(regdeal_2_w3), .V10(regdeal_2_v10), .D4(regdeal_2_d4),
    .R4(regdeal_2_r4), .W4(regdeal_2_w4), .V11(regdeal_2_v11), .DJ(regdeal_2_dj), .R(regdeal_2_r),
    .W(regdeal_2_w), .J(regdeal_2_j), .Restart(regdeal_2_restart));
  ResAndDefDeal resanddefdeal_1 (
    .D11(regdeal_1_d1), .R11(regdeal_1_r1), .W11(regdeal_1_w1), .V001(regdeal_1_v00), .D21(regdeal_1_d2),
    .R21(regdeal_1_r2), .W21(regdeal_1_w2), .V011(regdeal_1_v01), .D31(regdeal_1_d3), .R31(regdeal_1_r3),
    .W31(regdeal_1_w3), .V101(regdeal_1_v10), .D41(regdeal_1_d4), .R41(regdeal_1_r4), .W41(regdeal_1_w4),
    .V111(regdeal_1_v11), .DJ1(regdeal_1_dj), .R1(regdeal_1_r), .W1(regdeal_1_w), .J1(regdeal_1_j),
    .Re1(regdeal_1_restart), .D12(regdeal_2_d1), .R12(regdeal_2_r1), .W12(regdeal_2_w1),
    .V002(regdeal_2_v00), .D22(regdeal_2_d2), .R22(regdeal_2_r2), .W22(regdeal_2_w2), .V012(regdeal_2_v01),
    .D32(regdeal_2_d3), .R32(regdeal_2_r3), .W32(regdeal_2_w3), .V102(regdeal_2_v10), .D42(regdeal_2_d4),
    .R42(regdeal_2_r4), .W42(regdeal_2_w4), .V112(regdeal_2_v11), .DJ2(regdeal_2_dj), .R2(regdeal_2_r),
    .W2(regdeal_2_w), .J2(regdeal_2_j), .Re2(regdeal_2_restart), .WT(WT), .OD1(resanddefdeal_1_od1),
    .OR1(resanddefdeal_1_or1), .OW1(resanddefdeal_1_ow1), .OD2(resanddefdeal_1_od2),
    .OR2(resanddefdeal_1_or2), .OW2(resanddefdeal_1_ow2), .OD3(resanddefdeal_1_od3),
    .OR3(resanddefdeal_1_or3), .OW3(resanddefdeal_1_ow3), .OD4(resanddefdeal_1_od4),
    .OR4(resanddefdeal_1_or4), .OW4(resanddefdeal_1_ow4), .ODT1(resanddefdeal_1_odt1),
    .ORT1(resanddefdeal_1_ort1), .OWT1(resanddefdeal_1_owt1), .ODT2(resanddefdeal_1_odt2),
    .ORT2(resanddefdeal_1_ort2), .OWT2(resanddefdeal_1_owt2));
  Reg4 A0000 (
    .D(resanddefdeal_1_od1), .clk(clk), .R(resanddefdeal_1_or1), .E(resanddefdeal_1_ow1), .S(A0000_s),
    .I(A0000_i));
  Reg4 A0001 (
    .D(resanddefdeal_1_od2), .clk(clk), .R(resanddefdeal_1_or2), .E(resanddefdeal_1_ow2), .S(A0001_s),
    .I(A0001_i));
  Reg4 A0010 (
    .D(resanddefdeal_1_od3), .clk(clk), .R(resanddefdeal_1_or3), .E(resanddefdeal_1_ow3), .S(A0010_s),
    .I(A0010_i));
  Reg4 A0011 (
    .D(resanddefdeal_1_od4), .clk(clk), .R(resanddefdeal_1_or4), .E(resanddefdeal_1_ow4), .S(A0011_s),
    .I(A0011_i));
  Reg4 T1 (.D(resanddefdeal_1_odt1), .clk(clk), .R(resanddefdeal_1_ort1), .E(resanddefdeal_1_owt1), .S(T1_s), .I(T1_i));
  Reg4 T2 (.D(resanddefdeal_1_odt2), .clk(clk), .R(resanddefdeal_1_ort2), .E(resanddefdeal_1_owt2), .S(T2_s), .I(T2_i));
  ResultOutUnit resultoutunit_1 (
    .D00(A0000_s), .D01(A0001_s), .D10(A0010_s), .D11(A0011_s), .DT1(T1_s), .DT2(T2_s), .A1(A1), .VA1(VA1),
    .A2(A2), .VA2(VA2), .VD00(A0000_i), .VD01(A0001_i), .VD10(A0010_i), .VD11(A0011_i), .VDT1(T1_i),
    .VDT2(T2_i), .O1(O1), .O2(O2));

  assign OA = A;
  assign OAddress = A3;
  assign OP = P;
  assign OS = S;
  assign VA = VA3;
endmodule

module ALU (
  input  [7:0] I1,
  input  [7:0] I2,
  input  [3:0] A3,
  input  VA3,
  input  S,
  input  A,
  input  P,
  output [7:0] D,
  output PosSubCT,
  output CalV,
  output [3:0] OAddress,
  output OAV,
  output OS,
  output ALUOP
);

  wire add8b_1_oo, not_1_out, not_2_out, sub8b_1_sign;
  wire [7:0] add8b_1_o, controlled_buffer_1_out, controlled_buffer_2_out, sub8b_1_o;

  assign controlled_buffer_1_out = S ? I1 : 8'bz;  // Controlled_Buffer controlled_buffer_1
  assign controlled_buffer_2_out = S ? I2 : 8'bz;  // Controlled_Buffer controlled_buffer_2
  assign controlled_buffer_2_out = not_1_out ? {8{1'b0}} : 8'bz;  // Controlled_Buffer controlled_buffer_3
  assign controlled_buffer_1_out = not_1_out ? {8{1'b0}} : 8'bz;  // Controlled_Buffer controlled_buffer_4
  not not_1 (not_1_out, S);
  not not_2 (not_2_out, P);
  Add8b add8b_1 (.I(1'b0), .A(controlled_buffer_1_out), .B(controlled_buffer_2_out), .O(add8b_1_o), .OO(add8b_1_oo));
  assign D = not_2_out ? sub8b_1_o : 8'bz;  // Controlled_Buffer controlled_buffer_5
  Sub8b sub8b_1 (
    .I(not_2_out), .A(controlled_buffer_1_out), .B(controlled_buffer_2_out), .O(sub8b_1_o),
    .Sign(sub8b_1_sign));
  assign PosSubCT = not_2_out ? sub8b_1_sign : 1'bz;  // Controlled_Buffer controlled_buffer_6
  assign D = P ? add8b_1_o : 8'bz;  // Controlled_Buffer controlled_buffer_7
  assign PosSubCT = P ? add8b_1_oo : 1'bz;  // Controlled_Buffer controlled_buffer_8

  assign ALUOP = P;
  assign CalV = A;
  assign OAddress = A3;
  assign OAV = VA3;
  assign OS = S;
endmodule

module Encoder (
  input  [7:0] D,
  input  C,
  input  VD,
  input  [3:0] A,
  input  VA,
  input  S,
  input  ALUOP,
  output [15:0] OP,
  output OC,
  output PSpro,
  output OV
);

  wire not_1_out;

  not not_1 (not_1_out, S);
  And3 and3_1 (.I1(VD), .I2(VA), .I3(not_1_out), .O(OV));

  assign OC = C;
  assign OP = {4'b0000, A, D};
  assign PSpro = ALUOP;
endmodule

module TimeController (
  input  [15:0] NxOdrIns,
  input  [15:0] ExctIns,
  input  VN,
  input  VE,
  input  R,
  input  C,
  input  clk,
  input  clk4,
  output [15:0] ToDecoder
);

  wire controlled_buffer_1_out, controlled_buffer_2_out, decoder2to4_1_o00, decoder2to4_1_o01,
       decoder2to4_1_o10, decoder2to4_1_o11, not_1_out, not_2_out;
  wire [1:0] controlled_buffer_5_out;
  wire [15:0] controlled_buffer_9_out;

  assign controlled_buffer_1_out = not_1_out ? VN : 1'bz;  // Controlled_Buffer controlled_buffer_1
  assign controlled_buffer_2_out = not_1_out ? VE : 1'bz;  // Controlled_Buffer controlled_buffer_2
  assign controlled_buffer_1_out = C ? 1'b0 : 1'bz;  // Controlled_Buffer controlled_buffer_3
  assign controlled_buffer_2_out = C ? 1'b0 : 1'bz;  // Controlled_Buffer controlled_buffer_4
  not not_1 (not_1_out, C);
  assign controlled_buffer_5_out[0] = not_2_out ? controlled_buffer_1_out : 1'bz;  // Controlled_Buffer controlled_buffer_5
  assign controlled_buffer_5_out[1] = not_2_out ? controlled_buffer_2_out : 1'bz;  // Controlled_Buffer controlled_buffer_6
  assign controlled_buffer_5_out[0] = R ? 1'b1 : 1'bz;  // Controlled_Buffer controlled_buffer_7
  assign controlled_buffer_5_out[1] = R ? 1'b1 : 1'bz;  // Controlled_Buffer controlled_buffer_8
  not not_2 (not_2_out, R);
  Decoder2to4 decoder2to4_1 (
    .I(controlled_buffer_5_out), .O11(decoder2to4_1_o11), .O10(decoder2to4_1_o10), .O01(decoder2to4_1_o01),
    .O00(decoder2to4_1_o00));
  assign controlled_buffer_9_out = decoder2to4_1_o11 ? {16{1'b1}} : 16'bz;  // Controlled_Buffer controlled_buffer_9
  assign controlled_buffer_9_out = decoder2to4_1_o10 ? ExctIns : 16'bz;  // Controlled_Buffer controlled_buffer_10
  assign controlled_buffer_9_out = decoder2to4_1_o01 ? NxOdrIns : 16'bz;  // Controlled_Buffer controlled_buffer_11
  assign controlled_buffer_9_out = decoder2to4_1_o00 ? 16'he000 : 16'bz;  // Controlled_Buffer controlled_buffer_12
  Reg16b reg16b_1 (.D(controlled_buffer_9_out), .clk(clk), .R(R), .E(clk4), .S(ToDecoder));
endmodule

module And3 (
  input  I1,
  input  I2,
  input  I3,
  output O
);

  wire transistor_1_out, transistor_3_out, transistor_4_out;

  Transistor transistor_1 (.in(1'b1), .out(transistor_1_out), .gate(I1));
  Transistor transistor_2 (.in(1'b1), .out(transistor_1_out), .gate(I2));
  Transistor #(.\type ("n")) transistor_3 (.in(1'b0), .out(transistor_3_out), .gate(I1));
  Transistor #(.\type ("n")) transistor_4 (.in(transistor_3_out), .out(transistor_4_out), .gate(I2));
  Transistor transistor_5 (.in(1'b1), .out(transistor_1_out), .gate(I3));
  Transistor #(.\type ("n")) transistor_6 (.in(transistor_4_out), .out(transistor_1_out), .gate(I3));
  not not_1 (O, transistor_1_out);
endmodule

module Or3 (
  input  I1,
  input  I2,
  input  I3,
  output O
);

  wire transistor_1_out, transistor_2_out, transistor_3_out;

  Transistor transistor_1 (.in(1'b1), .out(transistor_1_out), .gate(I1));
  Transistor transistor_2 (.in(transistor_1_out), .out(transistor_2_out), .gate(I2));
  Transistor #(.\type ("n")) transistor_3 (.in(1'b0), .out(transistor_3_out), .gate(I1));
  Transistor #(.\type ("n")) transistor_4 (.in(1'b0), .out(transistor_3_out), .gate(I2));
  Transistor transistor_5 (.in(transistor_2_out), .out(transistor_3_out), .gate(I3));
  Transistor #(.\type ("n")) transistor_6 (.in(1'b0), .out(transistor_3_out), .gate(I3));
  not not_1 (O, transistor_3_out);
endmodule

module D_latch (
  input  R,
  input  E,
  input  S,
  output Q,
  output QA
);

  wire and_1_out, and_2_out;

  and and_1 (and_1_out, R, E);
  and and_2 (and_2_out, E, S);
  nor nor_1 (Q, and_1_out, QA);
  nor nor_2 (QA, Q, and_2_out);
endmodule

module D_filpflop (
  input  D,
  input  clk,
  output S
);

  wire d_latch_1_q, d_latch_1_qa, not_1_out, not_2_out;

  not not_1 (not_1_out, clk);
  not not_2 (not_2_out, D);
  D_latch d_latch_1 (.R(D), .E(not_1_out), .S(not_2_out), .Q(d_latch_1_q), .QA(d_latch_1_qa));
  D_latch d_latch_2 (.R(d_latch_1_q), .E(clk), .S(d_latch_1_qa), .Q(S));  // open: QA
endmodule

module Reg4 (
  input  [7:0] D,
  input  clk,
  input  R,
  input  E,
  output [7:0] S,
  output I
);

  wire not_1_out, not_2_out, not_3_out;
  wire [7:0] controlled_buffer_1_out, controlled_buffer_2_out;

  assign controlled_buffer_1_out = not_2_out ? S : 8'bz;  // Controlled_Buffer controlled_buffer_1
  assign controlled_buffer_2_out = not_1_out ? D : 8'bz;  // Controlled_Buffer controlled_buffer_2
  assign controlled_buffer_1_out = E ? controlled_buffer_2_out : 8'bz;  // Controlled_Buffer controlled_buffer_3
  assign controlled_buffer_2_out = R ? {8{1'b0}} : 8'bz;  // Controlled_Buffer controlled_buffer_4
  not not_1 (not_1_out, R);
  not not_2 (not_2_out, E);
  not not_3 (not_3_out, E);
  and and_1 (I, not_3_out, R);
  D_filpflop d_filpflop_1 (.D(controlled_buffer_1_out[0]), .clk(clk), .S(S[0]));
  D_filpflop d_filpflop_2 (.D(controlled_buffer_1_out[1]), .clk(clk), .S(S[1]));
  D_filpflop d_filpflop_3 (.D(controlled_buffer_1_out[2]), .clk(clk), .S(S[2]));
  D_filpflop d_filpflop_4 (.D(controlled_buffer_1_out[3]), .clk(clk), .S(S[3]));
  D_filpflop d_filpflop_5 (.D(controlled_buffer_1_out[4]), .clk(clk), .S(S[4]));
  D_filpflop d_filpflop_6 (.D(controlled_buffer_1_out[5]), .clk(clk), .S(S[5]));
  D_filpflop d_filpflop_7 (.D(controlled_buffer_1_out[6]), .clk(clk), .S(S[6]));
  D_filpflop d_filpflop_8 (.D(controlled_buffer_1_out[7]), .clk(clk), .S(S[7]));
endmodule

module Reg16b (
  input  [15:0] D,
  input  clk,
  input  R,
  input  E,
  output [15:0] S
);

  Reg4 reg4_1 (.D(D[7:0]), .clk(clk), .R(R), .E(E), .S(S[7:0]));  // open: I
  Reg4 reg4_2 (.D(D[15:8]), .clk(clk), .R(R), .E(E), .S(S[15:8]));  // open: I
endmodule

module Decoder2to4 (
  input  [1:0] I,
  output O11,
  output O10,
  output O01,
  output O00
);

  wire not_1_out, not_2_out;

  not not_1 (not_1_out, I[0]);
  not not_2 (not_2_out, I[1]);
  and and_1 (O11, I[0], I[1]);
  and and_2 (O10, not_1_out, I[1]);
  and and_3 (O01, I[0], not_2_out);
  and and_4 (O00, not_1_out, not_2_out);
endmodule

module Decoder4to16 (
  input  [3:0] I,
  output O0000,
  output O0001,
  output O0010,
  output O0011,
  output O0100,
  output O0101,
  output O0110,
  output O0111,
  output O1000,
  output O1001,
  output O1010,
  output O1011,
  output O1100,
  output O1101,
  output O1110,
  output O1111
);

  wire decoder2to4_1_o00, decoder2to4_1_o01, decoder2to4_1_o10, decoder2to4_1_o11, decoder2to4_2_o00,
       decoder2to4_2_o01, decoder2to4_2_o10, decoder2to4_2_o11;

  Decoder2to4 decoder2to4_1 (
    .I(I[1:0]), .O11(decoder2to4_1_o11), .O10(decoder2to4_1_o10), .O01(decoder2to4_1_o01),
    .O00(decoder2to4_1_o00));
  Decoder2to4 decoder2to4_2 (
    .I(I[3:2]), .O11(decoder2to4_2_o11), .O10(decoder2to4_2_o10), .O01(decoder2to4_2_o01),
    .O00(decoder2to4_2_o00));
  and and_1 (O0000, decoder2to4_2_o00, decoder2to4_1_o00);
  and and_2 (O0001, decoder2to4_2_o00, decoder2to4_1_o01);
  and and_3 (O0010, decoder2to4_2_o00, decoder2to4_1_o10);
  and and_4 (O0011, decoder2to4_2_o00, decoder2to4_1_o11);
  and and_5 (O0100, decoder2to4_2_o01, decoder2to4_1_o00);
  and and_6 (O0101, decoder2to4_2_o01, decoder2to4_1_o01);
  and and_7 (O0110, decoder2to4_2_o01, decoder2to4_1_o10);
  and and_8 (O0111, decoder2to4_2_o01, decoder2to4_1_o11);
  and and_9 (O1000, decoder2to4_2_o10, decoder2to4_1_o00);
  and and_10 (O1001, decoder2to4_2_o10, decoder2to4_1_o01);
  and and_11 (O1010, decoder2to4_2_o10, decoder2to4_1_o10);
  and and_12 (O1011, decoder2to4_2_o10, decoder2to4_1_o11);
  and and_13 (O1100, decoder2to4_2_o11, decoder2to4_1_o00);
  and and_14 (O1101, decoder2to4_2_o11, decoder2to4_1_o01);
  and and_15 (O1110, decoder2to4_2_o11, decoder2to4_1_o10);
  and and_16 (O1111, decoder2to4_2_o11, decoder2to4_1_o11);
endmodule

module Add1b (
  input  A,
  input  B,
  input  C,
  output P,
  output N
);

  wire and_1_out, and_2_out, xor_1_out;

  and and_1 (and_1_out, A, xor_1_out);
  and and_2 (and_2_out, C, B);
  xor xor_1 (xor_1_out, B, C);
  or or_1 (N, and_1_out, and_2_out);
  xor xor_2 (P, A, xor_1_out);
endmodule

module Add8b (
  input  I,
  input  [7:0] A,
  input  [7:0] B,
  output [7:0] O,
  output OO
);

  wire add1b_1_n, add1b_2_n, add1b_3_n, add1b_4_n, add1b_5_n, add1b_6_n, add1b_7_n;

  Add1b add1b_1 (.A(A[0]), .B(B[0]), .C(I), .P(O[0]), .N(add1b_1_n));
  Add1b add1b_2 (.A(add1b_1_n), .B(A[1]), .C(B[1]), .P(O[1]), .N(add1b_2_n));
  Add1b add1b_3 (.A(add1b_2_n), .B(A[2]), .C(B[2]), .P(O[2]), .N(add1b_3_n));
  Add1b add1b_4 (.A(add1b_3_n), .B(A[3]), .C(B[3]), .P(O[3]), .N(add1b_4_n));
  Add1b add1b_5 (.A(add1b_4_n), .B(A[4]), .C(B[4]), .P(O[4]), .N(add1b_5_n));
  Add1b add1b_6 (.A(add1b_5_n), .B(A[5]), .C(B[5]), .P(O[5]), .N(add1b_6_n));
  Add1b add1b_7 (.A(add1b_6_n), .B(A[6]), .C(B[6]), .P(O[6]), .N(add1b_7_n));
  Add1b add1b_8 (.A(add1b_7_n), .B(A[7]), .C(B[7]), .P(O[7]), .N(OO));
endmodule

module Sub8b (
  input  I,
  input  [7:0] A,
  input  [7:0] B,
  output [7:0] O,
  output Sign
);

  wire [7:0] not_1_out;

  assign not_1_out = ~B;  // NOT_Gate not_1, 8 bits wide
  Add8b add8b_1 (.I(I), .A(A), .B(not_1_out), .O(O), .OO(Sign));
endmodule

module SignalChecker (
  input  S1,
  input  S2,
  input  W,
  output E,
  output G
);

  wire and_1_out, not_1_out;

  and and_1 (and_1_out, S1, S2);
  not not_1 (not_1_out, W);
  and and_2 (E, and_1_out, W);
  and and_3 (G, and_1_out, not_1_out);
endmodule

module RegDeal (
  input  [7:0] Dt,
  input  VD,
  input  [3:0] Ads,
  input  VA,
  output [7:0] D1,
  output R1,
  output W1,
  output V00,
  output [7:0] D2,
  output R2,
  output W2,
  output V01,
  output [7:0] D3,
  output R3,
  output W3,
  output V10,
  output [7:0] D4,
  output R4,
  output W4,
  output V11,
  output [7:0] DJ,
  output R,
  output W,
  output J,
  output Restart
);

  wire decoder2to4_1_o00, decoder2to4_1_o01, decoder2to4_1_o10, decoder2to4_1_o11, decoder2to4_2_o00,
       decoder2to4_2_o01, decoder2to4_2_o10, decoder2to4_2_o11, not_1_out, or3_1_o, or_1_out;

  Decoder2to4 decoder2to4_1 (
    .I({VA, VD}), .O11(decoder2to4_1_o11), .O10(decoder2to4_1_o10), .O01(decoder2to4_1_o01),
    .O00(decoder2to4_1_o00));
  Decoder2to4 decoder2to4_2 (
    .I(Ads[1:0]), .O11(decoder2to4_2_o11), .O10(decoder2to4_2_o10), .O01(decoder2to4_2_o01),
    .O00(decoder2to4_2_o00));
  assign D1 = decoder2to4_1_o11 ? Dt : 8'bz;  // Controlled_Buffer controlled_buffer_1
  assign D1 = decoder2to4_1_o10 ? Dt : 8'bz;  // Controlled_Buffer controlled_buffer_2
  assign D1 = decoder2to4_1_o01 ? Dt : 8'bz;  // Controlled_Buffer controlled_buffer_3
  assign D1 = decoder2to4_1_o00 ? Dt : 8'bz;  // Controlled_Buffer controlled_buffer_4
  assign Restart = or3_1_o ? 1'b0 : 1'bz;  // Controlled_Buffer controlled_buffer_5
  Or3 or3_1 (.I1(decoder2to4_1_o01), .I2(decoder2to4_1_o10), .I3(decoder2to4_1_o11), .O(or3_1_o));
  not not_1 (not_1_out, or_1_out);
  and and_1 (V11, not_1_out, decoder2to4_2_o11);
  and and_2 (V10, not_1_out, decoder2to4_2_o10);
  assign W = decoder2to4_1_o11 ? 1'b1 : 1'bz;  // Controlled_Buffer controlled_buffer_6
  assign R = decoder2to4_1_o11 ? 1'b0 : 1'bz;  // Controlled_Buffer controlled_buffer_7
  assign W = decoder2to4_1_o10 ? 1'b0 : 1'bz;  // Controlled_Buffer controlled_buffer_8
  assign R = decoder2to4_1_o10 ? 1'b0 : 1'bz;  // Controlled_Buffer controlled_buffer_9
  assign W = decoder2to4_1_o01 ? 1'b1 : 1'bz;  // Controlled_Buffer controlled_buffer_10
  assign R = decoder2to4_1_o01 ? 1'b0 : 1'bz;  // Controlled_Buffer controlled_buffer_11
  assign W = decoder2to4_1_o00 ? 1'b1 : 1'bz;  // Controlled_Buffer controlled_buffer_12
  assign R = decoder2to4_1_o00 ? 1'b1 : 1'bz;  // Controlled_Buffer controlled_buffer_13
  or or_1 (or_1_out, J, Restart);
  assign J = decoder2to4_1_o11 ? 1'b0 : 1'bz;  // Controlled_Buffer controlled_buffer_14
  assign J = decoder2to4_1_o10 ? 1'b0 : 1'bz;  // Controlled_Buffer controlled_buffer_15
  assign J = decoder2to4_1_o01 ? 1'b1 : 1'bz;  // Controlled_Buffer controlled_buffer_16
  assign J = decoder2to4_1_o00 ? 1'b0 : 1'bz;  // Controlled_Buffer controlled_buffer_17
  assign Restart = decoder2to4_1_o00 ? 1'b1 : 1'bz;  // Controlled_Buffer controlled_buffer_18
  and and_3 (V01, not_1_out, decoder2to4_2_o01);
  and and_4 (V00, not_1_out, decoder2to4_2_o00);

  assign D2 = D1;
  assign D3 = D1;
  assign D4 = D1;
  assign DJ = D1;
  assign R1 = R;
  assign R2 = R;
  assign R3 = R;
  assign R4 = R;
  assign W1 = W;
  assign W2 = W;
  assign W3 = W;
  assign W4 = W;
endmodule

module ResAndDefDeal (
  input  [7:0] D11,
  input  R11,
  input  W11,
  input  V001,
  input  [7:0] D21,
  input  R21,
  input  W21,
  input  V011,
  input  [7:0] D31,
  input  R31,
  input  W31,
  input  V101,
  input  [7:0] D41,
  input  R41,
  input  W41,
  input  V111,
  input  [7:0] DJ1,
  input  R1,
  input  W1,
  input  J1,
  input  Re1,
  input  [7:0] D12,
  input  R12,
  input  W12,
  input  V002,
  input  [7:0] D22,
  input  R22,
  input  W22,
  input  V012,
  input  [7:0] D32,
  input  R32,
  input  W32,
  input  V102,
  input  [7:0] D42,
  input  R42,
  input  W42,
  input  V112,
  input  [7:0] DJ2,
  input  R2,
  input  W2,
  input  J2,
  input  Re2,
  input  WT,
  output [7:0] OD1,
  output OR1,
  output OW1,
  output [7:0] OD2,
  output OR2,
  output OW2,
  output [7:0] OD3,
  output OR3,
  output OW3,
  output [7:0] OD4,
  output OR4,
  output OW4,
  output [7:0] ODT1,
  output ORT1,
  output OWT1,
  output [7:0] ODT2,
  output ORT2,
  output OWT2
);

  wire and_1_out, and_2_out, and_3_out, and_4_out, and_5_out, and_6_out, and_7_out, and_8_out, and_9_out,
       and_10_out, and_11_out, and_12_out, controlled_buffer_31_out, controlled_buffer_32_out, not_1_out,
       not_2_out, not_3_out, not_4_out, not_5_out, not_6_out, not_7_out, not_8_out, not_9_out, not_10_out,
       or_1_out, or_2_out, or_3_out, or_4_out, or_5_out, or_6_out;
  wire [7:0] controlled_buffer_33_out;

  not not_1 (not_1_out, Re1);
  not not_2 (not_2_out, Re2);
  not not_3 (not_3_out, WT);
  and and_1 (and_1_out, not_1_out, J1);
  and and_2 (and_2_out, not_2_out, J2);
  assign ORT1 = or_1_out ? R1 : 1'bz;  // Controlled_Buffer controlled_buffer_1
  assign OWT1 = or_1_out ? W1 : 1'bz;  // Controlled_Buffer controlled_buffer_2
  and and_3 (and_3_out, not_1_out, V001);
  and and_4 (and_4_out, not_1_out, V011);
  and and_5 (and_5_out, not_1_out, V101);
  and and_6 (and_6_out, not_1_out, V111);
  or or_1 (or_1_out, and_1_out, WT);
  assign ORT2 = or_2_out ? R2 : 1'bz;  // Controlled_Buffer controlled_buffer_3
  assign OWT2 = or_2_out ? W2 : 1'bz;  // Controlled_Buffer controlled_buffer_4
  and and_7 (and_7_out, not_2_out, V002);
  and and_8 (and_8_out, not_2_out, V012);
  and and_9 (and_9_out, not_2_out, V102);
  and and_10 (and_10_out, not_2_out, V112);
  or or_2 (or_2_out, and_2_out, WT);
  and and_11 (and_11_out, Re1, Re2);
  assign OR4 = and_6_out ? R41 : 1'bz;  // Controlled_Buffer controlled_buffer_5
  assign OW4 = and_6_out ? W41 : 1'bz;  // Controlled_Buffer controlled_buffer_6
  assign ODT1 = and_1_out ? DJ1 : 8'bz;  // Controlled_Buffer controlled_buffer_7
  not not_4 (not_4_out, or_1_out);
  assign OR4 = and_10_out ? R42 : 1'bz;  // Controlled_Buffer controlled_buffer_8
  assign OW4 = and_10_out ? W42 : 1'bz;  // Controlled_Buffer controlled_buffer_9
  assign ODT2 = and_2_out ? DJ2 : 8'bz;  // Controlled_Buffer controlled_buffer_10
  not not_5 (not_5_out, or_2_out);
  and and_12 (and_12_out, and_11_out, not_3_out);
  assign OR3 = and_5_out ? R31 : 1'bz;  // Controlled_Buffer controlled_buffer_11
  assign OW3 = and_5_out ? W31 : 1'bz;  // Controlled_Buffer controlled_buffer_12
  assign OD4 = and_6_out ? D41 : 8'bz;  // Controlled_Buffer controlled_buffer_13
  assign OR3 = and_9_out ? R32 : 1'bz;  // Controlled_Buffer controlled_buffer_14
  assign OW3 = and_9_out ? W32 : 1'bz;  // Controlled_Buffer controlled_buffer_15
  assign OD4 = and_10_out ? D42 : 8'bz;  // Controlled_Buffer controlled_buffer_16
  assign OR2 = and_4_out ? R21 : 1'bz;  // Controlled_Buffer controlled_buffer_17
  assign OW2 = and_4_out ? W21 : 1'bz;  // Controlled_Buffer controlled_buffer_18
  assign OD3 = and_5_out ? D31 : 8'bz;  // Controlled_Buffer controlled_buffer_19
  assign OR2 = and_8_out ? R22 : 1'bz;  // Controlled_Buffer controlled_buffer_20
  assign OW2 = and_8_out ? W22 : 1'bz;  // Controlled_Buffer controlled_buffer_21
  assign OD3 = and_9_out ? D32 : 8'bz;  // Controlled_Buffer controlled_buffer_22
  or or_3 (or_3_out, and_6_out, and_10_out);
  not not_6 (not_6_out, or_3_out);
  assign OR1 = and_3_out ? R11 : 1'bz;  // Controlled_Buffer controlled_buffer_23
  assign OW1 = and_3_out ? W11 : 1'bz;  // Controlled_Buffer controlled_buffer_24
  assign OD2 = and_4_out ? D21 : 8'bz;  // Controlled_Buffer controlled_buffer_25
  assign OR1 = and_7_out ? R12 : 1'bz;  // Controlled_Buffer controlled_buffer_26
  assign OW1 = and_7_out ? W12 : 1'bz;  // Controlled_Buffer controlled_buffer_27
  assign OD2 = and_8_out ? D22 : 8'bz;  // Controlled_Buffer controlled_buffer_28
  or or_4 (or_4_out, and_5_out, and_9_out);
  not not_7 (not_7_out, or_4_out);
  assign OD1 = and_3_out ? D11 : 8'bz;  // Controlled_Buffer controlled_buffer_29
  assign OD1 = and_7_out ? D12 : 8'bz;  // Controlled_Buffer controlled_buffer_30
  or or_5 (or_5_out, and_4_out, and_8_out);
  not not_8 (not_8_out, or_5_out);
  or or_6 (or_6_out, and_3_out, and_7_out);
  not not_9 (not_9_out, or_6_out);
  assign controlled_buffer_31_out = and_12_out ? 1'b1 : 1'bz;  // Controlled_Buffer controlled_buffer_31
  assign controlled_buffer_32_out = and_12_out ? 1'b1 : 1'bz;  // Controlled_Buffer controlled_buffer_32
  assign controlled_buffer_33_out = and_12_out ? {8{1'b0}} : 8'bz;  // Controlled_Buffer controlled_buffer_33
  assign controlled_buffer_31_out = not_10_out ? 1'b0 : 1'bz;  // Controlled_Buffer controlled_buffer_34
  assign controlled_buffer_32_out = not_10_out ? 1'b1 : 1'bz;  // Controlled_Buffer controlled_buffer_35
  assign controlled_buffer_33_out = not_10_out ? {8{1'b0}} : 8'bz;  // Controlled_Buffer controlled_buffer_36
  assign OD1 = not_9_out ? controlled_buffer_33_out : 8'bz;  // Controlled_Buffer controlled_buffer_37
  assign OD2 = not_8_out ? controlled_buffer_33_out : 8'bz;  // Controlled_Buffer controlled_buffer_38
  assign OD3 = not_7_out ? controlled_buffer_33_out : 8'bz;  // Controlled_Buffer controlled_buffer_39
  assign OD4 = not_6_out ? controlled_buffer_33_out : 8'bz;  // Controlled_Buffer controlled_buffer_40
  assign ODT1 = not_4_out ? controlled_buffer_33_out : 8'bz;  // Controlled_Buffer controlled_buffer_41
  assign ODT2 = not_5_out ? controlled_buffer_33_out : 8'bz;  // Controlled_Buffer controlled_buffer_42
  not not_10 (not_10_out, and_12_out);
  assign OR1 = not_9_out ? controlled_buffer_32_out : 1'bz;  // Controlled_Buffer controlled_buffer_43
  assign OW1 = not_9_out ? controlled_buffer_31_out : 1'bz;  // Controlled_Buffer controlled_buffer_44
  assign OR2 = not_8_out ? controlled_buffer_32_out : 1'bz;  // Controlled_Buffer controlled_buffer_45
  assign OW2 = not_8_out ? controlled_buffer_31_out : 1'bz;  // Controlled_Buffer controlled_buffer_46
  assign OR3 = not_7_out ? controlled_buffer_32_out : 1'bz;  // Controlled_Buffer controlled_buffer_47
  assign OW3 = not_7_out ? controlled_buffer_31_out : 1'bz;  // Controlled_Buffer controlled_buffer_48
  assign OR4 = not_6_out ? controlled_buffer_32_out : 1'bz;  // Controlled_Buffer controlled_buffer_49
  assign OW4 = not_6_out ? controlled_buffer_31_out : 1'bz;  // Controlled_Buffer controlled_buffer_50
  assign ORT1 = not_4_out ? controlled_buffer_32_out : 1'bz;  // Controlled_Buffer controlled_buffer_51
  assign OWT1 = not_4_out ? controlled_buffer_31_out : 1'bz;  // Controlled_Buffer controlled_buffer_52
  assign ORT2 = not_5_out ? controlled_buffer_32_out : 1'bz;  // Controlled_Buffer controlled_buffer_53
  assign OWT2 = not_5_out ? controlled_buffer_31_out : 1'bz;  // Controlled_Buffer controlled_buffer_54
  assign ODT1 = WT ? controlled_buffer_33_out : 8'bz;  // Controlled_Buffer controlled_buffer_55
  assign ODT2 = WT ? controlled_buffer_33_out : 8'bz;  // Controlled_Buffer controlled_buffer_56
endmodule

module ResultOutUnit (
  input  [7:0] D00,
  input  [7:0] D01,
  input  [7:0] D10,
  input  [7:0] D11,
  input  [7:0] DT1,
  input  [7:0] DT2,
  input  [3:0] A1,
  input  VA1,
  input  [3:0] A2,
  input  VA2,
  input  VD00,
  input  VD01,
  input  VD10,
  input  VD11,
  input  VDT1,
  input  VDT2,
  output [7:0] O1,
  output [7:0] O2
);

  wire and3_1_o, and3_2_o, and_1_out, controlled_buffer_1_out, controlled_buffer_2_out,
       controlled_buffer_3_out, controlled_buffer_4_out, controlled_buffer_9_out, controlled_buffer_10_out,
       controlled_buffer_11_out, controlled_buffer_12_out, decoder2to4_1_o00, decoder2to4_1_o01,
       decoder2to4_1_o10, decoder2to4_1_o11, decoder2to4_2_o00, decoder2to4_2_o01, decoder2to4_2_o10,
       decoder2to4_2_o11, not_1_out, not_2_out, not_3_out;
  wire [7:0] controlled_buffer_17_out, controlled_buffer_22_out;

  not not_1 (not_1_out, VA1);
  not not_2 (not_2_out, VA2);
  And3 and3_1 (.I1(VD00), .I2(VD01), .I3(VD10), .O(and3_1_o));
  And3 and3_2 (.I1(VD11), .I2(VDT1), .I3(VDT2), .O(and3_2_o));
  Decoder2to4 decoder2to4_1 (
    .I(A1[1:0]), .O11(decoder2to4_1_o11), .O10(decoder2to4_1_o10), .O01(decoder2to4_1_o01),
    .O00(decoder2to4_1_o00));
  Decoder2to4 decoder2to4_2 (
    .I(A2[1:0]), .O11(decoder2to4_2_o11), .O10(decoder2to4_2_o10), .O01(decoder2to4_2_o01),
    .O00(decoder2to4_2_o00));
  and and_1 (and_1_out, and3_1_o, and3_2_o);
  assign controlled_buffer_1_out = VA1 ? decoder2to4_1_o11 : 1'bz;  // Controlled_Buffer controlled_buffer_1
  assign controlled_buffer_2_out = VA1 ? decoder2to4_1_o10 : 1'bz;  // Controlled_Buffer controlled_buffer_2
  assign controlled_buffer_3_out = VA1 ? decoder2to4_1_o01 : 1'bz;  // Controlled_Buffer controlled_buffer_3
  assign controlled_buffer_4_out = VA1 ? decoder2to4_1_o00 : 1'bz;  // Controlled_Buffer controlled_buffer_4
  assign controlled_buffer_1_out = not_1_out ? 1'b0 : 1'bz;  // Controlled_Buffer controlled_buffer_5
  assign controlled_buffer_2_out = not_1_out ? 1'b0 : 1'bz;  // Controlled_Buffer controlled_buffer_6
  assign controlled_buffer_3_out = not_1_out ? 1'b0 : 1'bz;  // Controlled_Buffer controlled_buffer_7
  assign controlled_buffer_4_out = not_1_out ? 1'b0 : 1'bz;  // Controlled_Buffer controlled_buffer_8
  assign controlled_buffer_9_out = VA2 ? decoder2to4_2_o11 : 1'bz;  // Controlled_Buffer controlled_buffer_9
  assign controlled_buffer_10_out = VA2 ? decoder2to4_2_o10 : 1'bz;  // Controlled_Buffer controlled_buffer_10
  assign controlled_buffer_11_out = VA2 ? decoder2to4_2_o01 : 1'bz;  // Controlled_Buffer controlled_buffer_11
  assign controlled_buffer_12_out = VA2 ? decoder2to4_2_o00 : 1'bz;  // Controlled_Buffer controlled_buffer_12
  assign controlled_buffer_9_out = not_2_out ? 1'b0 : 1'bz;  // Controlled_Buffer controlled_buffer_13
  assign controlled_buffer_10_out = not_2_out ? 1'b0 : 1'bz;  // Controlled_Buffer controlled_buffer_14
  assign controlled_buffer_11_out = not_2_out ? 1'b0 : 1'bz;  // Controlled_Buffer controlled_buffer_15
  assign controlled_buffer_12_out = not_2_out ? 1'b0 : 1'bz;  // Controlled_Buffer controlled_buffer_16
  assign controlled_buffer_17_out = controlled_buffer_4_out ? D00 : 8'bz;  // Controlled_Buffer controlled_buffer_17
  assign controlled_buffer_17_out = controlled_buffer_3_out ? D01 : 8'bz;  // Controlled_Buffer controlled_buffer_18
  assign controlled_buffer_17_out = controlled_buffer_2_out ? D10 : 8'bz;  // Controlled_Buffer controlled_buffer_19
  assign controlled_buffer_17_out = controlled_buffer_1_out ? D11 : 8'bz;  // Controlled_Buffer controlled_buffer_20
  assign controlled_buffer_17_out = not_1_out ? DT1 : 8'bz;  // Controlled_Buffer controlled_buffer_21
  assign controlled_buffer_22_out = controlled_buffer_12_out ? D00 : 8'bz;  // Controlled_Buffer controlled_buffer_22
  assign controlled_buffer_22_out = controlled_buffer_11_out ? D01 : 8'bz;  // Controlled_Buffer controlled_buffer_23
  assign controlled_buffer_22_out = controlled_buffer_10_out ? D10 : 8'bz;  // Controlled_Buffer controlled_buffer_24
  assign controlled_buffer_22_out = controlled_buffer_9_out ? D11 : 8'bz;  // Controlled_Buffer controlled_buffer_25
  assign O1 = not_3_out ? controlled_buffer_17_out : 8'bz;  // Controlled_Buffer controlled_buffer_26
  assign O2 = not_3_out ? controlled_buffer_22_out : 8'bz;  // Controlled_Buffer controlled_buffer_27
  assign controlled_buffer_22_out = not_2_out ? DT2 : 8'bz;  // Controlled_Buffer controlled_buffer_28
  not not_3 (not_3_out, and_1_out);
  assign O1 = and_1_out ? {8{1'b0}} : 8'bz;  // Controlled_Buffer controlled_buffer_29
  assign O2 = and_1_out ? {8{1'b0}} : 8'bz;  // Controlled_Buffer controlled_buffer_30
endmodule

module ClkAnalysier (
  input  clkd4,
  input  clk,
  output VD
);

  wire buffer_1_out, d_filpflop_1_s, not_1_out;

  buf buffer_1 (buffer_1_out, clkd4);
  not not_1 (not_1_out, d_filpflop_1_s);
  D_filpflop d_filpflop_1 (.D(buffer_1_out), .clk(clk), .S(d_filpflop_1_s));
  and and_1 (VD, buffer_1_out, not_1_out);
endmodule
