// Logisim project MINIRISCVadv.circ as structural Verilog: 8 circuits, main circuit RegisterFile
module main (
  input  Reset
);

  wire alu_1_i, alu_1_pcjump, alu_1_s, alu_1_wb, Clk_out, decodeunit_1_add, decodeunit_1_aluusedop,
       decodeunit_1_btypeop, decodeunit_1_eq, decodeunit_1_errortypeop, decodeunit_1_istypeop,
       decodeunit_1_isword, decodeunit_1_jumpop, decodeunit_1_onlyrfusedop, decodeunit_1_va1,
       decodeunit_1_va2, decodeunit_1_var, raminfodealer_1_ramwenable, rgb_video_1_p3;
  wire [1:0] alu_1_infolow2;
  wire [3:0] decodeunit_1_infoadd1, decodeunit_1_infoadd2, decodeunit_1_infoaddr;
  wire [7:0] alu_1_ramsbinfo, rgb_video_1_p4, rgb_video_1_p5;
  wire [17:0] alu_1_saddr, pc_1_addr, pc_1_nextaddr;
  wire [23:0] rgb_video_1_p6;
  wire [31:0] alu_1_result, alu_1_sw32, dataram_1_raminfo, decodeunit_1_imdadd2, decodeunit_1_imdlsb,
       decodeunit_1_imdlui, raminfodealer_1_toram, registerfile_1_value1, registerfile_1_value2, rom_1_data;

  Clock Clk (.out(Clk_out));
  ROM #(.addrWidth(18), .dataWidth(32)) rom_1 (.addr(pc_1_addr), .data(rom_1_data));
  PC pc_1 (
    .AddrC(alu_1_result), .Jump(alu_1_pcjump), .clk(Clk_out), .Reset(Reset), .Addr(pc_1_addr),
    .NextAddr(pc_1_nextaddr));
  DecodeUnit decodeunit_1 (
    .Data(rom_1_data), .ErrorTypeOP(decodeunit_1_errortypeop), .ALUUsedOP(decodeunit_1_aluusedop),
    .OnlyRFusedOP(decodeunit_1_onlyrfusedop), .JumpOP(decodeunit_1_jumpop), .IStypeOP(decodeunit_1_istypeop),
    .BtypeOP(decodeunit_1_btypeop), .InfoAdd1(decodeunit_1_infoadd1), .VA1(decodeunit_1_va1),
    .InfoAdd2(decodeunit_1_infoadd2), .VA2(decodeunit_1_va2), .InfoAddR(decodeunit_1_infoaddr),
    .VAR(decodeunit_1_var), .ImdAdd2(decodeunit_1_imdadd2), .ImdLuI(decodeunit_1_imdlui),
    .ImdLSB(decodeunit_1_imdlsb), .Add(decodeunit_1_add), .ISWord(decodeunit_1_isword), .EQ(decodeunit_1_eq));
  RegisterFile registerfile_1 (
    .ErrorOP(decodeunit_1_errortypeop), .ALUType(decodeunit_1_aluusedop),
    .GPRType(decodeunit_1_onlyrfusedop), .JumpType(decodeunit_1_jumpop), .IStypeOP(decodeunit_1_istypeop),
    .BTypeOP(decodeunit_1_btypeop), .Add1(decodeunit_1_infoadd1), .VA1(decodeunit_1_va1),
    .Add2(decodeunit_1_infoadd2), .VA2(decodeunit_1_va2), .AddR(decodeunit_1_infoaddr),
    .VR(decodeunit_1_var), .WBget(alu_1_wb), .InfoResult(alu_1_result), .InfoAdd2(decodeunit_1_imdadd2),
    .InfoLUI(decodeunit_1_imdlui), .InfoJump(pc_1_nextaddr), .InfoRAM(dataram_1_raminfo),
    .ISword(decodeunit_1_isword), .clk(Clk_out), .R(Reset), .Value1(registerfile_1_value1),
    .Value2(registerfile_1_value2));
  // RGB_Video #(.cursor("No Cursor"), .height(256), .scale(1), .width(256)) rgb_video_1: pin names not known; wires that end beside it: Reset, Clk_out, rgb_video_1_p3, rgb_video_1_p4, rgb_video_1_p5, rgb_video_1_p6
  ALU alu_1 (
    .Cal1(registerfile_1_value1), .Cal2(registerfile_1_value2), .LSBinfo(decodeunit_1_imdlsb),
    .Add(decodeunit_1_add), .ALUDemand(decodeunit_1_aluusedop), .JumpOP(decodeunit_1_jumpop),
    .ISOP(decodeunit_1_istypeop), .BOP(decodeunit_1_btypeop), .SaveIns(decodeunit_1_va2),
    .EQ(decodeunit_1_eq), .OriginalPos(pc_1_addr), .Result(alu_1_result), .Saddr(alu_1_saddr), .S(alu_1_s),
    .I(alu_1_i), .WB(alu_1_wb), .InfoLow2(alu_1_infolow2), .RAMSbInfo(alu_1_ramsbinfo),
    .PCJump(alu_1_pcjump), .SW32(alu_1_sw32));
  DataRAM dataram_1 (
    .In32(raminfodealer_1_toram), .In8(alu_1_ramsbinfo), .WBus(raminfodealer_1_ramwenable), .RBus(alu_1_i),
    .Saddr(alu_1_saddr), .ISOP(decodeunit_1_istypeop), .ISword(decodeunit_1_isword), .Sel(alu_1_infolow2),
    .clk(Clk_out), .RAMInfo(dataram_1_raminfo));
  RAMInfoDealer raminfodealer_1 (
    .RAMInfo(registerfile_1_value2), .SAddr(alu_1_sw32), .S(alu_1_s), .ToRAM(raminfodealer_1_toram),
    .ToOut(rgb_video_1_p6), .X(rgb_video_1_p4), .Y(rgb_video_1_p5), .RGBEnable(rgb_video_1_p3),
    .RAMWenable(raminfodealer_1_ramwenable));

  // Notes on the sheet:
  //   contents of rom_1 (hex, n*v repeats v):
  //   413 93137 10113 10b7 dbc08093 80e7 fe012823 fea10923 fea12423 fe914203 fe4109a3 ff012783 f787b3
  //   f787b3 4b6b7 f0068693 fdc10113 d787b3 10000713 f12423 10593 100793 b00513 2112023 12023 12223 e12623
  //   e12823 f10a23 10b7 a8408093 80e7 2012083 2410113 8067 ff410113 112423 10b7 a7c08093 80e7 513 1800093
  //   80e7 812083 513 c10113 8067 852583 feb12823 fe812e23 3437 a0840413 ff014183 3401b3 1c183 ff114203
  //   440233 24203 4181b3 ff214203 440233 24203 4181b3 ff314203 440233 24203 4181b3 3237 a0020213 320233
  //   24203 ffc12403 420233 420233 410233 11b7 85c18193 fe312823 14800193 fe312623 fec22203 20067 1052703
  //   52683 452783 fe810113 e12423 112a23 fed12823 fef12623 13737 c0070713 fe012223 ff314203 fe4102a3
  //   fef14203 fe410223 fe412203 470233 24203 fe4105a3 ff214203 fe4102a3 fee14203 fe410223 fe412203 470233
  //   24203 fe410523 ff114203 fe4102a3 fed14203 fe410223 fe412203 470233 24203 fe4104a3 ff014203 fe4102a3
  //   fec14203 fe410223 fe412203 470233 24203 fe410423 fe812703 c52603 fee12823 fe812e23 3437 a0840413
  //   ff014183 3401b3 1c183 ff114203 440233 24203 4181b3 ff214203 440233 24203 4181b3 ff314203 440233
  //   24203 4181b3 3237 a0020213 320233 24203 ffc12403 420233 420233 410233 66800193 fe312823 28000193
  //   fe312623 fec22203 20067 c68733 10000513 fe812e23 fe912c23 fee12823 50413 ff012483 fe812423 feb14183
  //   3181b3 fe312423 fe914183 3181b3 fe912423 feb14203 420233 fe412423 fe914203 4181b3 3181b3 fe312a23
  //   fe912423 33237 b0020213 feb14183 4181b3 1c183 fe3103a3 fea14183 4181b3 1c183 fe310323 fe914183
  //   4181b3 1c183 fe3102a3 fe814183 4181b3 1c183 fe310223 ff412183 fe412203 440233 120213 fe412423
  //   feb14203 420233 fe412423 fe914203 4181b3 3237 b0820213 320233 ff812483 ffc12403 24203 420233 420233
  //   410233 11b7 86018193 fe312823 38800193 fe312623 fec22203 20067 812703 10000513 812823 e78733
  //   fe812e23 fe912c23 fee12823 50413 ff012483 fe812423 feb14183 3181b3 fe312423 fe914183 3181b3 fe912423
  //   feb14203 420233 fe412423 fe914203 4181b3 3181b3 fe312a23 fe912423 33237 b0020213 feb14183 4181b3
  //   1c183 fe3103a3 fea14183 4181b3 1c183 fe310323 fe914183 4181b3 1c183 fe3102a3 fe814183 4181b3 1c183
  //   fe310223 ff412183 fe412203 440233 120213 fe412423 feb14203 420233 fe412423 fe914203 4181b3 3237
  //   b0820213 320233 ff812483 ffc12403 24203 420233 420233 410233 11b7 86418193 fe312823 49800193
  //   fe312623 fec22203 20067 8*f787b3 d787b3 f787b3 f787b3 20000437 f40433 812783 c60633 c60633 fef12423
  //   feb14183 3181b3 fe312423 fe914183 fff78213 fe412423 feb14203 420233 fe412423 fe914203 4181b3 3237
  //   b1820213 418233 24203 420233 420233 410233 65800193 fe312823 53c00193 fe312623 fec22203 20067 912623
  //   493 40513 c12223 b12023 10b7 de008093 80e7 12583 412603 812783 148493 40040413 c585b3 fef12823
  //   fe912623 fe812e23 fe912c23 4b437 d0040413 ff014183 340233 100193 320023 fec14183 3401b3 18023 24183
  //   ff114483 940233 100493 920023 fed14483 9404b3 48023 24483 9181b3 ff214483 940233 100493 920023
  //   fee14483 9404b3 48023 24483 9181b3 ff314483 940233 100493 920023 fef14483 9404b3 48023 24483 9181b3
  //   3237 a0020213 320233 24203 ff812483 ffc12403 420233 420233 410233 65400193 fe312823 54400193
  //   fe312623 fec22203 20067 c12483 1012403 1412083 1810113 8067 10000713 fec12823 fee12623 fe812e23
  //   fe912c23 4b437 d0040413 ff014183 340233 100193 320023 fec14183 3401b3 18023 24183 ff114483 940233
  //   100493 920023 fed14483 9404b3 48023 24483 9181b3 ff214483 940233 100493 920023 fee14483 9404b3 48023
  //   24483 9181b3 ff314483 940233 100493 920023 fef14483 9404b3 48023 24483 9181b3 3237 a0020213 320233
  //   24203 ff812483 ffc12403 420233 420233 410233 74c00193 fe312823 28000193 fe312623 fec22203 20067
  //   812703 fee12823 fec12623 fe812e23 fe912c23 4b437 d0040413 ff014183 340233 100193 320023 fec14183
  //   3401b3 18023 24183 ff114483 940233 100493 920023 fed14483 9404b3 48023 24483 9181b3 ff214483 940233
  //   100493 920023 fee14483 9404b3 48023 24483 9181b3 ff314483 940233 100493 920023 fef14483 9404b3 48023
  //   24483 9181b3 3237 a0020213 320233 24203 ff812483 ffc12403 420233 420233 410233 11b7 83418193
  //   fe312823 38800193 fe312623 fec22203 20067 1412083 40637 20000537 1810113 1237 de020213 20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
endmodule

module PC (
  input  [31:0] AddrC,
  input  Jump,
  input  clk,
  input  Reset,
  output [17:0] Addr,
  output [17:0] NextAddr
);

  wire not_1_out;
  wire [31:0] adder_1_out, controlled_buffer_1_out, register_1_q;

  assign controlled_buffer_1_out = Jump ? AddrC : 32'bz;  // Controlled_Buffer controlled_buffer_1
  not not_1 (not_1_out, Jump);
  assign controlled_buffer_1_out = not_1_out ? {adder_1_out[31:20], NextAddr, adder_1_out[1:0]} : 32'bz;  // Controlled_Buffer controlled_buffer_2
  Register #(.width(32)) register_1 (
    .D(controlled_buffer_1_out), .en(1'b1), .clk(clk), .Q({register_1_q[31:20], Addr, register_1_q[1:0]}),
    .clr(Reset));
  Adder #(.width(32)) adder_1 (
    .a({register_1_q[31:20], Addr, register_1_q[1:0]}), .b(32'h4),
    .out({adder_1_out[31:20], NextAddr, adder_1_out[1:0]}));  // open: cin, cout
endmodule

module DecodeUnit (
  input  [31:0] Data,
  output ErrorTypeOP,
  output ALUUsedOP,
  output OnlyRFusedOP,
  output JumpOP,
  output IStypeOP,
  output BtypeOP,
  output [3:0] InfoAdd1,
  output VA1,
  output [3:0] InfoAdd2,
  output VA2,
  output [3:0] InfoAddR,
  output VAR,
  output [31:0] ImdAdd2,
  output [31:0] ImdLuI,
  output [31:0] ImdLSB,
  output Add,
  output ISWord,
  output EQ
);

  wire and_1_out, and_3_out, and_4_out, and_5_out, and_7_out, and_8_out, and_9_out, and_10_out,
       decoder_1_out0, decoder_1_out2, decoder_1_out4, decoder_1_out6, decoder_1_out7, decoder_1_out12,
       decoder_1_out13, decoder_2_out0, decoder_2_out1, decoder_2_out2, decoder_2_out4, not_1_out, not_2_out;
  wire [31:0] bit_extender_1_out, bit_extender_3_out;

  not not_1 (not_1_out, Data[3]);
  nand nand_1 (ErrorTypeOP, Data[0], not_1_out, Data[1]);
  assign bit_extender_1_out = {{19{Data[31]}}, {Data[31], Data[7], Data[30:25], Data[11:8], 1'b0}};  // Bit_Extender bit_extender_1
  Decoder #(.select(4)) decoder_1 (
    .out0(decoder_1_out0), .out2(decoder_1_out2), .out4(decoder_1_out4), .out6(decoder_1_out6),
    .out7(decoder_1_out7), .out12(decoder_1_out12), .out13(decoder_1_out13), .sel({Data[6:4], Data[2]}));  // open: out1, out3, out5, out8, out9, out10, out11, out14, out15, en
  and and_1 (and_1_out, decoder_2_out1, decoder_1_out12);
  Decoder #(.select(3)) decoder_2 (
    .out0(decoder_2_out0), .out1(decoder_2_out1), .out2(decoder_2_out2), .out4(decoder_2_out4),
    .sel(Data[14:12]));  // open: out3, out5, out6, out7, en
  assign ImdAdd2 = {{20{Data[31]}}, Data[31:20]};  // Bit_Extender bit_extender_2
  assign bit_extender_3_out = {{20{Data[31]}}, {Data[31:25], Data[11:7]}};  // Bit_Extender bit_extender_3
  and and_2 (EQ, decoder_2_out0, decoder_1_out12);
  or or_1 (BtypeOP, EQ, and_1_out);
  not not_2 (not_2_out, Data[30]);
  and and_3 (and_3_out, decoder_1_out2, decoder_2_out0);
  and and_4 (and_4_out, decoder_1_out6, decoder_2_out0);
  and and_5 (and_5_out, decoder_1_out4, decoder_2_out2);
  and and_6 (JumpOP, decoder_1_out13, decoder_2_out0);
  and and_7 (and_7_out, decoder_1_out4, decoder_2_out0);
  and and_8 (and_8_out, decoder_1_out0, decoder_2_out2);
  and and_9 (and_9_out, decoder_1_out0, decoder_2_out4);
  or or_2 (ISWord, and_8_out, and_5_out);
  and and_10 (and_10_out, and_4_out, not_2_out);
  or or_3 (ALUUsedOP, BtypeOP, and_9_out, and_3_out, and_5_out, JumpOP, and_8_out, and_4_out, and_7_out);
  or or_4 (IStypeOP, and_8_out, and_5_out, and_7_out, and_9_out);
  or or_5 (VA1, and_5_out, and_8_out, and_7_out, and_9_out, BtypeOP, JumpOP, and_3_out, and_4_out);
  or or_6 (VA2, and_4_out, EQ, and_5_out, and_1_out, and_7_out);
  or or_7 (VAR, and_3_out, and_4_out, decoder_1_out7, JumpOP, and_8_out, and_9_out);
  Multiplexer #(.width(32)) multiplexer_1 (
    .in0(bit_extender_3_out), .in1(bit_extender_1_out), .out(ImdLSB), .sel(BtypeOP));
  or or_8 (Add, and_10_out, JumpOP, and_3_out);
  buf or_9 (OnlyRFusedOP, decoder_1_out7);  // OR_Gate

  assign ImdLuI = {Data[31:12], {12{1'b0}}};
  assign InfoAdd1 = Data[18:15];
  assign InfoAdd2 = Data[23:20];
  assign InfoAddR = Data[10:7];
endmodule

module RegisterFile (
  input  ErrorOP,
  input  ALUType,
  input  GPRType,
  input  JumpType,
  input  IStypeOP,
  input  BTypeOP,
  input  [3:0] Add1,
  input  VA1,
  input  [3:0] Add2,
  input  VA2,
  input  [3:0] AddR,
  input  VR,
  input  WBget,
  input  [31:0] InfoResult,
  input  [31:0] InfoAdd2,
  input  [31:0] InfoLUI,
  input  [17:0] InfoJump,
  input  [31:0] InfoRAM,
  input  ISword,
  input  clk,
  input  R,
  output [31:0] Value1,
  output [31:0] Value2
);

  wire decoder_1_out16, decoder_1_out17, decoder_1_out18, decoder_1_out19, decoder_1_out20, decoder_1_out21,
       decoder_1_out22, decoder_1_out23, decoder_1_out24, decoder_1_out25, decoder_1_out26, decoder_1_out27,
       decoder_1_out28, decoder_1_out29, decoder_1_out30, decoder_1_out31, decoder_2_out0, decoder_2_out1,
       decoder_2_out2, decoder_2_out3, decoder_2_out4, decoder_2_out5, decoder_2_out6, decoder_2_out7,
       decoder_2_out8, decoder_2_out9, decoder_2_out10, decoder_2_out11, decoder_2_out12, decoder_2_out13,
       decoder_2_out14, decoder_2_out15, decoder_3_out0, decoder_3_out1, decoder_3_out2, decoder_3_out3,
       decoder_3_out4, decoder_3_out5, decoder_3_out6, decoder_3_out7, decoder_3_out8, decoder_3_out9,
       decoder_3_out10, decoder_3_out11, decoder_3_out12, decoder_3_out13, decoder_3_out14, decoder_3_out15,
       not_1_out;
  wire [31:0] controlled_buffer_1_out, controller_1_inputvalue, controller_1_output2, register_1_q,
       register_2_q, register_3_q, register_4_q, register_5_q, register_6_q, register_7_q, register_8_q,
       register_9_q, register_10_q, register_11_q, register_12_q, register_13_q, register_14_q,
       register_15_q, register_16_q;

  Controller controller_1 (
    .ALUType(ALUType), .GPRType(GPRType), .JumpType(JumpType), .LStype(IStypeOP), .Btype(BTypeOP), .VA2(VA2),
    .VR(VR), .VBget(WBget), .LSWord(ISword), .InfoALU(InfoResult), .InfoAdd2(InfoAdd2), .InfoLui(InfoLUI),
    .InfoRAM(InfoRAM), .InfoJump(InfoJump), .Output2(controller_1_output2),
    .InputValue(controller_1_inputvalue));
  Decoder #(.select(5)) decoder_1 (
    .out16(decoder_1_out16), .out17(decoder_1_out17), .out18(decoder_1_out18), .out19(decoder_1_out19),
    .out20(decoder_1_out20), .out21(decoder_1_out21), .out22(decoder_1_out22), .out23(decoder_1_out23),
    .out24(decoder_1_out24), .out25(decoder_1_out25), .out26(decoder_1_out26), .out27(decoder_1_out27),
    .out28(decoder_1_out28), .out29(decoder_1_out29), .out30(decoder_1_out30), .out31(decoder_1_out31),
    .sel({VR, AddR}));  // open: out0, out1, out2, out3, out4, out5, out6, out7, out8, out9, out10, out11, out12, out13, out14, out15, en
  Decoder #(.select(4)) decoder_2 (
    .out0(decoder_2_out0), .out1(decoder_2_out1), .out2(decoder_2_out2), .out3(decoder_2_out3),
    .out4(decoder_2_out4), .out5(decoder_2_out5), .out6(decoder_2_out6), .out7(decoder_2_out7),
    .out8(decoder_2_out8), .out9(decoder_2_out9), .out10(decoder_2_out10), .out11(decoder_2_out11),
    .out12(decoder_2_out12), .out13(decoder_2_out13), .out14(decoder_2_out14), .out15(decoder_2_out15),
    .sel(Add1), .en(VA1));
  Decoder #(.select(4)) decoder_3 (
    .out0(decoder_3_out0), .out1(decoder_3_out1), .out2(decoder_3_out2), .out3(decoder_3_out3),
    .out4(decoder_3_out4), .out5(decoder_3_out5), .out6(decoder_3_out6), .out7(decoder_3_out7),
    .out8(decoder_3_out8), .out9(decoder_3_out9), .out10(decoder_3_out10), .out11(decoder_3_out11),
    .out12(decoder_3_out12), .out13(decoder_3_out13), .out14(decoder_3_out14), .out15(decoder_3_out15),
    .sel(Add2), .en(VA2));
  Register #(.width(32)) register_1 (.D({32{1'b0}}), .en(decoder_1_out16), .clk(clk), .Q(register_1_q), .clr(R));
  Register #(.width(32)) register_2 (
    .D(controller_1_inputvalue), .en(decoder_1_out17), .clk(clk), .Q(register_2_q), .clr(R));
  Register #(.width(32)) register_3 (
    .D(controller_1_inputvalue), .en(decoder_1_out18), .clk(clk), .Q(register_3_q), .clr(R));
  Register #(.width(32)) register_4 (
    .D(controller_1_inputvalue), .en(decoder_1_out19), .clk(clk), .Q(register_4_q), .clr(R));
  assign controlled_buffer_1_out = decoder_2_out0 ? register_1_q : 32'bz;  // Controlled_Buffer controlled_buffer_1
  assign controlled_buffer_1_out = decoder_2_out1 ? register_2_q : 32'bz;  // Controlled_Buffer controlled_buffer_2
  assign controller_1_output2 = decoder_3_out0 ? register_1_q : 32'bz;  // Controlled_Buffer controlled_buffer_3
  assign controller_1_output2 = decoder_3_out1 ? register_2_q : 32'bz;  // Controlled_Buffer controlled_buffer_4
  assign controlled_buffer_1_out = decoder_2_out2 ? register_3_q : 32'bz;  // Controlled_Buffer controlled_buffer_5
  assign controlled_buffer_1_out = decoder_2_out3 ? register_4_q : 32'bz;  // Controlled_Buffer controlled_buffer_6
  Register #(.width(32)) register_5 (
    .D(controller_1_inputvalue), .en(decoder_1_out20), .clk(clk), .Q(register_5_q), .clr(R));
  Register #(.width(32)) register_6 (
    .D(controller_1_inputvalue), .en(decoder_1_out21), .clk(clk), .Q(register_6_q), .clr(R));
  Register #(.width(32)) register_7 (
    .D(controller_1_inputvalue), .en(decoder_1_out22), .clk(clk), .Q(register_7_q), .clr(R));
  assign controller_1_output2 = decoder_3_out2 ? register_3_q : 32'bz;  // Controlled_Buffer controlled_buffer_7
  Register #(.width(32)) register_8 (
    .D(controller_1_inputvalue), .en(decoder_1_out23), .clk(clk), .Q(register_8_q), .clr(R));
  assign controller_1_output2 = decoder_3_out3 ? register_4_q : 32'bz;  // Controlled_Buffer controlled_buffer_8
  assign controlled_buffer_1_out = decoder_2_out4 ? register_5_q : 32'bz;  // Controlled_Buffer controlled_buffer_9
  assign controlled_buffer_1_out = decoder_2_out5 ? register_6_q : 32'bz;  // Controlled_Buffer controlled_buffer_10
  assign controller_1_output2 = decoder_3_out4 ? register_5_q : 32'bz;  // Controlled_Buffer controlled_buffer_11
  assign controller_1_output2 = decoder_3_out5 ? register_6_q : 32'bz;  // Controlled_Buffer controlled_buffer_12
  assign controlled_buffer_1_out = decoder_2_out6 ? register_7_q : 32'bz;  // Controlled_Buffer controlled_buffer_13
  assign controlled_buffer_1_out = decoder_2_out7 ? register_8_q : 32'bz;  // Controlled_Buffer controlled_buffer_14
  Register #(.width(32)) register_9 (
    .D(controller_1_inputvalue), .en(decoder_1_out24), .clk(clk), .Q(register_9_q), .clr(R));
  Register #(.width(32)) register_10 (
    .D(controller_1_inputvalue), .en(decoder_1_out25), .clk(clk), .Q(register_10_q), .clr(R));
  Register #(.width(32)) register_11 (
    .D(controller_1_inputvalue), .en(decoder_1_out26), .clk(clk), .Q(register_11_q), .clr(R));
  assign controller_1_output2 = decoder_3_out6 ? register_7_q : 32'bz;  // Controlled_Buffer controlled_buffer_15
  Register #(.width(32)) register_12 (
    .D(controller_1_inputvalue), .en(decoder_1_out27), .clk(clk), .Q(register_12_q), .clr(R));
  assign controller_1_output2 = decoder_3_out7 ? register_8_q : 32'bz;  // Controlled_Buffer controlled_buffer_16
  assign controlled_buffer_1_out = decoder_2_out8 ? register_9_q : 32'bz;  // Controlled_Buffer controlled_buffer_17
  assign controlled_buffer_1_out = decoder_2_out9 ? register_10_q : 32'bz;  // Controlled_Buffer controlled_buffer_18
  assign controller_1_output2 = decoder_3_out8 ? register_9_q : 32'bz;  // Controlled_Buffer controlled_buffer_19
  assign controller_1_output2 = decoder_3_out9 ? register_10_q : 32'bz;  // Controlled_Buffer controlled_buffer_20
  assign controlled_buffer_1_out = decoder_2_out10 ? register_11_q : 32'bz;  // Controlled_Buffer controlled_buffer_21
  assign controlled_buffer_1_out = decoder_2_out11 ? register_12_q : 32'bz;  // Controlled_Buffer controlled_buffer_22
  Register #(.width(32)) register_13 (
    .D(controller_1_inputvalue), .en(decoder_1_out28), .clk(clk), .Q(register_13_q), .clr(R));
  Register #(.width(32)) register_14 (
    .D(controller_1_inputvalue), .en(decoder_1_out29), .clk(clk), .Q(register_14_q), .clr(R));
  Register #(.width(32)) register_15 (
    .D(controller_1_inputvalue), .en(decoder_1_out30), .clk(clk), .Q(register_15_q), .clr(R));
  assign controller_1_output2 = decoder_3_out10 ? register_11_q : 32'bz;  // Controlled_Buffer controlled_buffer_23
  Register #(.width(32)) register_16 (
    .D(controller_1_inputvalue), .en(decoder_1_out31), .clk(clk), .Q(register_16_q), .clr(R));
  assign controller_1_output2 = decoder_3_out11 ? register_12_q : 32'bz;  // Controlled_Buffer controlled_buffer_24
  assign controlled_buffer_1_out = decoder_2_out12 ? register_13_q : 32'bz;  // Controlled_Buffer controlled_buffer_25
  assign controlled_buffer_1_out = decoder_2_out13 ? register_14_q : 32'bz;  // Controlled_Buffer controlled_buffer_26
  assign controller_1_output2 = decoder_3_out12 ? register_13_q : 32'bz;  // Controlled_Buffer controlled_buffer_27
  assign controller_1_output2 = decoder_3_out13 ? register_14_q : 32'bz;  // Controlled_Buffer controlled_buffer_28
  assign controlled_buffer_1_out = decoder_2_out14 ? register_15_q : 32'bz;  // Controlled_Buffer controlled_buffer_29
  assign controlled_buffer_1_out = decoder_2_out15 ? register_16_q : 32'bz;  // Controlled_Buffer controlled_buffer_30
  not not_1 (not_1_out, ErrorOP);
  assign controller_1_output2 = decoder_3_out14 ? register_15_q : 32'bz;  // Controlled_Buffer controlled_buffer_31
  assign controller_1_output2 = decoder_3_out15 ? register_16_q : 32'bz;  // Controlled_Buffer controlled_buffer_32
  assign Value1 = not_1_out ? controlled_buffer_1_out : 32'bz;  // Controlled_Buffer controlled_buffer_33
  assign Value1 = ErrorOP ? {32{1'b0}} : 32'bz;  // Controlled_Buffer controlled_buffer_34
  assign Value2 = not_1_out ? controller_1_output2 : 32'bz;  // Controlled_Buffer controlled_buffer_35
  assign Value2 = ErrorOP ? {32{1'b0}} : 32'bz;  // Controlled_Buffer controlled_buffer_36
endmodule

module Controller (
  input  ALUType,
  input  GPRType,
  input  JumpType,
  input  LStype,
  input  Btype,
  input  VA2,
  input  VR,
  input  VBget,
  input  LSWord,
  input  [31:0] InfoALU,
  input  [31:0] InfoAdd2,
  input  [31:0] InfoLui,
  input  [31:0] InfoRAM,
  input  [17:0] InfoJump,
  output [31:0] Output2,
  output [31:0] InputValue
);

  wire and_1_out, and_2_out, decoder_1_out0, decoder_1_out1, decoder_1_out2, decoder_1_out3, decoder_1_out4,
       decoder_1_out5, decoder_1_out6, decoder_1_out7, decoder_1_out8, decoder_1_out9, decoder_1_out10,
       decoder_1_out11, decoder_1_out12, decoder_1_out13, decoder_1_out14, decoder_1_out15, decoder_2_out0,
       decoder_2_out1, decoder_3_out0, decoder_3_out1, decoder_3_out2, decoder_3_out3, not_1_out, not_2_out,
       or_1_out;
  wire [31:0] controlled_buffer_1_out, controlled_buffer_4_out, controlled_buffer_15_out,
       controlled_buffer_16_out, controlled_buffer_18_out, controlled_buffer_22_out;

  not not_1 (not_1_out, Btype);
  Decoder #(.select(4)) decoder_1 (
    .out0(decoder_1_out0), .out1(decoder_1_out1), .out2(decoder_1_out2), .out3(decoder_1_out3),
    .out4(decoder_1_out4), .out5(decoder_1_out5), .out6(decoder_1_out6), .out7(decoder_1_out7),
    .out8(decoder_1_out8), .out9(decoder_1_out9), .out10(decoder_1_out10), .out11(decoder_1_out11),
    .out12(decoder_1_out12), .out13(decoder_1_out13), .out14(decoder_1_out14), .out15(decoder_1_out15),
    .sel({LStype, JumpType, GPRType, ALUType}), .en(not_1_out));
  and and_1 (and_1_out, Btype, ALUType);
  not not_2 (not_2_out, VA2);
  and and_2 (and_2_out, VR, VBget);
  assign controlled_buffer_1_out = not_2_out ? InfoAdd2 : 32'bz;  // Controlled_Buffer controlled_buffer_1
  Decoder decoder_2 (.out0(decoder_2_out0), .out1(decoder_2_out1), .sel(and_2_out));  // open: en
  assign Output2 = decoder_1_out1 ? controlled_buffer_1_out : 32'bz;  // Controlled_Buffer controlled_buffer_2
  assign InputValue = decoder_1_out1 ? controlled_buffer_4_out : 32'bz;  // Controlled_Buffer controlled_buffer_3
  assign controlled_buffer_4_out = decoder_2_out0 ? {32{1'b0}} : 32'bz;  // Controlled_Buffer controlled_buffer_4
  assign controlled_buffer_4_out = decoder_2_out1 ? InfoALU : 32'bz;  // Controlled_Buffer controlled_buffer_5
  assign Output2 = decoder_1_out2 ? {32{1'b0}} : 32'bz;  // Controlled_Buffer controlled_buffer_6
  assign InputValue = decoder_1_out2 ? InfoLui : 32'bz;  // Controlled_Buffer controlled_buffer_7
  assign Output2 = decoder_1_out5 ? controlled_buffer_1_out : 32'bz;  // Controlled_Buffer controlled_buffer_8
  assign InputValue = decoder_1_out5 ? {{12{1'b0}}, InfoJump, 2'b00} : 32'bz;  // Controlled_Buffer controlled_buffer_9
  assign Output2 = decoder_1_out9 ? controlled_buffer_15_out : 32'bz;  // Controlled_Buffer controlled_buffer_10
  assign InputValue = decoder_1_out9 ? controlled_buffer_22_out : 32'bz;  // Controlled_Buffer controlled_buffer_11
  Decoder #(.select(2)) decoder_3 (
    .out0(decoder_3_out0), .out1(decoder_3_out1), .out2(decoder_3_out2), .out3(decoder_3_out3),
    .sel({VA2, LSWord}));  // open: en
  or or_1 (or_1_out, decoder_1_out0, decoder_1_out3, decoder_1_out4, decoder_1_out6, decoder_1_out7, decoder_1_out8, decoder_1_out10, decoder_1_out11, decoder_1_out12, decoder_1_out13, decoder_1_out14, decoder_1_out15);
  assign Output2 = or_1_out ? {32{1'b0}} : 32'bz;  // Controlled_Buffer controlled_buffer_12
  assign Output2 = and_1_out ? controlled_buffer_16_out : 32'bz;  // Controlled_Buffer controlled_buffer_13
  assign InputValue = or_1_out ? {32{1'b0}} : 32'bz;  // Controlled_Buffer controlled_buffer_14
  assign controlled_buffer_15_out = decoder_3_out3 ? controlled_buffer_16_out : 32'bz;  // Controlled_Buffer controlled_buffer_15
  assign controlled_buffer_16_out = 1'b0 ? {32{1'b0}} : 32'bz;  // Controlled_Buffer controlled_buffer_16
  assign controlled_buffer_15_out = decoder_3_out2 ? controlled_buffer_18_out : 32'bz;  // Controlled_Buffer controlled_buffer_17
  assign controlled_buffer_18_out = 1'b0 ? controlled_buffer_1_out : 32'bz;  // Controlled_Buffer controlled_buffer_18
  assign controlled_buffer_15_out = decoder_3_out1 ? controlled_buffer_1_out : 32'bz;  // Controlled_Buffer controlled_buffer_19
  assign controlled_buffer_15_out = decoder_3_out0 ? controlled_buffer_1_out : 32'bz;  // Controlled_Buffer controlled_buffer_20
  assign InputValue = and_1_out ? {32{1'b0}} : 32'bz;  // Controlled_Buffer controlled_buffer_21
  assign controlled_buffer_22_out = decoder_3_out3 ? {32{1'b0}} : 32'bz;  // Controlled_Buffer controlled_buffer_22
  assign controlled_buffer_22_out = decoder_3_out2 ? controlled_buffer_1_out : 32'bz;  // Controlled_Buffer controlled_buffer_23
  assign controlled_buffer_22_out = decoder_3_out1 ? InfoRAM : 32'bz;  // Controlled_Buffer controlled_buffer_24
  assign controlled_buffer_22_out = decoder_3_out0 ? InfoRAM : 32'bz;  // Controlled_Buffer controlled_buffer_25
endmodule

module ALU (
  input  [31:0] Cal1,
  input  [31:0] Cal2,
  input  [31:0] LSBinfo,
  input  Add,
  input  ALUDemand,
  input  JumpOP,
  input  ISOP,
  input  BOP,
  input  SaveIns,
  input  EQ,
  input  [17:0] OriginalPos,
  output [31:0] Result,
  output [17:0] Saddr,
  output S,
  output I,
  output WB,
  output [1:0] InfoLow2,
  output [7:0] RAMSbInfo,
  output PCJump,
  output [31:0] SW32
);

  wire and_1_out, and_2_out, comparator_1_eq, decoder_1_out0, decoder_1_out1, decoder_1_out2, decoder_1_out3,
       decoder_1_out4, decoder_1_out5, decoder_1_out6, decoder_1_out7, decoder_1_out8, decoder_1_out9,
       decoder_1_out10, decoder_1_out11, decoder_1_out12, decoder_1_out13, decoder_1_out14, decoder_1_out15,
       not_2_out, not_3_out, not_4_out, not_5_out, or_1_out, or_2_out, or_3_out, or_5_out, or_6_out,
       xnor_1_out;
  wire [31:0] adder_2_out, adder_3_out, adder_4_out, controlled_buffer_1_out, controlled_buffer_6_out,
       controlled_buffer_20_out, not_1_out;

  assign controlled_buffer_1_out = or_1_out ? LSBinfo : 32'bz;  // Controlled_Buffer controlled_buffer_1
  assign not_1_out = ~Cal2;  // NOT_Gate not_1, 32 bits wide
  Adder #(.width(32)) adder_1 (.a(Cal1), .b(controlled_buffer_1_out), .out(SW32));  // open: cin, cout
  assign controlled_buffer_1_out = not_2_out ? Cal2 : 32'bz;  // Controlled_Buffer controlled_buffer_2
  not not_2 (not_2_out, or_1_out);
  Decoder #(.select(4)) decoder_1 (
    .out0(decoder_1_out0), .out1(decoder_1_out1), .out2(decoder_1_out2), .out3(decoder_1_out3),
    .out4(decoder_1_out4), .out5(decoder_1_out5), .out6(decoder_1_out6), .out7(decoder_1_out7),
    .out8(decoder_1_out8), .out9(decoder_1_out9), .out10(decoder_1_out10), .out11(decoder_1_out11),
    .out12(decoder_1_out12), .out13(decoder_1_out13), .out14(decoder_1_out14), .out15(decoder_1_out15),
    .sel({BOP, ISOP, JumpOP, ALUDemand}));  // open: en
  Adder #(.width(32)) adder_2 (.a(Cal1), .b(Cal2), .out(adder_2_out));  // open: cin, cout
  Adder #(.width(32)) adder_3 (.a(Cal1), .b(not_1_out), .out(adder_3_out), .cin(1'b1));  // open: cout
  or or_1 (or_1_out, BOP, SaveIns);
  Adder #(.width(32)) adder_4 (
    .a({{12{1'b0}}, OriginalPos, 2'b00}), .b(LSBinfo), .out(adder_4_out));  // open: cin, cout
  or or_2 (or_2_out, decoder_1_out10, decoder_1_out11, decoder_1_out12, decoder_1_out9, decoder_1_out13, decoder_1_out14, decoder_1_out15, decoder_1_out8);
  assign WB = decoder_1_out1 ? 1'b1 : 1'bz;  // Controlled_Buffer controlled_buffer_3
  assign WB = decoder_1_out3 ? 1'b1 : 1'bz;  // Controlled_Buffer controlled_buffer_4
  assign WB = decoder_1_out5 ? 1'b0 : 1'bz;  // Controlled_Buffer controlled_buffer_5
  Comparator #(.width(32)) comparator_1 (.a(adder_2_out), .b(adder_3_out), .eq(comparator_1_eq));  // open: gt, lt
  assign controlled_buffer_6_out = and_1_out ? adder_2_out : 32'bz;  // Controlled_Buffer controlled_buffer_6
  assign I = decoder_1_out1 ? 1'b0 : 1'bz;  // Controlled_Buffer controlled_buffer_7
  assign S = decoder_1_out1 ? 1'b0 : 1'bz;  // Controlled_Buffer controlled_buffer_8
  assign I = decoder_1_out3 ? 1'b0 : 1'bz;  // Controlled_Buffer controlled_buffer_9
  assign S = decoder_1_out3 ? 1'b0 : 1'bz;  // Controlled_Buffer controlled_buffer_10
  assign I = decoder_1_out5 ? not_3_out : 1'bz;  // Controlled_Buffer controlled_buffer_11
  assign S = decoder_1_out5 ? SaveIns : 1'bz;  // Controlled_Buffer controlled_buffer_12
  not not_3 (not_3_out, SaveIns);
  assign controlled_buffer_6_out = not_5_out ? adder_3_out : 32'bz;  // Controlled_Buffer controlled_buffer_13
  assign Saddr = decoder_1_out1 ? {18{1'b0}} : 18'bz;  // Controlled_Buffer controlled_buffer_14
  assign RAMSbInfo = decoder_1_out1 ? {8{1'b0}} : 8'bz;  // Controlled_Buffer controlled_buffer_15
  assign Saddr = decoder_1_out3 ? {18{1'b0}} : 18'bz;  // Controlled_Buffer controlled_buffer_16
  assign RAMSbInfo = decoder_1_out3 ? {8{1'b0}} : 8'bz;  // Controlled_Buffer controlled_buffer_17
  assign Saddr = decoder_1_out5 ? SW32[19:2] : 18'bz;  // Controlled_Buffer controlled_buffer_18
  assign RAMSbInfo = decoder_1_out5 ? Cal2[7:0] : 8'bz;  // Controlled_Buffer controlled_buffer_19
  or or_3 (or_3_out, decoder_1_out0, decoder_1_out2, decoder_1_out4, decoder_1_out6, decoder_1_out7);
  or or_4 (PCJump, JumpOP, and_2_out);
  assign controlled_buffer_20_out = WB ? controlled_buffer_6_out : 32'bz;  // Controlled_Buffer controlled_buffer_20
  assign controlled_buffer_20_out = not_4_out ? {32{1'b0}} : 32'bz;  // Controlled_Buffer controlled_buffer_21
  not not_4 (not_4_out, WB);
  assign InfoLow2 = decoder_1_out1 ? 2'b00 : 2'bz;  // Controlled_Buffer controlled_buffer_22
  assign InfoLow2 = decoder_1_out3 ? 2'b00 : 2'bz;  // Controlled_Buffer controlled_buffer_23
  assign InfoLow2 = decoder_1_out5 ? SW32[1:0] : 2'bz;  // Controlled_Buffer controlled_buffer_24
  assign WB = or_5_out ? 1'b0 : 1'bz;  // Controlled_Buffer controlled_buffer_25
  assign I = or_5_out ? 1'b0 : 1'bz;  // Controlled_Buffer controlled_buffer_26
  or or_5 (or_5_out, or_3_out, or_2_out);
  xnor xnor_1 (xnor_1_out, EQ, comparator_1_eq);
  Multiplexer #(.width(32)) multiplexer_1 (.in0(controlled_buffer_20_out), .in1(adder_4_out), .out(Result), .sel(BOP));
  not not_5 (not_5_out, and_1_out);
  and and_1 (and_1_out, Add, or_6_out);
  or or_6 (or_6_out, decoder_1_out1, decoder_1_out3, I);
  assign S = or_5_out ? 1'b0 : 1'bz;  // Controlled_Buffer controlled_buffer_27
  assign Saddr = or_5_out ? {18{1'b0}} : 18'bz;  // Controlled_Buffer controlled_buffer_28
  assign RAMSbInfo = or_5_out ? {8{1'b0}} : 8'bz;  // Controlled_Buffer controlled_buffer_29
  assign InfoLow2 = or_5_out ? 2'b00 : 2'bz;  // Controlled_Buffer controlled_buffer_30
  and and_2 (and_2_out, decoder_1_out9, xnor_1_out);
endmodule

module DataRAM (
  input  [31:0] In32,
  input  [7:0] In8,
  input  WBus,
  input  RBus,
  input  [17:0] Saddr,
  input  ISOP,
  input  ISword,
  input  [1:0] Sel,
  input  clk,
  output [31:0] RAMInfo
);

  wire and_1_out, controlled_buffer_10_out, controlled_buffer_11_out, controlled_buffer_12_out,
       controlled_buffer_13_out, controlled_buffer_15_out, controlled_buffer_16_out,
       controlled_buffer_17_out, controlled_buffer_18_out, controlled_buffer_19_out,
       controlled_buffer_20_out, controlled_buffer_21_out, controlled_buffer_22_out,
       controlled_buffer_23_out, controlled_buffer_24_out, controlled_buffer_25_out,
       controlled_buffer_26_out, controlled_buffer_39_out, controlled_buffer_40_out,
       controlled_buffer_41_out, controlled_buffer_42_out, controlled_buffer_43_out,
       controlled_buffer_44_out, controlled_buffer_45_out, controlled_buffer_46_out, decoder_1_out0,
       decoder_1_out1, decoder_1_out2, decoder_1_out3, decoder_1_out4, decoder_1_out5, decoder_1_out6,
       decoder_1_out7, decoder_1_out8, decoder_1_out9, decoder_1_out10, decoder_1_out11, decoder_1_out12,
       decoder_1_out13, decoder_1_out14, decoder_1_out15, decoder_2_out0, decoder_2_out1, decoder_2_out2,
       decoder_2_out3, decoder_3_out0, decoder_3_out1, decoder_3_out2, decoder_3_out3, decoder_3_out4,
       decoder_3_out5, decoder_3_out6, decoder_3_out7, decoder_3_out8, decoder_3_out9, decoder_3_out10,
       decoder_3_out11, decoder_3_out12, decoder_3_out13, decoder_3_out14, decoder_3_out15, decoder_4_out0,
       decoder_4_out1, decoder_4_out2, decoder_4_out3, decoder_5_out0, decoder_5_out1, decoder_6_out0,
       decoder_6_out1, decoder_6_out2, decoder_6_out3, not_1_out, not_2_out, not_3_out, not_4_out, not_5_out,
       or_1_out, or_2_out, or_3_out, or_4_out, or_5_out, or_6_out;
  wire [7:0] controlled_buffer_2_out, controlled_buffer_3_out, controlled_buffer_4_out,
       controlled_buffer_8_out, controlled_buffer_99_out;
  wire [31:0] controlled_buffer_1_out, controlled_buffer_95_out, controlled_buffer_103_out, ram_1_dout,
       ram_2_dout, ram_3_dout, ram_4_dout;

  assign controlled_buffer_1_out = decoder_3_out13 ? In32 : 32'bz;  // Controlled_Buffer controlled_buffer_1
  not not_1 (not_1_out, decoder_2_out0);
  Decoder #(.select(4)) decoder_1 (
    .out0(decoder_1_out0), .out1(decoder_1_out1), .out2(decoder_1_out2), .out3(decoder_1_out3),
    .out4(decoder_1_out4), .out5(decoder_1_out5), .out6(decoder_1_out6), .out7(decoder_1_out7),
    .out8(decoder_1_out8), .out9(decoder_1_out9), .out10(decoder_1_out10), .out11(decoder_1_out11),
    .out12(decoder_1_out12), .out13(decoder_1_out13), .out14(decoder_1_out14), .out15(decoder_1_out15),
    .sel({Sel, Saddr[17:16]}));  // open: en
  Decoder #(.select(2)) decoder_2 (
    .out0(decoder_2_out0), .out1(decoder_2_out1), .out2(decoder_2_out2), .out3(decoder_2_out3), .sel(Sel));  // open: en
  assign controlled_buffer_2_out = decoder_2_out0 ? In8 : 8'bz;  // Controlled_Buffer controlled_buffer_2
  assign controlled_buffer_3_out = decoder_2_out1 ? In8 : 8'bz;  // Controlled_Buffer controlled_buffer_3
  assign controlled_buffer_4_out = decoder_2_out2 ? In8 : 8'bz;  // Controlled_Buffer controlled_buffer_4
  not not_2 (not_2_out, decoder_2_out2);
  not not_3 (not_3_out, decoder_2_out3);
  not not_4 (not_4_out, decoder_2_out1);
  assign controlled_buffer_2_out = not_1_out ? {8{1'b0}} : 8'bz;  // Controlled_Buffer controlled_buffer_5
  assign controlled_buffer_3_out = not_4_out ? {8{1'b0}} : 8'bz;  // Controlled_Buffer controlled_buffer_6
  assign controlled_buffer_4_out = not_2_out ? {8{1'b0}} : 8'bz;  // Controlled_Buffer controlled_buffer_7
  assign controlled_buffer_8_out = not_3_out ? {8{1'b0}} : 8'bz;  // Controlled_Buffer controlled_buffer_8
  assign controlled_buffer_8_out = decoder_2_out3 ? In8 : 8'bz;  // Controlled_Buffer controlled_buffer_9
  or or_1 (or_1_out, decoder_3_out0, decoder_3_out1, decoder_3_out2, decoder_3_out3, decoder_3_out4, decoder_3_out5, decoder_3_out6, decoder_3_out7, decoder_3_out8);
  Decoder #(.select(4)) decoder_3 (
    .out0(decoder_3_out0), .out1(decoder_3_out1), .out2(decoder_3_out2), .out3(decoder_3_out3),
    .out4(decoder_3_out4), .out5(decoder_3_out5), .out6(decoder_3_out6), .out7(decoder_3_out7),
    .out8(decoder_3_out8), .out9(decoder_3_out9), .out10(decoder_3_out10), .out11(decoder_3_out11),
    .out12(decoder_3_out12), .out13(decoder_3_out13), .out14(decoder_3_out14), .out15(decoder_3_out15),
    .sel({ISOP, ISword, RBus, WBus}));  // open: en
  Decoder #(.select(2)) decoder_4 (
    .out0(decoder_4_out0), .out1(decoder_4_out1), .out2(decoder_4_out2), .out3(decoder_4_out3),
    .sel(Saddr[17:16]));  // open: en
  or or_2 (or_2_out, or_5_out, or_4_out);
  assign controlled_buffer_10_out = decoder_3_out9 ? decoder_1_out0 : 1'bz;  // Controlled_Buffer controlled_buffer_10
  assign controlled_buffer_11_out = decoder_3_out9 ? decoder_1_out4 : 1'bz;  // Controlled_Buffer controlled_buffer_11
  assign controlled_buffer_12_out = decoder_3_out9 ? decoder_1_out8 : 1'bz;  // Controlled_Buffer controlled_buffer_12
  assign controlled_buffer_13_out = decoder_3_out9 ? decoder_1_out12 : 1'bz;  // Controlled_Buffer controlled_buffer_13
  assign controlled_buffer_1_out = decoder_3_out9 ? {controlled_buffer_8_out, controlled_buffer_4_out, controlled_buffer_3_out, controlled_buffer_2_out} : 32'bz;  // Controlled_Buffer controlled_buffer_14
  assign controlled_buffer_15_out = decoder_3_out9 ? 1'b1 : 1'bz;  // Controlled_Buffer controlled_buffer_15
  assign controlled_buffer_16_out = decoder_3_out9 ? 1'b0 : 1'bz;  // Controlled_Buffer controlled_buffer_16
  assign controlled_buffer_17_out = decoder_3_out9 ? 1'b1 : 1'bz;  // Controlled_Buffer controlled_buffer_17
  assign controlled_buffer_18_out = decoder_3_out9 ? 1'b0 : 1'bz;  // Controlled_Buffer controlled_buffer_18
  assign controlled_buffer_19_out = decoder_3_out9 ? 1'b1 : 1'bz;  // Controlled_Buffer controlled_buffer_19
  assign controlled_buffer_20_out = decoder_3_out9 ? 1'b0 : 1'bz;  // Controlled_Buffer controlled_buffer_20
  assign controlled_buffer_21_out = decoder_3_out9 ? 1'b1 : 1'bz;  // Controlled_Buffer controlled_buffer_21
  assign controlled_buffer_22_out = decoder_3_out9 ? 1'b0 : 1'bz;  // Controlled_Buffer controlled_buffer_22
  or or_3 (or_3_out, decoder_3_out11, decoder_3_out12, decoder_3_out15);
  assign controlled_buffer_23_out = decoder_3_out9 ? decoder_1_out1 : 1'bz;  // Controlled_Buffer controlled_buffer_23
  assign controlled_buffer_24_out = decoder_3_out9 ? decoder_1_out5 : 1'bz;  // Controlled_Buffer controlled_buffer_24
  assign controlled_buffer_25_out = decoder_3_out9 ? decoder_1_out9 : 1'bz;  // Controlled_Buffer controlled_buffer_25
  assign controlled_buffer_26_out = decoder_3_out9 ? decoder_1_out13 : 1'bz;  // Controlled_Buffer controlled_buffer_26
  assign controlled_buffer_16_out = or_4_out ? 1'b0 : 1'bz;  // Controlled_Buffer controlled_buffer_27
  assign controlled_buffer_15_out = or_4_out ? 1'b0 : 1'bz;  // Controlled_Buffer controlled_buffer_28
  assign controlled_buffer_15_out = decoder_3_out13 ? decoder_4_out3 : 1'bz;  // Controlled_Buffer controlled_buffer_29
  assign controlled_buffer_17_out = or_4_out ? 1'b0 : 1'bz;  // Controlled_Buffer controlled_buffer_30
  assign controlled_buffer_19_out = or_4_out ? 1'b0 : 1'bz;  // Controlled_Buffer controlled_buffer_31
  assign controlled_buffer_17_out = decoder_3_out13 ? decoder_4_out2 : 1'bz;  // Controlled_Buffer controlled_buffer_32
  assign controlled_buffer_20_out = or_4_out ? 1'b0 : 1'bz;  // Controlled_Buffer controlled_buffer_33
  assign controlled_buffer_18_out = or_4_out ? 1'b0 : 1'bz;  // Controlled_Buffer controlled_buffer_34
  assign controlled_buffer_19_out = decoder_3_out13 ? decoder_4_out1 : 1'bz;  // Controlled_Buffer controlled_buffer_35
  assign controlled_buffer_21_out = or_4_out ? 1'b0 : 1'bz;  // Controlled_Buffer controlled_buffer_36
  assign controlled_buffer_21_out = decoder_3_out13 ? decoder_4_out0 : 1'bz;  // Controlled_Buffer controlled_buffer_37
  assign controlled_buffer_22_out = or_4_out ? 1'b0 : 1'bz;  // Controlled_Buffer controlled_buffer_38
  Decoder decoder_5 (.out0(decoder_5_out0), .out1(decoder_5_out1), .sel(and_1_out));  // open: en
  and and_1 (and_1_out, RBus, ISOP);
  or or_4 (or_4_out, or_3_out, or_1_out);
  assign controlled_buffer_39_out = decoder_3_out9 ? decoder_1_out2 : 1'bz;  // Controlled_Buffer controlled_buffer_39
  assign controlled_buffer_40_out = decoder_3_out9 ? decoder_1_out3 : 1'bz;  // Controlled_Buffer controlled_buffer_40
  assign controlled_buffer_41_out = decoder_3_out9 ? decoder_1_out6 : 1'bz;  // Controlled_Buffer controlled_buffer_41
  assign controlled_buffer_42_out = decoder_3_out9 ? decoder_1_out7 : 1'bz;  // Controlled_Buffer controlled_buffer_42
  assign controlled_buffer_43_out = decoder_3_out9 ? decoder_1_out10 : 1'bz;  // Controlled_Buffer controlled_buffer_43
  assign controlled_buffer_44_out = decoder_3_out9 ? decoder_1_out11 : 1'bz;  // Controlled_Buffer controlled_buffer_44
  assign controlled_buffer_45_out = decoder_3_out9 ? decoder_1_out14 : 1'bz;  // Controlled_Buffer controlled_buffer_45
  assign controlled_buffer_46_out = decoder_3_out9 ? decoder_1_out15 : 1'bz;  // Controlled_Buffer controlled_buffer_46
  assign controlled_buffer_16_out = decoder_3_out13 ? 1'b0 : 1'bz;  // Controlled_Buffer controlled_buffer_47
  assign controlled_buffer_18_out = decoder_3_out13 ? 1'b0 : 1'bz;  // Controlled_Buffer controlled_buffer_48
  assign controlled_buffer_20_out = decoder_3_out13 ? 1'b0 : 1'bz;  // Controlled_Buffer controlled_buffer_49
  assign controlled_buffer_22_out = decoder_3_out13 ? 1'b0 : 1'bz;  // Controlled_Buffer controlled_buffer_50
  or or_5 (or_5_out, decoder_3_out10, decoder_3_out14);
  or or_6 (or_6_out, or_5_out, or_4_out);
  assign controlled_buffer_46_out = or_6_out ? 1'b0 : 1'bz;  // Controlled_Buffer controlled_buffer_51
  assign controlled_buffer_44_out = or_6_out ? 1'b0 : 1'bz;  // Controlled_Buffer controlled_buffer_52
  assign controlled_buffer_42_out = or_6_out ? 1'b0 : 1'bz;  // Controlled_Buffer controlled_buffer_53
  assign controlled_buffer_40_out = or_6_out ? 1'b0 : 1'bz;  // Controlled_Buffer controlled_buffer_54
  assign controlled_buffer_46_out = decoder_3_out13 ? 1'b1 : 1'bz;  // Controlled_Buffer controlled_buffer_55
  assign controlled_buffer_44_out = decoder_3_out13 ? 1'b1 : 1'bz;  // Controlled_Buffer controlled_buffer_56
  assign controlled_buffer_42_out = decoder_3_out13 ? 1'b1 : 1'bz;  // Controlled_Buffer controlled_buffer_57
  assign controlled_buffer_40_out = decoder_3_out13 ? 1'b1 : 1'bz;  // Controlled_Buffer controlled_buffer_58
  assign controlled_buffer_22_out = or_5_out ? 1'b1 : 1'bz;  // Controlled_Buffer controlled_buffer_59
  assign controlled_buffer_20_out = or_5_out ? 1'b1 : 1'bz;  // Controlled_Buffer controlled_buffer_60
  assign controlled_buffer_21_out = or_5_out ? 1'b0 : 1'bz;  // Controlled_Buffer controlled_buffer_61
  assign controlled_buffer_19_out = or_5_out ? 1'b0 : 1'bz;  // Controlled_Buffer controlled_buffer_62
  assign controlled_buffer_1_out = or_2_out ? {32{1'b0}} : 32'bz;  // Controlled_Buffer controlled_buffer_63
  assign controlled_buffer_1_out = or_2_out ? {32{1'b0}} : 32'bz;  // Controlled_Buffer controlled_buffer_64
  assign controlled_buffer_45_out = or_6_out ? 1'b0 : 1'bz;  // Controlled_Buffer controlled_buffer_65
  assign controlled_buffer_43_out = or_6_out ? 1'b0 : 1'bz;  // Controlled_Buffer controlled_buffer_66
  assign controlled_buffer_41_out = or_6_out ? 1'b0 : 1'bz;  // Controlled_Buffer controlled_buffer_67
  assign controlled_buffer_39_out = or_6_out ? 1'b0 : 1'bz;  // Controlled_Buffer controlled_buffer_68
  assign controlled_buffer_18_out = or_5_out ? 1'b1 : 1'bz;  // Controlled_Buffer controlled_buffer_69
  assign controlled_buffer_17_out = or_5_out ? 1'b0 : 1'bz;  // Controlled_Buffer controlled_buffer_70
  assign controlled_buffer_1_out = or_2_out ? {32{1'b0}} : 32'bz;  // Controlled_Buffer controlled_buffer_71
  assign controlled_buffer_1_out = or_2_out ? {32{1'b0}} : 32'bz;  // Controlled_Buffer controlled_buffer_72
  assign controlled_buffer_26_out = or_6_out ? 1'b0 : 1'bz;  // Controlled_Buffer controlled_buffer_73
  assign controlled_buffer_25_out = or_6_out ? 1'b0 : 1'bz;  // Controlled_Buffer controlled_buffer_74
  assign controlled_buffer_24_out = or_6_out ? 1'b0 : 1'bz;  // Controlled_Buffer controlled_buffer_75
  assign controlled_buffer_23_out = or_6_out ? 1'b0 : 1'bz;  // Controlled_Buffer controlled_buffer_76
  assign controlled_buffer_45_out = decoder_3_out13 ? 1'b1 : 1'bz;  // Controlled_Buffer controlled_buffer_77
  assign controlled_buffer_43_out = decoder_3_out13 ? 1'b1 : 1'bz;  // Controlled_Buffer controlled_buffer_78
  assign controlled_buffer_41_out = decoder_3_out13 ? 1'b1 : 1'bz;  // Controlled_Buffer controlled_buffer_79
  assign controlled_buffer_39_out = decoder_3_out13 ? 1'b1 : 1'bz;  // Controlled_Buffer controlled_buffer_80
  assign controlled_buffer_16_out = or_5_out ? 1'b1 : 1'bz;  // Controlled_Buffer controlled_buffer_81
  assign controlled_buffer_15_out = or_5_out ? 1'b0 : 1'bz;  // Controlled_Buffer controlled_buffer_82
  assign controlled_buffer_26_out = decoder_3_out13 ? 1'b1 : 1'bz;  // Controlled_Buffer controlled_buffer_83
  assign controlled_buffer_25_out = decoder_3_out13 ? 1'b1 : 1'bz;  // Controlled_Buffer controlled_buffer_84
  assign controlled_buffer_24_out = decoder_3_out13 ? 1'b1 : 1'bz;  // Controlled_Buffer controlled_buffer_85
  assign controlled_buffer_23_out = decoder_3_out13 ? 1'b1 : 1'bz;  // Controlled_Buffer controlled_buffer_86
  assign controlled_buffer_13_out = or_6_out ? 1'b0 : 1'bz;  // Controlled_Buffer controlled_buffer_87
  assign controlled_buffer_12_out = or_6_out ? 1'b0 : 1'bz;  // Controlled_Buffer controlled_buffer_88
  assign controlled_buffer_11_out = or_6_out ? 1'b0 : 1'bz;  // Controlled_Buffer controlled_buffer_89
  assign controlled_buffer_10_out = or_6_out ? 1'b0 : 1'bz;  // Controlled_Buffer controlled_buffer_90
  assign controlled_buffer_13_out = decoder_3_out13 ? 1'b1 : 1'bz;  // Controlled_Buffer controlled_buffer_91
  assign controlled_buffer_12_out = decoder_3_out13 ? 1'b1 : 1'bz;  // Controlled_Buffer controlled_buffer_92
  assign controlled_buffer_11_out = decoder_3_out13 ? 1'b1 : 1'bz;  // Controlled_Buffer controlled_buffer_93
  assign controlled_buffer_10_out = decoder_3_out13 ? 1'b1 : 1'bz;  // Controlled_Buffer controlled_buffer_94
  RAM #(.addrWidth(16), .asyncread("true"), .byteenables("byteEnables"), .dataWidth(32), .\type ("nonvolatile")) ram_1 (
    .addr(Saddr[15:0]), .we(controlled_buffer_21_out), .oe(controlled_buffer_22_out), .clk(clk),
    .din(controlled_buffer_1_out), .dout(ram_1_dout), .be3(controlled_buffer_13_out),
    .be2(controlled_buffer_12_out), .be1(controlled_buffer_11_out), .be0(controlled_buffer_10_out));
  assign controlled_buffer_95_out = decoder_4_out0 ? ram_1_dout : 32'bz;  // Controlled_Buffer controlled_buffer_95
  RAM #(.addrWidth(16), .asyncread("true"), .byteenables("byteEnables"), .dataWidth(32), .\type ("nonvolatile")) ram_2 (
    .addr(Saddr[15:0]), .we(controlled_buffer_19_out), .oe(controlled_buffer_20_out), .clk(clk),
    .din(controlled_buffer_1_out), .dout(ram_2_dout), .be3(controlled_buffer_26_out),
    .be2(controlled_buffer_25_out), .be1(controlled_buffer_24_out), .be0(controlled_buffer_23_out));
  assign controlled_buffer_95_out = decoder_4_out1 ? ram_2_dout : 32'bz;  // Controlled_Buffer controlled_buffer_96
  RAM #(.addrWidth(16), .asyncread("true"), .byteenables("byteEnables"), .dataWidth(32), .\type ("nonvolatile")) ram_3 (
    .addr(Saddr[15:0]), .we(controlled_buffer_17_out), .oe(controlled_buffer_18_out), .clk(clk),
    .din(controlled_buffer_1_out), .dout(ram_3_dout), .be3(controlled_buffer_45_out),
    .be2(controlled_buffer_43_out), .be1(controlled_buffer_41_out), .be0(controlled_buffer_39_out));
  assign controlled_buffer_95_out = decoder_4_out2 ? ram_3_dout : 32'bz;  // Controlled_Buffer controlled_buffer_97
  RAM #(.addrWidth(16), .asyncread("true"), .byteenables("byteEnables"), .dataWidth(32), .\type ("nonvolatile")) ram_4 (
    .addr(Saddr[15:0]), .we(controlled_buffer_15_out), .oe(controlled_buffer_16_out), .clk(clk),
    .din(controlled_buffer_1_out), .dout(ram_4_dout), .be3(controlled_buffer_46_out),
    .be2(controlled_buffer_44_out), .be1(controlled_buffer_42_out), .be0(controlled_buffer_40_out));
  assign controlled_buffer_95_out = decoder_4_out3 ? ram_4_dout : 32'bz;  // Controlled_Buffer controlled_buffer_98
  Decoder #(.select(2)) decoder_6 (
    .out0(decoder_6_out0), .out1(decoder_6_out1), .out2(decoder_6_out2), .out3(decoder_6_out3), .sel(Sel));  // open: en
  assign controlled_buffer_99_out = decoder_6_out0 ? controlled_buffer_95_out[7:0] : 8'bz;  // Controlled_Buffer controlled_buffer_99
  assign controlled_buffer_99_out = decoder_6_out1 ? controlled_buffer_95_out[15:8] : 8'bz;  // Controlled_Buffer controlled_buffer_100
  assign controlled_buffer_99_out = decoder_6_out2 ? controlled_buffer_95_out[23:16] : 8'bz;  // Controlled_Buffer controlled_buffer_101
  assign controlled_buffer_99_out = decoder_6_out3 ? controlled_buffer_95_out[31:24] : 8'bz;  // Controlled_Buffer controlled_buffer_102
  assign controlled_buffer_103_out = not_5_out ? {{24{1'b0}}, controlled_buffer_99_out} : 32'bz;  // Controlled_Buffer controlled_buffer_103
  not not_5 (not_5_out, ISword);
  assign controlled_buffer_103_out = ISword ? controlled_buffer_95_out : 32'bz;  // Controlled_Buffer controlled_buffer_104
  assign RAMInfo = decoder_5_out1 ? controlled_buffer_103_out : 32'bz;  // Controlled_Buffer controlled_buffer_105
  assign RAMInfo = decoder_5_out0 ? {32{1'b0}} : 32'bz;  // Controlled_Buffer controlled_buffer_106
endmodule

module RAMInfoDealer (
  input  [31:0] RAMInfo,
  input  [31:0] SAddr,
  input  S,
  output [31:0] ToRAM,
  output [23:0] ToOut,
  output [7:0] X,
  output [7:0] Y,
  output RGBEnable,
  output RAMWenable
);

  wire and_1_out, not_1_out, not_2_out, not_3_out, not_4_out, not_5_out, subtractor_1_bout, subtractor_2_bout;
  wire [31:0] controlled_buffer_3_out;
  wire [31:24] controlled_buffer_2_out;

  Subtractor #(.width(32)) subtractor_1 (
    .a(SAddr), .b(32'h20000000), .bin(1'b0), .bout(subtractor_1_bout));  // open: out
  not not_1 (not_1_out, subtractor_1_bout);
  and and_1 (and_1_out, not_1_out, subtractor_2_bout);
  not not_2 (not_2_out, and_1_out);
  Subtractor #(.width(32)) subtractor_2 (
    .a(SAddr), .b(32'h20040000), .bin(1'b0), .bout(subtractor_2_bout));  // open: out
  and and_2 (RGBEnable, and_1_out, S);
  and and_3 (RAMWenable, not_2_out, S);
  assign ToRAM = RGBEnable ? {32{1'b0}} : 32'bz;  // Controlled_Buffer controlled_buffer_1
  not not_3 (not_3_out, RGBEnable);
  assign {controlled_buffer_2_out, ToOut} = RGBEnable ? RAMInfo : 32'bz;  // Controlled_Buffer controlled_buffer_2
  not not_4 (not_4_out, RGBEnable);
  assign {controlled_buffer_3_out[31:18], Y, X, controlled_buffer_3_out[1:0]} = RGBEnable ? SAddr : 32'bz;  // Controlled_Buffer controlled_buffer_3
  not not_5 (not_5_out, RGBEnable);
  assign ToRAM = not_3_out ? RAMInfo : 32'bz;  // Controlled_Buffer controlled_buffer_4
  assign {controlled_buffer_2_out, ToOut} = not_4_out ? {32{1'b0}} : 32'bz;  // Controlled_Buffer controlled_buffer_5
  assign {controlled_buffer_3_out[31:18], Y, X, controlled_buffer_3_out[1:0]} = not_5_out ? {32{1'b0}} : 32'bz;  // Controlled_Buffer controlled_buffer_6
endmodule
